// Logisim project PC.circ as structural Verilog: 3 circuits, main circuit PC
module PC (
  input  ENABLE,
  input  RESET
);

  wire and_1_out, bridge_1_read_ram, bridge_1_sel_cmos, bridge_1_sel_mmio, bridge_1_sel_ram, clock_1_out,
       decoder_1_out0, decoder_1_out1, decoder_1_out2, decoder_1_out3, decoder_1_out4, decoder_1_out5,
       decoder_2_out12, decoder_2_out24, decoder_2_out25, or_1_out, or_2_out, pull_resistor_20_node,
       pull_resistor_21_node, pull_resistor_23_node, pull_resistor_25_node, pull_resistor_26_node,
       pull_resistor_27_node, ram_1_p2, ram_1_p3;
  wire [2:0] priority_encoder_1_out;
  wire [3:0] cpu_1_le0, pull_resistor_3_node, pull_resistor_5_node, pull_resistor_7_node,
       pull_resistor_9_node;
  wire [3:2] cpu_1_mwe;
  wire [5:0] cpu_1_addr_out_2;
  wire [7:0] cpu_1_addr_out, multiplexer_2_out, portio_23_p1, portio_24_p1, pull_resistor_2_node,
       pull_resistor_4_node, pull_resistor_6_node, pull_resistor_8_node, pull_resistor_18_node,
       pull_resistor_19_node, rom_1_p1, rom_1_p2, rom_1_p3, rom_1_p4, undriven, undriven_2, undriven_3,
       undriven_4, undriven_5, undriven_6, undriven_7, undriven_8, undriven_9, undriven_10, undriven_11,
       undriven_12, undriven_13, undriven_14, undriven_15, undriven_16, undriven_17, undriven_18,
       undriven_19, undriven_20, undriven_21, undriven_22, undriven_23, undriven_24, undriven_25,
       undriven_26, undriven_27, undriven_28, undriven_29, undriven_30, undriven_31, undriven_32;
  wire [7:6] cpu_1_addr_out_3;
  wire [19:0] ram_1_p1;
  wire [31:0] cpu_1_data_out, cpu_1_ic_out, disk_ctrl_1_data_out, multiplexer_3_out, multiplexer_4_out,
       multiplexer_5_out, pull_resistor_1_node, pull_resistor_10_node, pull_resistor_11_node,
       pull_resistor_12_node, pull_resistor_13_node, pull_resistor_36_node;
  wire [31:16] cpu_1_addr_out_4;
  wire [31:20] disk_ctrl_1_disk_addr;
  wire [63:0] disk_ctrl_1_disk_out, multiplexer_1_out;

  // RAM #(.addrWidth(20), .enables("line"), .line("octo"), .misaligned("true")) ram_1: pin names not known; wires that end beside it: ram_1_p1, ram_1_p2, ram_1_p3
  DISK_CTRL disk_ctrl_1 (
    .CLK(clock_1_out), .PORT_SEL(cpu_1_addr_out), .MAIN_CTRL({cpu_1_mwe, RESET, ENABLE}),
    .DATA_IN(cpu_1_data_out),
    .DISK_IN({undriven_8, undriven_7, undriven_6, undriven_5, undriven_4, undriven_3, undriven_2, undriven}),
    .DATA_OUT(disk_ctrl_1_data_out), .DISK_ADDR({disk_ctrl_1_disk_addr, ram_1_p1}), .DISK_WE(ram_1_p2),
    .CLK_OUT(ram_1_p3), .DISK_OUT(disk_ctrl_1_disk_out));
  Pull_Resistor pull_resistor_1 (.node(pull_resistor_1_node));
  assign pull_resistor_1_node = decoder_1_out1 ? disk_ctrl_1_data_out : 32'bz;  // Controlled_Buffer controlled_buffer_1
  TTY #(.cols(80), .rows(24)) tty_1 (.data(cpu_1_data_out[6:0]), .clk(clock_1_out), .we(and_1_out), .clr(or_1_out));
  Clock clock_1 (.out(clock_1_out));
  and and_1 (and_1_out, decoder_2_out24, cpu_1_mwe[2]);
  Multiplexer #(.width(64)) multiplexer_1 (
    .in0({undriven_16, undriven_15, undriven_14, undriven_13, undriven_12, undriven_11, undriven_10, undriven_9}),
    .in1({undriven_24, undriven_23, undriven_22, undriven_21, undriven_20, undriven_19, undriven_18, undriven_17}),
    .out(multiplexer_1_out), .sel(bridge_1_read_ram));
  // PortIO #(.direction("onlyinput"), .number(1)) portio_1: pin names not known
  // PortIO #(.direction("onlyinput"), .number(1)) portio_2: pin names not known
  // PortIO #(.direction("onlyinput"), .number(1)) portio_3: pin names not known
  // PortIO #(.direction("onlyinput"), .number(1)) portio_4: pin names not known; wires that end beside it: clock_1_out
  CPU cpu_1 (
    .INST_IN(multiplexer_1_out), .DATA_IN(multiplexer_5_out), .ENABLE(ENABLE), .CLK(clock_1_out),
    .RESET(RESET), .LE0(cpu_1_le0[0]), .LE1(cpu_1_le0[1]), .LE2(cpu_1_le0[2]), .LE3(cpu_1_le0[3]),
    .DATA_OUT(cpu_1_data_out), .MWE(cpu_1_mwe[2]), .MOE(cpu_1_mwe[3]),
    .ADDR_OUT({cpu_1_addr_out_4, cpu_1_addr_out_3, cpu_1_addr_out_2, cpu_1_addr_out}), .IC_OUT(cpu_1_ic_out));  // open: INT_IN, CALL_IRQ, FLAGS_OUT, IRQ_EN
  Decoder #(.select(6)) decoder_1 (
    .out0(decoder_1_out0), .out1(decoder_1_out1), .out2(decoder_1_out2), .out3(decoder_1_out3),
    .out4(decoder_1_out4), .out5(decoder_1_out5), .sel(cpu_1_addr_out_2), .en(bridge_1_sel_mmio));  // open: out6, out7, out8, out9, out10, out11, out12, out13, out14, out15, out16, out17, out18, out19, out20, out21, out22, out23, out24, out25, out26, out27, out28, out29, out30, out31, out32, out33, out34, out35, out36, out37, out38, out39, out40, out41, out42, out43, out44, out45, out46, out47, out48, out49, out50, out51, out52, out53, out54, out55, out56, out57, out58, out59, out60, out61, out62, out63
  Pull_Resistor pull_resistor_2 (.node(pull_resistor_2_node));
  Pull_Resistor pull_resistor_3 (.node(pull_resistor_3_node));
  assign pull_resistor_2_node = decoder_1_out2 ? cpu_1_addr_out : 8'bz;  // Controlled_Buffer controlled_buffer_2
  assign pull_resistor_3_node = decoder_1_out2 ? {cpu_1_mwe, RESET, ENABLE} : 4'bz;  // Controlled_Buffer controlled_buffer_3
  // PortIO #(.direction("onlyinput")) portio_5: pin names not known
  // PortIO #(.direction("onlyinput"), .number(4)) portio_6: pin names not known
  Pull_Resistor pull_resistor_4 (.node(pull_resistor_4_node));
  Pull_Resistor pull_resistor_5 (.node(pull_resistor_5_node));
  assign pull_resistor_4_node = decoder_1_out3 ? cpu_1_addr_out : 8'bz;  // Controlled_Buffer controlled_buffer_4
  assign pull_resistor_5_node = decoder_1_out3 ? {cpu_1_mwe, RESET, ENABLE} : 4'bz;  // Controlled_Buffer controlled_buffer_5
  // PortIO #(.direction("onlyinput")) portio_7: pin names not known
  // PortIO #(.direction("onlyinput"), .number(4)) portio_8: pin names not known
  Pull_Resistor pull_resistor_6 (.node(pull_resistor_6_node));
  Pull_Resistor pull_resistor_7 (.node(pull_resistor_7_node));
  assign pull_resistor_6_node = decoder_1_out4 ? cpu_1_addr_out : 8'bz;  // Controlled_Buffer controlled_buffer_6
  assign pull_resistor_7_node = decoder_1_out4 ? {cpu_1_mwe, RESET, ENABLE} : 4'bz;  // Controlled_Buffer controlled_buffer_7
  // PortIO #(.direction("onlyinput")) portio_9: pin names not known
  // PortIO #(.direction("onlyinput"), .number(4)) portio_10: pin names not known
  Pull_Resistor pull_resistor_8 (.node(pull_resistor_8_node));
  Pull_Resistor pull_resistor_9 (.node(pull_resistor_9_node));
  assign pull_resistor_8_node = decoder_1_out5 ? cpu_1_addr_out : 8'bz;  // Controlled_Buffer controlled_buffer_8
  assign pull_resistor_9_node = decoder_1_out5 ? {cpu_1_mwe, RESET, ENABLE} : 4'bz;  // Controlled_Buffer controlled_buffer_9
  // PortIO #(.direction("onlyinput")) portio_11: pin names not known
  // PortIO #(.direction("onlyinput"), .number(4)) portio_12: pin names not known
  or or_1 (or_1_out, decoder_2_out25, RESET);
  Pull_Resistor pull_resistor_10 (.node(pull_resistor_10_node));
  assign pull_resistor_10_node = decoder_1_out2 ? cpu_1_data_out : 32'bz;  // Controlled_Buffer controlled_buffer_10
  // PortIO #(.direction("onlyinput"), .number(32)) portio_13: pin names not known
  Pull_Resistor pull_resistor_11 (.node(pull_resistor_11_node));
  assign pull_resistor_11_node = decoder_1_out3 ? cpu_1_data_out : 32'bz;  // Controlled_Buffer controlled_buffer_11
  // PortIO #(.direction("onlyinput"), .number(32)) portio_14: pin names not known
  Pull_Resistor pull_resistor_12 (.node(pull_resistor_12_node));
  assign pull_resistor_12_node = decoder_1_out4 ? cpu_1_data_out : 32'bz;  // Controlled_Buffer controlled_buffer_12
  // PortIO #(.direction("onlyinput"), .number(32)) portio_15: pin names not known
  Pull_Resistor pull_resistor_13 (.node(pull_resistor_13_node));
  assign pull_resistor_13_node = decoder_1_out5 ? cpu_1_data_out : 32'bz;  // Controlled_Buffer controlled_buffer_13
  // PortIO #(.direction("onlyinput"), .number(32)) portio_16: pin names not known
  or or_2 (or_2_out, decoder_1_out2, decoder_1_out3, decoder_1_out4, decoder_1_out5, decoder_1_out1);
  Pull_Resistor pull_resistor_14 (.node(pull_resistor_1_node));
  Controlled_Buffer #(.width(32)) controlled_buffer_14 (.out(pull_resistor_1_node), .en(decoder_1_out2));  // open: in
  // PortIO #(.direction("onlyOutput"), .number(32)) portio_17: pin names not known
  Pull_Resistor pull_resistor_15 (.node(pull_resistor_1_node));
  Controlled_Buffer #(.width(32)) controlled_buffer_15 (.out(pull_resistor_1_node), .en(decoder_1_out3));  // open: in
  // PortIO #(.direction("onlyOutput"), .number(32)) portio_18: pin names not known
  Pull_Resistor pull_resistor_16 (.node(pull_resistor_1_node));
  Controlled_Buffer #(.width(32)) controlled_buffer_16 (.out(pull_resistor_1_node), .en(decoder_1_out4));  // open: in
  // PortIO #(.direction("onlyOutput"), .number(32)) portio_19: pin names not known
  Pull_Resistor pull_resistor_17 (.node(pull_resistor_1_node));
  Controlled_Buffer #(.width(32)) controlled_buffer_17 (.out(pull_resistor_1_node), .en(decoder_1_out5));  // open: in
  // PortIO #(.direction("onlyOutput"), .number(32)) portio_20: pin names not known
  BRIDGE bridge_1 (
    .INST_ADDR_IN(cpu_1_ic_out),
    .DATA_ADDR_IN({cpu_1_addr_out_4, cpu_1_addr_out_3, cpu_1_addr_out_2, cpu_1_addr_out}),
    .READ_RAM(bridge_1_read_ram), .SEL_CMOS(bridge_1_sel_cmos), .SEL_MMIO(bridge_1_sel_mmio),
    .SEL_RAM(bridge_1_sel_ram));  // open: SEL_BIOS
  Pull_Resistor pull_resistor_18 (.node(pull_resistor_18_node));
  // PortIO #(.direction("onlyOutput")) portio_21: pin names not known
  Pull_Resistor pull_resistor_19 (.node(pull_resistor_19_node));
  // PortIO #(.direction("onlyOutput")) portio_22: pin names not known; wires that end beside it: pull_resistor_19_node
  // PortIO #(.direction("onlyOutput")) portio_23: pin names not known; wires that end beside it: portio_23_p1
  // PortIO #(.direction("onlyOutput")) portio_24: pin names not known; wires that end beside it: portio_24_p1
  Multiplexer #(.select(3), .width(8)) multiplexer_2 (
    .in1(pull_resistor_18_node), .in2(pull_resistor_19_node), .in3(portio_23_p1), .in4(portio_24_p1),
    .out(multiplexer_2_out), .sel(priority_encoder_1_out));  // open: in0, in5, in6, in7
  Pull_Resistor pull_resistor_20 (.node(pull_resistor_20_node));
  // PortIO #(.direction("onlyOutput"), .number(1)) portio_25: pin names not known; wires that end beside it: pull_resistor_20_node
  Pull_Resistor pull_resistor_21 (.node(pull_resistor_21_node));
  // PortIO #(.direction("onlyOutput"), .number(1)) portio_26: pin names not known
  Pull_Resistor pull_resistor_22 (.node(portio_23_p1));
  Pull_Resistor pull_resistor_23 (.node(pull_resistor_23_node));
  // PortIO #(.direction("onlyOutput"), .number(1)) portio_27: pin names not known
  Pull_Resistor pull_resistor_24 (.node(portio_24_p1));
  Pull_Resistor pull_resistor_25 (.node(pull_resistor_25_node));
  // PortIO #(.direction("onlyOutput"), .number(1)) portio_28: pin names not known
  // OR_Gate or_3 has open pins: in0=pull_resistor_20_node, in1=pull_resistor_21_node, in2=pull_resistor_23_node, in3=pull_resistor_25_node, out=open
  Priority_Encoder priority_encoder_1 (
    .in1(pull_resistor_20_node), .out(priority_encoder_1_out));  // open: in0, in2, in3, in4, in5, in6, in7, en_in, gs, en_out
  Pull_Resistor pull_resistor_26 (.node(pull_resistor_26_node));
  assign pull_resistor_26_node = bridge_1_sel_cmos ? cpu_1_mwe[2] : 1'bz;  // Controlled_Buffer controlled_buffer_18
  Pull_Resistor pull_resistor_27 (.node(pull_resistor_27_node));
  assign pull_resistor_27_node = bridge_1_sel_ram ? cpu_1_mwe[2] : 1'bz;  // Controlled_Buffer controlled_buffer_19
  // ROM #(.addrWidth(16), .line("octo"), .misaligned("true")) BIOS: pin names not known
  // ROM #(.addrWidth(16), .line("quad"), .misaligned("true")) rom_1: pin names not known; wires that end beside it: rom_1_p1, rom_1_p2, rom_1_p3, rom_1_p4
  // RAM #(.addrWidth(16), .enables("line"), .line("quad"), .misaligned("true")) CMOS_RAM: pin names not known; wires that end beside it: pull_resistor_26_node, clock_1_out
  // DualRAM #(.addrWidth(24), .clearpin("true"), .enables("line"), .line("octo"), .misaligned("true")) DRAM: pin names not known; wires that end beside it: cpu_1_ic_out[23:0], clock_1_out, {cpu_1_addr_out_4[23:16], cpu_1_addr_out_3, cpu_1_addr_out_2, cpu_1_addr_out}, pull_resistor_27_node, RESET
  Pull_Resistor pull_resistor_28 ();  // open: node
  Pull_Resistor pull_resistor_29 ();  // open: node
  Pull_Resistor pull_resistor_30 ();  // open: node
  Pull_Resistor pull_resistor_31 ();  // open: node
  Pull_Resistor pull_resistor_32 ();  // open: node
  Pull_Resistor pull_resistor_33 ();  // open: node
  Pull_Resistor pull_resistor_34 ();  // open: node
  Pull_Resistor pull_resistor_35 ();  // open: node
  Decoder #(.select(5)) decoder_2 (
    .out12(decoder_2_out12), .out24(decoder_2_out24), .out25(decoder_2_out25), .sel(cpu_1_addr_out[4:0]),
    .en(decoder_1_out0));  // open: out0, out1, out2, out3, out4, out5, out6, out7, out8, out9, out10, out11, out13, out14, out15, out16, out17, out18, out19, out20, out21, out22, out23, out26, out27, out28, out29, out30, out31
  Pull_Resistor pull_resistor_36 (.node(pull_resistor_36_node));
  assign pull_resistor_36_node = or_2_out ? pull_resistor_1_node : 32'bz;  // Controlled_Buffer controlled_buffer_20
  Multiplexer #(.width(32)) multiplexer_3 (
    .in0({rom_1_p1, rom_1_p2, rom_1_p3, rom_1_p4}),
    .in1({undriven_28, undriven_27, undriven_26, undriven_25}), .out(multiplexer_3_out),
    .sel(bridge_1_sel_cmos));
  Multiplexer #(.width(32)) multiplexer_4 (
    .in0(multiplexer_3_out), .in1({undriven_32, undriven_31, undriven_30, undriven_29}),
    .out(multiplexer_4_out), .sel(bridge_1_sel_ram));
  Multiplexer #(.width(32)) multiplexer_5 (
    .in0(multiplexer_4_out), .in1(pull_resistor_36_node), .out(multiplexer_5_out), .sel(bridge_1_sel_mmio));
  Pull_Resistor pull_resistor_37 (.node(pull_resistor_36_node));
  assign pull_resistor_36_node = decoder_2_out12 ? 32'hffffff : 32'bz;  // Controlled_Buffer controlled_buffer_21

  // Notes on the sheet:
  //   contents of BIOS (hex, n*v repeats v):
  //   27 21 3 18 0 4 ff 0 21 3 19 0 4 7f 80 21 3 1a 0 0 3 e7 21 1 10 10 10 0 0 1 78 21 1 f a 22 a f 0 2 0
  //   18 22 a f 0 2 0 18 21 0 f 0 21 3 1a 0 0 3 f8 21 1 10 5 10 0 0 1 52 21 1 f 20 22 a f 0 2 0 18 10 0 0
  //   1 5d 21 1 10 8 21 3 1a 0 0 3 fd 10 0 0 1 32 21 1 f a 22 a f 0 2 0 18 22 a f 0 2 0 18 21 1 10 f 21 3
  //   1a 0 0 4 21 10 0 0 1 10 21 1 f a 22 a f 0 2 0 18 21 1 10 1d 21 3 1a 0 0 4 31 10 0 0 0 f5 21 1 f a 22
  //   a f 0 2 0 18 21 1 10 1d 21 3 1a 0 0 4 4e 10 0 0 0 da 21 1 f a 22 a f 0 2 0 18 21 1 10 1e 21 3 1a 0 0
  //   4 6b 10 0 0 0 bf 21 1 f a 22 a f 0 2 0 18 21 2 1e 0 1 21 3 1b 0 1 1 0 21 3 1a 0 2 1 0 1b 0 20 20 21
  //   1 20 3 1b 0 7 7 21 1 15 2 23 c 21 1a 3 3 1a 0 0 1 0 21 0 1f 1e 14 1f 2 3 0 1b 1f 22 c 21 1b 21 3 1b
  //   0 0 2 89 22 a 1b 0 3 1 4 21 3 1b 0 0 3 2b 22 a 1b 0 3 1 8 21 1 10 1a 21 3 1a 0 0 4 6 10 0 0 0 4b 1b
  //   0 8 8 1b 0 9 9 1b 0 a a 1b 0 b b 1b 0 c c 1b 0 d d 1b 0 e e 21 3 1a 0 5 0 0 1b 0 1c 1c 21 3 2 4*0 21
  //   3 3 0 0 0 1 23 a 1d 0 3 1 4 11 1d 22 0 0 0 2 0 19 20 0 0 5 0 0 1b 0 17 17 23 4 f 1a fd 22 0 f 0 2 0
  //   18 c 1a d 10 1e 6 ff ff ff e6 13 1b 0 7 7 23 a 7 0 2 0 c 15 7 a c 7 21 0 3 7 1b 0 17 17 c 12 21 0 2
  //   3 9 3 3 0 0 0 a 29 3 2 0 0 0 a 21 0 1 2 3 1 f 30 e f 1c 3 3 4*0 1e 6 ff ff ff d1 d 12 f f 22 0 f 0 2
  //   0 18 1e 6 ff ff ff ef 21 0 4 0 21 0 3 0 21 0 2 0 21 0 1 0 13 21 0 6 7 21 3 5 0 0 0 f 21 1 1d 1 1b 0
  //   17 17 21 0 3 2 19 0 3 5 21 0 4 2 15 4 4 19 0 4 5 1c 1 12 a 1e 8 0 0 0 a 3 1 12 30 1e 4*0 4 3 1 11 37
  //   1c 1 11 a 1e 8 0 0 0 a 3 1 11 30 1e 4*0 4 3 1 11 37 22 2 11 19 3 0 19 1d 22 2 12 19 3 0 19 1d 15 2 8
  //   d 6 1e 6 ff ff ff 9e 13 1b 0 23 23 21 2 b 1 0 22 a 2 0 2 1 12 21 1 15 2 22 a 7 0 2 1 11 23 a 7 0 2 1
  //   10 21 1 14 1 19 0 7 6 1c 0 7 0 1e c ff ff ff e7 21 1 15 1 22 a 7 0 2 1 11 1b 0 7 7 22 a 7 0 2 1 11
  //   22 a 23 0 2 1 1c 23 a 1 0 2 1 1a 22 b 1 1a 1c 3 3 23 0 0 0 4 3 3 1c 0 0 0 4 d 4 1e 6 ff ff ff d7 3 0
  //   1a 1c 1b 0 1c 1c c 2 d 3 1e 6 ff ff ff 7b 1b 0 8 8 1b 0 9 9 1b 0 a a 1b 0 b b 1b 0 c c 1b 0 d d 1b 0
  //   e e 13 21 2 b 1 0 22 a 2 0 2 1 12 1b 0 17 17 23 b 1 1b 1c 21 1 15 8 22 a 1 0 2 1 1b 22 a 7 0 2 1 11
  //   1b 0 7 7 22 a 7 0 2 1 11 3 3 23 0 0 0 4 22 a 23 0 2 1 1c 3 3 1c 0 0 0 4 d 4 1e 6 ff ff ff bd 21 1 15
  //   4 22 a 7 0 2 1 11 23 a 7 0 2 1 10 21 1 14 1 19 0 7 6 1c 0 7 0 1e c ff ff ff e7 21 1 15 1 22 a 7 0 2
  //   1 11 1b 0 7 7 22 a 7 0 2 1 11 3 0 1b 1c 1b 0 1c 1c c 2 d 3 1e 6 ff ff ff 65 1b 0 8 8 1b 0 9 9 1b 0 a
  //   a 1b 0 b b 1b 0 c c 1b 0 d d 1b 0 e e 13 4*0 49 6e 69 74 20 42 49 4f 53 20 2e 20 2e 20 2e 20 0 52 41
  //   4d 3a 0 4b 42 20 2d 20 4f 4b 21 0 53 74 61 72 74 69 6e 67 20 73 79 73 74 65 6d 20 64 69 73 6b 20 2e
  //   20 2e 20 2e 0 44 65 76 69 63 65 20 6c 69 73 74 69 6e 67 3a 0 23 53 4c 4f 54 20 2d 20 23 44 45 56 43
  //   20 2d 20 23 56 45 4e 44 20 2d 20 23 4e 41 4d 45 29*5f 4*30 68 20 2d 20 4*30 68 20 2d 20 4*30 68 20
  //   2d 20 53 79 73 74 65 6d 4e 6f 6e 65 0 53 79 73 74 65 6d 0 44 69 73 6b 20 63 74 72 6c 72
  //   contents of rom_1 (hex, n*v repeats v):
  //   27 21 3 18 0 4 ff 0 21 3 19 0 4 7f 80 21 3 1a 0 0 3 e7 21 1 10 10 10 0 0 1 78 21 1 f a 22 a f 0 2 0
  //   18 22 a f 0 2 0 18 21 0 f 0 21 3 1a 0 0 3 f8 21 1 10 5 10 0 0 1 52 21 1 f 20 22 a f 0 2 0 18 10 0 0
  //   1 5d 21 1 10 8 21 3 1a 0 0 3 fd 10 0 0 1 32 21 1 f a 22 a f 0 2 0 18 22 a f 0 2 0 18 21 1 10 f 21 3
  //   1a 0 0 4 21 10 0 0 1 10 21 1 f a 22 a f 0 2 0 18 21 1 10 1d 21 3 1a 0 0 4 31 10 0 0 0 f5 21 1 f a 22
  //   a f 0 2 0 18 21 1 10 1d 21 3 1a 0 0 4 4e 10 0 0 0 da 21 1 f a 22 a f 0 2 0 18 21 1 10 1e 21 3 1a 0 0
  //   4 6b 10 0 0 0 bf 21 1 f a 22 a f 0 2 0 18 21 2 1e 0 1 21 3 1b 0 1 1 0 21 3 1a 0 2 1 0 1b 0 20 20 21
  //   1 20 3 1b 0 7 7 21 1 15 2 23 c 21 1a 3 3 1a 0 0 1 0 21 0 1f 1e 14 1f 2 3 0 1b 1f 22 c 21 1b 21 3 1b
  //   0 0 2 89 22 a 1b 0 3 1 4 21 3 1b 0 0 3 2b 22 a 1b 0 3 1 8 21 1 10 1a 21 3 1a 0 0 4 6 10 0 0 0 4b 1b
  //   0 8 8 1b 0 9 9 1b 0 a a 1b 0 b b 1b 0 c c 1b 0 d d 1b 0 e e 21 3 1a 0 5 0 0 1b 0 1c 1c 21 3 2 4*0 21
  //   3 3 0 0 0 1 23 a 1d 0 3 1 4 11 1d 22 0 0 0 2 0 19 20 0 0 5 0 0 1b 0 17 17 23 4 f 1a fd 22 0 f 0 2 0
  //   18 c 1a d 10 1e 6 ff ff ff e6 13 1b 0 7 7 23 a 7 0 2 0 c 15 7 a c 7 21 0 3 7 1b 0 17 17 c 12 21 0 2
  //   3 9 3 3 0 0 0 a 29 3 2 0 0 0 a 21 0 1 2 3 1 f 30 e f 1c 3 3 4*0 1e 6 ff ff ff d1 d 12 f f 22 0 f 0 2
  //   0 18 1e 6 ff ff ff ef 21 0 4 0 21 0 3 0 21 0 2 0 21 0 1 0 13 21 0 6 7 21 3 5 0 0 0 f 21 1 1d 1 1b 0
  //   17 17 21 0 3 2 19 0 3 5 21 0 4 2 15 4 4 19 0 4 5 1c 1 12 a 1e 8 0 0 0 a 3 1 12 30 1e 4*0 4 3 1 11 37
  //   1c 1 11 a 1e 8 0 0 0 a 3 1 11 30 1e 4*0 4 3 1 11 37 22 2 11 19 3 0 19 1d 22 2 12 19 3 0 19 1d 15 2 8
  //   d 6 1e 6 ff ff ff 9e 13 1b 0 23 23 21 2 b 1 0 22 a 2 0 2 1 12 21 1 15 2 22 a 7 0 2 1 11 23 a 7 0 2 1
  //   10 21 1 14 1 19 0 7 6 1c 0 7 0 1e c ff ff ff e7 21 1 15 1 22 a 7 0 2 1 11 1b 0 7 7 22 a 7 0 2 1 11
  //   22 a 23 0 2 1 1c 23 a 1 0 2 1 1a 22 b 1 1a 1c 3 3 23 0 0 0 4 3 3 1c 0 0 0 4 d 4 1e 6 ff ff ff d7 3 0
  //   1a 1c 1b 0 1c 1c c 2 d 3 1e 6 ff ff ff 7b 1b 0 8 8 1b 0 9 9 1b 0 a a 1b 0 b b 1b 0 c c 1b 0 d d 1b 0
  //   e e 13 21 2 b 1 0 22 a 2 0 2 1 12 1b 0 17 17 23 b 1 1b 1c 21 1 15 8 22 a 1 0 2 1 1b 22 a 7 0 2 1 11
  //   1b 0 7 7 22 a 7 0 2 1 11 3 3 23 0 0 0 4 22 a 23 0 2 1 1c 3 3 1c 0 0 0 4 d 4 1e 6 ff ff ff bd 21 1 15
  //   4 22 a 7 0 2 1 11 23 a 7 0 2 1 10 21 1 14 1 19 0 7 6 1c 0 7 0 1e c ff ff ff e7 21 1 15 1 22 a 7 0 2
  //   1 11 1b 0 7 7 22 a 7 0 2 1 11 3 0 1b 1c 1b 0 1c 1c c 2 d 3 1e 6 ff ff ff 65 1b 0 8 8 1b 0 9 9 1b 0 a
  //   a 1b 0 b b 1b 0 c c 1b 0 d d 1b 0 e e 13 4*0 49 6e 69 74 20 42 49 4f 53 20 2e 20 2e 20 2e 20 0 52 41
  //   4d 3a 0 4b 42 20 2d 20 4f 4b 21 0 53 74 61 72 74 69 6e 67 20 73 79 73 74 65 6d 20 64 69 73 6b 20 2e
  //   20 2e 20 2e 0 44 65 76 69 63 65 20 6c 69 73 74 69 6e 67 3a 0 23 53 4c 4f 54 20 2d 20 23 44 45 56 43
  //   20 2d 20 23 56 45 4e 44 20 2d 20 23 4e 41 4d 45 29*5f 4*30 68 20 2d 20 4*30 68 20 2d 20 4*30 68 20
  //   2d 20 53 79 73 74 65 6d 4e 6f 6e 65 0 53 79 73 74 65 6d 0 44 69 73 6b 20 63 74 72 6c 72
endmodule

module BRIDGE (
  input  [31:0] INST_ADDR_IN,
  input  [31:0] DATA_ADDR_IN,
  output READ_RAM,
  output SEL_BIOS,
  output SEL_CMOS,
  output SEL_MMIO,
  output SEL_RAM
);

  wire comparator_1_eq, comparator_1_gt, comparator_2_eq, comparator_2_gt, comparator_3_eq, comparator_3_lt,
       comparator_4_eq, comparator_4_gt, comparator_5_eq, comparator_5_lt, comparator_6_eq, comparator_6_gt,
       comparator_7_eq, comparator_7_lt, comparator_8_eq, comparator_8_gt, comparator_9_eq, comparator_9_lt,
       or_2_out, or_3_out, or_4_out, or_5_out, or_6_out, or_7_out, or_8_out, or_9_out;

  or or_1 (READ_RAM, comparator_1_gt, comparator_1_eq);
  Comparator #(.mode("unsigned"), .width(32)) comparator_1 (
    .a(INST_ADDR_IN), .b(32'h10000), .gt(comparator_1_gt), .eq(comparator_1_eq));  // open: lt
  or or_2 (or_2_out, comparator_2_gt, comparator_2_eq);
  Comparator #(.mode("unsigned"), .width(32)) comparator_2 (
    .a(DATA_ADDR_IN), .b({32{1'b0}}), .gt(comparator_2_gt), .eq(comparator_2_eq));  // open: lt
  and and_1 (SEL_BIOS, or_2_out, or_3_out);
  or or_3 (or_3_out, comparator_3_eq, comparator_3_lt);
  Comparator #(.mode("unsigned"), .width(32)) comparator_3 (
    .a(DATA_ADDR_IN), .b(32'hffff), .eq(comparator_3_eq), .lt(comparator_3_lt));  // open: gt
  or or_4 (or_4_out, comparator_4_gt, comparator_4_eq);
  Comparator #(.mode("unsigned"), .width(32)) comparator_4 (
    .a(DATA_ADDR_IN), .b(32'h10000), .gt(comparator_4_gt), .eq(comparator_4_eq));  // open: lt
  and and_2 (SEL_CMOS, or_4_out, or_5_out);
  or or_5 (or_5_out, comparator_5_eq, comparator_5_lt);
  Comparator #(.mode("unsigned"), .width(32)) comparator_5 (
    .a(DATA_ADDR_IN), .b(32'h1ffff), .eq(comparator_5_eq), .lt(comparator_5_lt));  // open: gt
  or or_6 (or_6_out, comparator_6_gt, comparator_6_eq);
  Comparator #(.mode("unsigned"), .width(32)) comparator_6 (
    .a(DATA_ADDR_IN), .b(32'h20000), .gt(comparator_6_gt), .eq(comparator_6_eq));  // open: lt
  and and_3 (SEL_MMIO, or_6_out, or_7_out);
  or or_7 (or_7_out, comparator_7_eq, comparator_7_lt);
  Comparator #(.mode("unsigned"), .width(32)) comparator_7 (
    .a(DATA_ADDR_IN), .b(32'h2ffff), .eq(comparator_7_eq), .lt(comparator_7_lt));  // open: gt
  or or_8 (or_8_out, comparator_8_gt, comparator_8_eq);
  Comparator #(.mode("unsigned"), .width(32)) comparator_8 (
    .a(DATA_ADDR_IN), .b(32'h30000), .gt(comparator_8_gt), .eq(comparator_8_eq));  // open: lt
  and and_4 (SEL_RAM, or_8_out, or_9_out);
  or or_9 (or_9_out, comparator_9_eq, comparator_9_lt);
  Comparator #(.mode("unsigned"), .width(32)) comparator_9 (
    .a(DATA_ADDR_IN), .b({32{1'b1}}), .eq(comparator_9_eq), .lt(comparator_9_lt));  // open: gt
endmodule

module DISK_CTRL (
  input  CLK,
  input  [7:0] PORT_SEL,
  input  [3:0] MAIN_CTRL,
  input  [31:0] DATA_IN,
  input  [63:0] DISK_IN,
  output [31:0] DATA_OUT,
  output [31:0] DISK_ADDR,
  output DISK_WE,
  output CLK_OUT,
  output [63:0] DISK_OUT
);

  wire and_1_out, and_2_out, and_3_out, and_4_out, and_5_out, and_7_out, and_8_out, and_10_out, BUSY_q,
       comparator_1_eq, d_ff_1_q, decoder_1_out0, decoder_1_out2, decoder_1_out16, decoder_1_out17,
       decoder_1_out18, decoder_1_out26, decoder_1_out27, decoder_1_out28, or_1_out, or_2_out, or_3_out,
       or_4_out, or_5_out;
  wire [7:0] DEVICE_STATUS_q;
  wire [10:0] adder_2_out;
  wire [31:0] BUFFER_OFFS_q, CONTROL_q, DISK_DIN_q, DISK_LBA_q, register_1_q, shifter_1_out, undriven_2;
  wire [31:8] undriven;

  Decoder #(.select(5)) decoder_1 (
    .out0(decoder_1_out0), .out2(decoder_1_out2), .out16(decoder_1_out16), .out17(decoder_1_out17),
    .out18(decoder_1_out18), .out26(decoder_1_out26), .out27(decoder_1_out27), .out28(decoder_1_out28),
    .sel(PORT_SEL[4:0]));  // open: out1, out3, out4, out5, out6, out7, out8, out9, out10, out11, out12, out13, out14, out15, out19, out20, out21, out22, out23, out24, out25, out29, out30, out31, en
  Register DEVICE_STATUS (.D(DATA_IN[7:0]), .en(and_1_out), .clk(CLK), .Q(DEVICE_STATUS_q), .clr(MAIN_CTRL[1]));
  and and_1 (and_1_out, MAIN_CTRL[2], decoder_1_out2);
  Register #(.width(32)) CONTROL (.D(DATA_IN), .en(and_2_out), .clk(CLK), .Q(CONTROL_q), .clr(MAIN_CTRL[1]));
  and and_2 (and_2_out, MAIN_CTRL[2], decoder_1_out17);
  Register #(.width(32)) DISK_LBA (.D(DATA_IN), .en(and_3_out), .clk(CLK), .Q(DISK_LBA_q), .clr(MAIN_CTRL[1]));
  and and_3 (and_3_out, MAIN_CTRL[2], decoder_1_out18);
  Register #(.width(32)) DISK_DIN (.D(DATA_IN), .en(and_4_out), .clk(CLK), .Q(DISK_DIN_q), .clr(MAIN_CTRL[1]));
  and and_4 (and_4_out, MAIN_CTRL[2], decoder_1_out27);
  Register #(.width(32)) BUFFER_OFFS (.D(DATA_IN), .en(and_5_out), .clk(CLK), .Q(BUFFER_OFFS_q), .clr(MAIN_CTRL[1]));
  and and_5 (and_5_out, MAIN_CTRL[2], decoder_1_out28);
  Pull_Resistor pull_resistor_1 (.node(DATA_OUT));
  assign DATA_OUT = decoder_1_out0 ? 32'h1 : 32'bz;  // Controlled_Buffer controlled_buffer_1
  Pull_Resistor pull_resistor_2 (.node(DEVICE_STATUS_q));
  Pull_Resistor pull_resistor_3 (.node(DATA_OUT));
  assign DATA_OUT = decoder_1_out2 ? {undriven, DEVICE_STATUS_q} : 32'bz;  // Controlled_Buffer controlled_buffer_2
  Pull_Resistor pull_resistor_4 (.node(DATA_OUT));
  assign DATA_OUT = decoder_1_out17 ? CONTROL_q : 32'bz;  // Controlled_Buffer controlled_buffer_3
  Pull_Resistor pull_resistor_5 (.node(DATA_OUT));
  assign DATA_OUT = decoder_1_out18 ? DISK_LBA_q : 32'bz;  // Controlled_Buffer controlled_buffer_4
  Pull_Resistor pull_resistor_6 (.node(DATA_OUT));
  assign DATA_OUT = decoder_1_out27 ? DISK_DIN_q : 32'bz;  // Controlled_Buffer controlled_buffer_5
  assign DATA_OUT = decoder_1_out28 ? BUFFER_OFFS_q : 32'bz;  // Controlled_Buffer controlled_buffer_6
  D_Flip_Flop d_ff_1 (.D(comparator_1_eq), .clk(comparator_1_eq), .Q(d_ff_1_q), .reset(or_1_out));  // open: Qn, preset
  Pull_Resistor pull_resistor_7 (.node(DATA_OUT));
  assign DATA_OUT = decoder_1_out26 ? undriven_2 : 32'bz;  // Controlled_Buffer controlled_buffer_7
  and and_6 (CLK_OUT, CLK, ~d_ff_1_q);  // AND_Gate
  or or_1 (or_1_out, CONTROL_q[0], MAIN_CTRL[1]);
  D_Flip_Flop BUSY (.D(and_7_out), .clk(and_7_out), .Q(BUSY_q), .reset(or_2_out));  // open: Qn, preset
  or or_2 (or_2_out, MAIN_CTRL[1], or_4_out);
  Register #(.width(11)) register_1 (
    .D(adder_2_out), .en(and_7_out), .clk(CLK_OUT), .Q(register_1_q[10:0]), .clr(or_4_out));
  or or_3 (or_3_out, CONTROL_q[2], CONTROL_q[1]);
  and and_7 (and_7_out, or_3_out, MAIN_CTRL[0]);
  Pull_Resistor pull_resistor_8 (.node(DATA_OUT));
  assign DATA_OUT[0] = decoder_1_out16 ? BUSY_q : 1'bz;  // Controlled_Buffer controlled_buffer_8
  Shifter #(.width(32)) shifter_1 (.in(DISK_LBA_q), .\dist (5'b01010), .out(shifter_1_out));
  Pull_Resistor pull_resistor_9 (.node(register_1_q));
  Pull_Resistor pull_resistor_10 (.node(register_1_q[10:0]));
  or or_4 (or_4_out, MAIN_CTRL[1], and_8_out);
  and and_8 (and_8_out, CLK, or_5_out);
  or or_5 (or_5_out, MAIN_CTRL[1], CONTROL_q[0], d_ff_1_q);
  Adder #(.width(32)) adder_1 (.a(shifter_1_out), .b(register_1_q), .out(DISK_ADDR));  // open: cin, cout
  Adder #(.width(11)) adder_2 (.a(register_1_q[10:0]), .b(11'h8), .out(adder_2_out));  // open: cin, cout
  Comparator #(.mode("unsigned"), .width(11)) comparator_1 (
    .a(register_1_q[10:0]), .b(11'h400), .eq(comparator_1_eq));  // open: gt, lt
  and and_9 (DISK_WE, MAIN_CTRL[0], CONTROL_q[2]);
  and and_10 (and_10_out, CONTROL_q[1], MAIN_CTRL[0]);
  // DualRAM #(.addrWidth(10), .clearpin("true"), .enables("line"), .line("octo"), .misaligned("true")) dualram_1: pin names not known; wires that end beside it: register_1_q[9:0], and_10_out, CLK_OUT, DISK_IN[63:56], DISK_IN[55:48], DISK_IN[47:40], DISK_IN[39:32], DISK_IN[31:24], DISK_IN[23:16], DISK_IN[15:8], DISK_IN[7:0], BUFFER_OFFS_q[9:0], CONTROL_q[3], CONTROL_q[3], CONTROL_q[3], CONTROL_q[3], CONTROL_q[3], MAIN_CTRL[1]
endmodule
