// Logisim project i80148.circ as structural Verilog: 2 circuits, main circuit CPU
module CPU (
  input  [63:0] INST_IN,
  input  [31:0] DATA_IN,
  input  [7:0] INT_IN,
  input  CALL_IRQ,
  input  ENABLE,
  input  CLK,
  input  RESET,
  output LE0,
  output LE1,
  output LE2,
  output LE3,
  output [31:0] DATA_OUT,
  output MWE,
  output MOE,
  output [31:0] ADDR_OUT,
  output [31:0] IC_OUT,
  output [7:0] FLAGS_OUT,
  output IRQ_EN
);

  wire ABSB, adder_6_cout, ALUEN, and_1_out, and_2_out, and_3_out, and_4_out, and_5_out, and_6_out,
       and_7_out, and_8_out, and_9_out, and_10_out, and_11_out, and_12_out, and_13_out, and_14_out,
       and_15_out, and_16_out, and_19_out, and_20_out, and_21_out, and_22_out, and_23_out, and_24_out,
       and_25_out, and_26_out, and_27_out, and_28_out, and_29_out, and_30_out, and_31_out, and_32_out,
       and_33_out, and_34_out, and_35_out, and_36_out, and_37_out, and_38_out, and_39_out, and_40_out,
       and_41_out, and_42_out, and_43_out, BSW2IMM, CALLINT, CNSB, CNSC, CNSDISP, comparator_1_eq, DCSP,
       decoder_1_out1, decoder_1_out2, decoder_1_out3, decoder_1_out4, decoder_1_out5, decoder_1_out6,
       decoder_1_out7, decoder_2_out1, decoder_2_out2, decoder_2_out3, decoder_2_out4, decoder_2_out5,
       decoder_2_out6, decoder_2_out7, decoder_2_out8, decoder_2_out9, decoder_2_out10, decoder_2_out11,
       decoder_2_out12, decoder_2_out13, decoder_2_out14, decoder_2_out15, decoder_2_out16, decoder_2_out17,
       decoder_2_out18, decoder_2_out19, decoder_2_out20, decoder_2_out21, decoder_2_out23, decoder_2_out24,
       decoder_2_out25, decoder_2_out26, decoder_2_out27, decoder_2_out28, decoder_2_out29, decoder_2_out30,
       decoder_2_out31, decoder_2_out32, decoder_2_out33, decoder_2_out34, decoder_2_out35, decoder_2_out36,
       decoder_3_out2, decoder_3_out3, DISIRQ, ENIRQ, HALT_FL_q, INDB, INT_EN_q, multiplexer_18_out,
       multiplexer_31_out, multiplexer_32_out, not_1_out, not_2_out, not_3_out, not_4_out, or_1_out,
       or_2_out, or_3_out, or_4_out, or_5_out, or_6_out, or_7_out, or_8_out, or_9_out, or_10_out, or_11_out,
       or_12_out, or_13_out, or_14_out, or_15_out, or_16_out, or_17_out, or_18_out, or_19_out, or_20_out,
       or_22_out, or_23_out, or_24_out, or_25_out, or_26_out, or_27_out, or_28_out, or_29_out, or_30_out,
       or_31_out, or_32_out, or_34_out, or_36_out, or_38_out, pull_resistor_158_node, pull_resistor_159_node,
       RADDR2SP, RELB, RETINT, RIDT, SETSG, SIMM, SMEM, SPOUTIC, SPRINC, SPWRIC, SREG, subtractor_2_bout,
       SWB2I, SWD2R, UPDFL, UPDSP, USEBR, USEC, USECR, USEFL, WAIT_FL_q, WREG;
  wire [1:0] not_6_out;
  wire [2:0] comparator_2_gt, comparator_3_gt, comparator_4_gt, comparator_5_gt, comparator_6_gt,
       comparator_7_gt, multiplexer_24_out, multiplexer_37_out, multiplexer_38_out, multiplexer_39_out,
       multiplexer_43_out, multiplexer_46_out, rom_1_data;
  wire [3:0] LENGHT_out, multiplexer_8_out, pla_2_out, pull_resistor_157_node;
  wire [4:0] multiplexer_42_out;
  wire [5:0] multiplexer_3_out, multiplexer_4_out, multiplexer_5_out, multiplexer_6_out,
       pull_resistor_71_node, pull_resistor_72_node, pull_resistor_73_node, pull_resistor_74_node,
       pull_resistor_75_node, pull_resistor_76_node, pull_resistor_77_node, pull_resistor_78_node,
       pull_resistor_79_node, pull_resistor_80_node, pull_resistor_82_node, pull_resistor_83_node,
       pull_resistor_84_node, pull_resistor_85_node, pull_resistor_86_node, pull_resistor_87_node,
       pull_resistor_88_node, pull_resistor_89_node, pull_resistor_90_node, pull_resistor_91_node,
       pull_resistor_92_node, pull_resistor_93_node, pull_resistor_94_node, pull_resistor_95_node,
       pull_resistor_96_node, pull_resistor_97_node, pull_resistor_98_node, pull_resistor_99_node,
       pull_resistor_100_node, pull_resistor_101_node, pull_resistor_102_node, pull_resistor_103_node,
       pull_resistor_104_node, pull_resistor_105_node, pull_resistor_106_node, pull_resistor_107_node,
       pull_resistor_108_node, pull_resistor_109_node, pull_resistor_110_node, pull_resistor_111_node,
       pull_resistor_112_node, pull_resistor_113_node, pull_resistor_114_node, pull_resistor_115_node,
       pull_resistor_116_node, pull_resistor_117_node, pull_resistor_118_node, pull_resistor_119_node,
       pull_resistor_120_node, pull_resistor_121_node, pull_resistor_122_node, pull_resistor_123_node,
       pull_resistor_124_node, pull_resistor_125_node, pull_resistor_126_node, pull_resistor_127_node,
       pull_resistor_128_node, pull_resistor_129_node, pull_resistor_130_node, pull_resistor_131_node,
       pull_resistor_132_node, pull_resistor_133_node, pull_resistor_134_node, pull_resistor_135_node,
       pull_resistor_136_node, pull_resistor_137_node, pull_resistor_138_node, pull_resistor_139_node,
       pull_resistor_140_node, pull_resistor_141_node, pull_resistor_142_node, pull_resistor_143_node,
       pull_resistor_144_node, pull_resistor_145_node, pull_resistor_146_node, pull_resistor_147_node,
       pull_resistor_148_node, pull_resistor_149_node, pull_resistor_150_node, pull_resistor_151_node,
       pull_resistor_152_node, pull_resistor_153_node, pull_resistor_154_node, pull_resistor_155_node,
       pull_resistor_156_node;
  wire [7:0] and_17_out, and_18_out, multiplexer_1_out, multiplexer_22_out, or_21_out, pull_resistor_1_node,
       pull_resistor_2_node, pull_resistor_3_node, pull_resistor_4_node, pull_resistor_5_node,
       pull_resistor_6_node, pull_resistor_7_node, pull_resistor_166_node, pull_resistor_166_node_3, X1_q,
       X2_q, X3_q, X4_q, X5_q, X6_q, XL1_q, XL2_q, XL3_q, XL4_q, XL5_q, XL6_q;
  wire [15:0] EX1_q, EX2_q, EX3_q, EX4_q, EX5_q, EX6_q, EX7_q, pla_1_out;
  wire [31:0] A0_q, A1_q, A2_q, A3_q, A4_q, A5_q, A6_q, A7_q, adder_1_out, adder_2_out, adder_3_out,
       adder_4_out, adder_5_out, adder_6_out, adder_7_out, adder_8_out, adder_9_out, and_44_out,
       bit_extender_1_out, BP_q, demultiplexer_1_out0, demultiplexer_1_out1, divider_1_out, divider_1_rem,
       divider_2_out, divider_2_rem, IC_BKUP_q, IDT_q, IX_q, IY_q, multiplexer_2_out, multiplexer_7_out,
       multiplexer_9_out, multiplexer_10_out, multiplexer_11_out, multiplexer_12_out, multiplexer_13_out,
       multiplexer_14_out, multiplexer_15_out, multiplexer_16_out, multiplexer_17_out, multiplexer_19_out,
       multiplexer_20_out, multiplexer_21_out, multiplexer_23_out, multiplexer_25_out, multiplexer_26_out,
       multiplexer_27_out, multiplexer_29_out, multiplexer_30_out, multiplexer_33_out, multiplexer_34_out,
       multiplexer_35_out, multiplexer_36_out, multiplexer_40_out, multiplexer_45_out, multiplier_1_out,
       multiplier_2_out, not_5_out, not_7_out, or_37_out, pull_resistor_55_node, pull_resistor_56_node,
       pull_resistor_57_node, pull_resistor_58_node, pull_resistor_59_node, pull_resistor_60_node,
       pull_resistor_61_node, pull_resistor_62_node, pull_resistor_63_node, pull_resistor_64_node,
       pull_resistor_65_node, pull_resistor_66_node, pull_resistor_67_node, pull_resistor_68_node,
       pull_resistor_69_node, pull_resistor_70_node, pull_resistor_174_node, pull_resistor_176_node,
       pull_resistor_177_node, pull_resistor_178_node, pull_resistor_180_node, shifter_1_out, shifter_2_out,
       shifter_3_out, shifter_4_out, shifter_5_out, shifter_6_out, SP_q, subtractor_1_out, subtractor_2_out,
       xor_1_out;
  wire [31:4] pull_resistor_44_node;
  wire [31:8] pull_resistor_45_node, pull_resistor_47_node, pull_resistor_49_node, pull_resistor_51_node,
       pull_resistor_52_node, pull_resistor_53_node, pull_resistor_54_node, pull_resistor_81_node,
       pull_resistor_167_node, pull_resistor_168_node, pull_resistor_169_node, pull_resistor_170_node,
       pull_resistor_171_node, pull_resistor_172_node, pull_resistor_173_node, pull_resistor_175_node,
       pull_resistor_179_node;
  wire [31:16] pull_resistor_46_node, pull_resistor_48_node, pull_resistor_50_node, pull_resistor_160_node,
       pull_resistor_161_node, pull_resistor_162_node, pull_resistor_163_node, pull_resistor_164_node,
       pull_resistor_165_node, pull_resistor_166_node_2;
  wire [35:0] CU_out;

  and and_1 (and_1_out, ENABLE, ~or_1_out, CLK);  // AND_Gate
  or or_1 (or_1_out, WAIT_FL_q, HALT_FL_q);
  D_Flip_Flop HALT_FL (.D(CU_out[0]), .clk(CU_out[0]), .Q(HALT_FL_q), .reset(RESET));  // open: Qn, preset
  Decoder #(.select(4)) decoder_1 (
    .out1(decoder_1_out1), .out2(decoder_1_out2), .out3(decoder_1_out3), .out4(decoder_1_out4),
    .out5(decoder_1_out5), .out6(decoder_1_out6), .out7(decoder_1_out7), .sel(LENGHT_out));  // open: out0, out8, out9, out10, out11, out12, out13, out14, out15, en
  or or_2 (or_2_out, decoder_1_out1, decoder_1_out2, decoder_1_out3, decoder_1_out4, decoder_1_out5, decoder_1_out6, decoder_1_out7);
  or or_3 (or_3_out, decoder_1_out2, decoder_1_out3, decoder_1_out4, decoder_1_out5, decoder_1_out6, decoder_1_out7);
  or or_4 (or_4_out, decoder_1_out3, decoder_1_out4, decoder_1_out5, decoder_1_out6, decoder_1_out7);
  or or_5 (or_5_out, decoder_1_out4, decoder_1_out5, decoder_1_out6, decoder_1_out7);
  or or_6 (or_6_out, decoder_1_out5, decoder_1_out6, decoder_1_out7);
  or or_7 (or_7_out, decoder_1_out6, decoder_1_out7);
  D_Flip_Flop WAIT_FL (.D(CU_out[1]), .clk(CU_out[1]), .Q(WAIT_FL_q), .reset(or_8_out));  // open: Qn, preset
  or or_8 (or_8_out, RESET, and_3_out);
  PLA #(.in_width(16), .out_width(16), .\table ("00000000xxxxxxxx 0000000000000000 # NOP\n00000001xxxxxxxx 0000000000000000 # HALT\n00000010xxxxxxxx 0000000000000000 # WAIT\n0000001100000000 0011100011101100 # ADD\n0000001100000001 0100000011101000 # ADD.b\n0000001100000010 0100100011101001 # ADD.w\n0000001100000011 0101000011101010 # ADD.dw\n0000010000000000 0011100011101100 # ADC\n0000010000000001 0100000011101000 # ADC.b\n0000010000000010 0100100011101001 # ADC.w\n0000010000000011 0101000011101010 # ADC.dw\n0000010100000000 0011100011110100 # SUB\n0000010100000001 0100000011110000 # SUB.b\n0000010100000010 0100100011110001 # SUB.w\n0000010100000011 0101000011110010 # SUB.dw\n0000011000000000 0011100011110100 # SBB\n0000011000000001 0100000011110000 # SBB.b\n0000011000000010 0100100011110001 # SBB.w\n0000011000000011 0101000011110010 # SBB.dw\n0000011100000000 0011100011100100 # MUL\n0000011100000001 0100000011100000 # MUL.b\n0000011100000010 0100100011100001 # MUL.w\n0000011100000011 0101000011100010 # MUL.dw\n0000100000000000 0011100011100100 # IMUL\n0000100000000001 0100000011100000 # IMUL.b\n0000100000000010 0100100011100001 # IMUL.w\n0000100000000011 0101000011100010 # IMUL.dw\n0000100100000000 0011100011100100 # DIV\n0000100100000001 0100000011100000 # DIV.b\n0000100100000010 0100100011100001 # DIV.w\n0000100100000011 0101000011100010 # DIV.dw\n0000101000000000 0011100011100100 # IDIV\n0000101000000001 0100000011100000 # IDIV.b\n0000101000000010 0100100011100001 # IDIV.w\n0000101000000011 0101000011100010 # IDIV.dw\n00001011xxxxxxxx 0001100011100100 # NOT\n00001100xxxxxxxx 0001100011101100 # INC\n00001101xxxxxxxx 0001100011110100 # DEC\n00001110xxxxxxxx 0001000000000010 # PUSH\n00001111xxxxxxxx 0000100000000100 # POP\n00010000xxxxxxxx 0011000000000010 # CALL\n00010001xxxxxxxx 0001000000000010 # CALLR\n00010010xxxxxxxx 0011000000000010 # CLABS\n00010011xxxxxxxx 0000000000000010 # RET\n00010100xxxxxxxx 0111000011100100 # LSL\n00010101xxxxxxxx 0111000011100100 # LSR\n00010110xxxxxxxx 0111000011100100 # ASR\n00010111xxxxxxxx 0111000011100100 # ROL\n00011000xxxxxxxx 0111000011100100 # ROR\n0001100100000000 0011100011100100 # AND\n0001101000000000 0011100011100100 # OR\n0001101100000000 0011100011100100 # XOR\n0001110000000000 0011111111110100 # CMP\n0001110000000001 0100011111111000 # CMP.b\n0001110000000010 0100111111111001 # CMP.w\n0001110000000011 0101011111111010 # CMP.dw\n0001110100000000 0011111111111100 # ICMP\n0001110100000001 0100011111111000 # ICMP.b\n0001110100000010 0100111111111001 # ICMP.w\n0001110100000011 0101011111111010 # ICMP.dw\n00011110xxxxxxxx 0101100000000000 # JMP\n00011111xxxxxxxx 0110000000000100 # JMPR\n00100000xxxxxxxx 0101100000000000 # JMA\n0010000100000000 0111100000000100 # COPY\n0010000100000001 1000000000000000 # LDI.b\n0010000100000010 1000100000000001 # LDI.w\n0010000100000011 1001000000000010 # LDI.dw\n0010001000000000 1001100000000000 # STR.b F\n0010001000000001 1010000000000000 # STR.b S\n0010001000000010 1010100000000000 # STR.b R\n0010001000000011 1011000000000000 # STR.b SD\n0010001000000100 1011100000000000 # STR.b RD\n0010001000000101 1001100000000001 # STR.w F\n0010001000000110 1010000000000001 # STR.w S\n0010001000000111 1010100000000001 # STR.w R\n0010001000001000 1011000000000001 # STR.w SD\n0010001000001001 1011100000000001 # STR.w RD\n0010001000001010 1001100000000010 # STR.dw F\n0010001000001011 1010000000000010 # STR.dw S\n0010001000001100 1010100000000010 # STR.dw R\n0010001000001101 1011000000000010 # STR.dw SD\n0010001000001110 1011100000000010 # STR.dw RD\n0010001100000000 1100000000000000 # LOD.b F\n0010001100000001 1100100000000000 # LOD.b S\n0010001100000010 1101000000000000 # LOD.b R\n0010001100000011 1101100000000000 # LOD.b SD\n0010001100000100 1110000000000000 # LOD.b RD\n0010001100000101 1100000000000001 # LOD.w F\n0010001100000110 1100100000000001 # LOD.w S\n0010001100000111 1101000000000001 # LOD.w R\n0010001100001000 1101100000000001 # LOD.w SD\n0010001100001001 1110000000000001 # LOD.w RD\n0010001100001010 1100000000000010 # LOD.dw F\n0010001100001011 1100100000000010 # LOD.dw S\n0010001100001100 1101000000000010 # LOD.dw R\n0010001100001101 1101100000000010 # LOD.dw SD\n0010001100001110 1110000000000010 # LOD.dw RD\n00100101xxxxxxxx 0010000000000010 # INT\n00100110xxxxxxxx 0000000000000000 # IRET\n00100111xxxxxxxx 0000000000000000 # CLI\n00101000xxxxxxxx 0000000000000000 # STI\n0010100100000000 0011100011100100 # REM\n0010100100000001 0100000011100000 # REM.b\n0010100100000010 0100100011100001 # REM.w\n0010100100000011 0101000011100010 # REM.dw\n0010101000000000 0011100011100100 # IREM\n0010101000000001 0100000011100000 # IREM.b\n0010101000000010 0100100011100001 # IREM.w\n0010101000000011 0101000011100010 # IREM.dw")) pla_1 (
    .in(INST_IN[63:48]), .out(pla_1_out));
  Pull_Resistor pull_resistor_1 (.node(pull_resistor_1_node));
  assign pull_resistor_1_node = or_2_out ? INST_IN[55:48] : 8'bz;  // Controlled_Buffer controlled_buffer_1
  Pull_Resistor pull_resistor_2 (.node(pull_resistor_2_node));
  assign pull_resistor_2_node = or_3_out ? INST_IN[47:40] : 8'bz;  // Controlled_Buffer controlled_buffer_2
  Pull_Resistor pull_resistor_3 (.node(pull_resistor_3_node));
  assign pull_resistor_3_node = or_4_out ? INST_IN[39:32] : 8'bz;  // Controlled_Buffer controlled_buffer_3
  Pull_Resistor pull_resistor_4 (.node(pull_resistor_4_node));
  assign pull_resistor_4_node = or_5_out ? INST_IN[31:24] : 8'bz;  // Controlled_Buffer controlled_buffer_4
  Pull_Resistor pull_resistor_5 (.node(pull_resistor_5_node));
  assign pull_resistor_5_node = or_6_out ? INST_IN[23:16] : 8'bz;  // Controlled_Buffer controlled_buffer_5
  Pull_Resistor pull_resistor_6 (.node(pull_resistor_6_node));
  assign pull_resistor_6_node = or_7_out ? INST_IN[15:8] : 8'bz;  // Controlled_Buffer controlled_buffer_6
  Pull_Resistor pull_resistor_7 (.node(pull_resistor_7_node));
  assign pull_resistor_7_node = decoder_1_out7 ? INST_IN[7:0] : 8'bz;  // Controlled_Buffer controlled_buffer_7
  PLA #(.in_width(5), .out_width(4), .\table ("00000 0000 # S0\n00001 0001 # S1\n00010 0001 # S2\n00011 0001 # S3\n00100 0001 # S4\n00101 0010 # S5\n00110 0100 # S6\n00111 0011 # A0\n01000 0011 # A1\n01001 0100 # A2\n01010 0110 # A3\n01011 0101 # J0\n01100 0010 # J1\n01101 0101 # I0\n01110 0010 # H0\n01111 0011 # D0\n10000 0011 # D1B\n10001 0100 # D1W\n10010 0110 # D1DW\n10011 0110 # D2F\n10100 0100 # D2S\n10101 0011 # D2R\n10110 0101 # D2SD\n10111 0100 # D2RD\n11000 0110 # D3F\n11001 0100 # D3S\n11010 0011 # D3R\n11011 0101 # D3SD\n11100 0100 # D3RD")) LENGHT (
    .in(pla_1_out[15:11]), .out(LENGHT_out));
  PLA #(.in_width(16), .out_width(36), .\table ("00000000xxxxxxxx 000000000000000000000000000000000000 # NOP\n00000001xxxxxxxx 000000000000000000000000000000000001 # HALT\n00000010xxxxxxxx 000000000000000000000000000000000010 # WAIT\n0000001100000000 000000000010000000000000010000000100 # ADD\n0000001100000001 000000000010000000000000010000100100 # ADD.b\n0000001100000010 000000000010000000000000010000100100 # ADD.w\n0000001100000011 000000000010000000000000010000100100 # ADD.dw\n0000010000000000 000000000010000000000000010001000100 # ADC\n0000010000000001 000000000010000000000000010001100100 # ADC.b\n0000010000000010 000000000010000000000000010001100100 # ADC.w\n0000010000000011 000000000010000000000000010001100100 # ADC.dw\n0000010100000000 000000000010000000000000010000000100 # SUB\n0000010100000001 000000000010000000000000010000100100 # SUB.b\n0000010100000010 000000000010000000000000010000100100 # SUB.w\n0000010100000011 000000000010000000000000010000100100 # SUB.dw\n0000011000000000 000000000010000000000000010010000100 # SBB\n0000011000000001 000000000010000000000000010010100100 # SBB.b\n0000011000000010 000000000010000000000000010010100100 # SBB.w\n0000011000000010 000000000010000000000000010010100100 # SBB.dw\n0000011100000000 000000000010000000000000010000000100 # MUL\n0000011100000001 000000000010000000000000010000100100 # MUL.b\n0000011100000010 000000000010000000000000010000100100 # MUL.w\n0000011100000011 000000000010000000000000010000100100 # MUL.dw\n0000100000000000 000000000010000000000000010000001100 # IMUL\n0000100000000001 000000000010000000000000010000101100 # IMUL.b\n0000100000000010 000000000010000000000000010000101100 # IMUL.w\n0000100000000011 000000000010000000000000010000101100 # IMUL.dw\n0000100100000000 000000000010000000000000010000000100 # DIV\n0000100100000001 000000000010000000000000010000100100 # DIV.b\n0000100100000010 000000000010000000000000010000100100 # DIV.w\n0000100100000011 000000000010000000000000010000100100 # DIV.dw\n0000101000000000 000000000010000000000000010000001100 # IDIV\n0000101000000001 000000000010000000000000010000101100 # IDIV.b\n0000101000000010 000000000010000000000000010000101100 # IDIV.w\n0000101000000011 000000000010000000000000010000101100 # IDIV.dw\n00001011xxxxxxxx 000000000010000000000000010000000100 # NOT\n00001100xxxxxxxx 000000000010000000000000010101000100 # INC\n00001101xxxxxxxx 000000000010000000000000011010000100 # DEC\n00001110xxxxxxxx 000000000001000000010100000000000000 # PUSH\n00001111xxxxxxxx 000000000001100010010010010000000000 # POP\n00010000xxxxxxxx 000000010001010100010100000000000000 # CALL\n00010001xxxxxxxx 000000101001011100010100000000000000 # CALLR\n00010010xxxxxxxx 000000001001010100010100000000000000 # CLABS\n00010011xxxxxxxx 000000000001100010011000000000000000 # RET\n00010100xxxxxxxx 000000000010000000000000010000100100 # LSL\n00010101xxxxxxxx 000000000010000000000000010000100100 # LSR\n00010110xxxxxxxx 000000000010000000000000010000100100 # ASR\n00010111xxxxxxxx 000000000010000000000000010000100100 # ROL\n00011000xxxxxxxx 000000000010000000000000010000100100 # ROR\n0001100100000000 000000000010000000000000010000000100 # AND\n0001101000000000 000000000010000000000000010000000100 # OR\n0001101100000000 000000000010000000000000010000000100 # XOR\n0001110000000000 000000000010000000000000000000000100 # CMP\n0001110000000001 000000000010000000000000000000100100 # CMP.b\n0001110000000010 000000000010000000000000000000100100 # CMP.w\n0001110000000011 000000000010000000000000000000100100 # CMP.dw\n0001110100000000 000000000010000000000000000000001100 # ICMP\n0001110100000001 000000000010000000000000000000101100 # ICMP.b\n0001110100000010 000000000010000000000000000000101100 # ICMP.w\n0001110100000011 000000000010000000000000000000101100 # ICMP.dw\n00011110xxxxxxxx 000000010100000000000000000000000000 # JMP\n00011111xxxxxxxx 000000101100000000000000000000000000 # JMPR\n00100000xxxxxxxx 000000001100000000000000000000000000 # JMA\n0010000100000000 000000000000000000000000110000000000 # COPY\n0010000100000001 000000000000000000000001010000000000 # LDI.b\n0010000100000010 000000000000000000000001010000000000 # LDI.w\n0010000100000011 000000000000000000000001010000000000 # LDI.dw\n0010001000000000 000000000000000000000100000000100000 # STR.b F\n0010001000000001 000000000000000000100100000000000000 # STR.b S\n0010001000000010 000000000000000000000100000000000000 # STR.b R\n0010001000000011 000000000000000001100100000000000000 # STR.b SD\n0010001000000100 000000000000000001000100000000000000 # STR.b RD\n0010001000000101 000000000000000000000100000000100000 # STR.w F\n0010001000000110 000000000000000000100100000000000000 # STR.w S\n0010001000000111 000000000000000000000100000000000000 # STR.w R\n0010001000001000 000000000000000001100100000000000000 # STR.w SD\n0010001000001001 000000000000000001000100000000000000 # STR.w RD\n0010001000001010 000000000000000000000100000000100000 # STR.dw F\n0010001000001011 000000000000000000100100000000000000 # STR.dw S\n0010001000001100 000000000000000000000100000000000000 # STR.dw R\n0010001000001101 000000000000000001100100000000000000 # STR.dw SD\n0010001000001110 000000000000000001000100000000000000 # STR.dw RD\n0010001100000000 000000000000000010000010010000100000 # LOD.b F\n0010001100000001 000000000000000010100010010000000000 # LOD.b S\n0010001100000010 000000000000000010000010010000000000 # LOD.b R\n0010001100000011 000000000000000011100010010000000000 # LOD.b SD\n0010001100000100 000000000000000011000010010000000000 # LOD.b RD\n0010001100000101 000000000000000010000010010000100000 # LOD.w F\n0010001100000110 000000000000000010100010010000000000 # LOD.w S\n0010001100000111 000000000000000010000010010000000000 # LOD.w R\n0010001100001000 000000000000000011100010010000000000 # LOD.w SD\n0010001100001001 000000000000000011000010010000000000 # LOD.w RD\n0010001100001010 000000000000000010000010010000100000 # LOD.dw F\n0010001100001011 000000000000000010100010010000000000 # LOD.dw S\n0010001100001100 000000000000000010000010010000000000 # LOD.dw R\n0010001100001101 000000000000000011100010010000000000 # LOD.dw SD\n0010001100001110 000000000000000011000010010000000000 # LOD.dw RD\n00100101xxxxxxxx 010101001000000000000000000000000000 # INT\n00100110xxxxxxxx 001010000000000000000000000000000000 # IRET\n00100111xxxxxxxx 000100000000000000000000000000000000 # CLI\n00101000xxxxxxxx 001000000000000000000000000000000000 # STI\n0010100100000000 000000000010000000000000010000010100 # REM\n0010100100000001 000000000010000000000000010000110100 # REM.b\n0010100100000010 000000000010000000000000010000110100 # REM.w\n0010100100000011 000000000010000000000000010000110100 # REM.dw\n0010101000000000 000000000010000000000000010000011100 # IREM\n0010101000000001 000000000010000000000000010000111100 # IREM.b\n0010101000000010 000000000010000000000000010000111100 # IREM.w\n0010101000000011 000000000010000000000000010000111100 # IREM.dw")) CU (
    .in({INST_IN[63:56], pull_resistor_1_node}),
    .out({CU_out[35], RIDT, ENIRQ, DISIRQ, RETINT, CALLINT, INDB, RELB, ABSB, USEFL, UPDFL, UPDSP, DCSP, BSW2IMM, SPRINC, SPOUTIC, MOE, CNSDISP, USEC, RADDR2SP, SPWRIC, MWE, SMEM, SIMM, SREG, WREG, USEBR, USECR, CNSB, CNSC, SWB2I, SWD2R, SETSG, ALUEN, CU_out[1:0]}));
  Pull_Resistor pull_resistor_8 (.node(CU_out[0]));
  LED HALT_CLOCK (.in(CU_out[0]));
  Pull_Resistor pull_resistor_9 (.node(CU_out[1]));
  LED WAIT_UNTIL_IRQ (.in(CU_out[1]));
  Pull_Resistor pull_resistor_10 (.node(ALUEN));
  LED ALU_EN (.in(ALUEN));
  Pull_Resistor pull_resistor_11 (.node(SETSG));
  LED SET_SIGN (.in(SETSG));
  Pull_Resistor pull_resistor_12 (.node(SWD2R));
  LED SWITH_DIV2REM (.in(SWD2R));
  Pull_Resistor pull_resistor_13 (.node(SWB2I));
  LED SWITH_B2IMM (.in(SWB2I));
  Pull_Resistor pull_resistor_14 (.node(CNSC));
  LED CONSIDE_CARRY (.in(CNSC));
  Pull_Resistor pull_resistor_15 (.node(CNSB));
  LED CONSIDE_BORROW (.in(CNSB));
  Pull_Resistor pull_resistor_16 (.node(USECR));
  LED ANYWAY_USE_CARRY (.in(USECR));
  Pull_Resistor pull_resistor_17 (.node(USEBR));
  LED ANYWAY_USE_BORROW (.in(USEBR));
  Pull_Resistor pull_resistor_18 (.node(WREG));
  LED WE_REG (.in(WREG));
  Pull_Resistor pull_resistor_19 (.node(SREG));
  LED SET_REG (.in(SREG));
  Pull_Resistor pull_resistor_20 (.node(SIMM));
  LED SET_IMM (.in(SIMM));
  Pull_Resistor pull_resistor_21 (.node(SMEM));
  LED SET_MEM (.in(SMEM));
  Pull_Resistor pull_resistor_22 (.node(MWE));
  LED MEM_WE (.in(MWE));
  Pull_Resistor pull_resistor_23 (.node(SPWRIC));
  LED SP_WR_IC (.in(SPWRIC));
  Pull_Resistor pull_resistor_24 (.node(RADDR2SP));
  LED REP_ADDR2SP (.in(RADDR2SP));
  Pull_Resistor pull_resistor_25 (.node(USEC));
  LED USE_C (.in(USEC));
  Pull_Resistor pull_resistor_26 (.node(CNSDISP));
  LED CONSIDE_DISP (.in(CNSDISP));
  Pull_Resistor pull_resistor_27 (.node(MOE));
  LED MEM_OE (.in(MOE));
  Pull_Resistor pull_resistor_28 (.node(SPOUTIC));
  LED SP_OUT_IC (.in(SPOUTIC));
  Pull_Resistor pull_resistor_29 (.node(SPRINC));
  LED SP_REGINC (.in(SPRINC));
  Pull_Resistor pull_resistor_30 (.node(BSW2IMM));
  LED BRH_SWITCH_TO_IMM (.in(BSW2IMM));
  Pull_Resistor pull_resistor_31 (.node(DCSP));
  LED DECREMENT_SP (.in(DCSP));
  Pull_Resistor pull_resistor_32 (.node(UPDSP));
  LED UPDATE_SP (.in(UPDSP));
  Pull_Resistor pull_resistor_33 (.node(UPDFL));
  LED UPDATE_FLAGS (.in(UPDFL));
  Pull_Resistor pull_resistor_34 (.node(USEFL));
  LED USE_FLAGS (.in(USEFL));
  Pull_Resistor pull_resistor_35 (.node(ABSB));
  LED ABS_BRANCH (.in(ABSB));
  Pull_Resistor pull_resistor_36 (.node(RELB));
  LED REL_BRANCH (.in(RELB));
  Pull_Resistor pull_resistor_37 (.node(INDB));
  LED IND_BRANCH (.in(INDB));
  Pull_Resistor pull_resistor_38 (.node(CALLINT));
  LED CALL_INT (.in(CALLINT));
  Pull_Resistor pull_resistor_39 (.node(RETINT));
  LED RET_FROM_INT (.in(RETINT));
  Pull_Resistor pull_resistor_40 (.node(DISIRQ));
  LED DISABLE_IRQ (.in(DISIRQ));
  Pull_Resistor pull_resistor_41 (.node(ENIRQ));
  LED ENABLE_IRQ (.in(ENIRQ));
  Pull_Resistor pull_resistor_42 (.node(RIDT));
  LED READ_IDT (.in(RIDT));
  Pull_Resistor pull_resistor_43 (.node(CU_out[35]));
  LED WRITE_IDT (.in(CU_out[35]));
  Pull_Resistor pull_resistor_44 (.node({pull_resistor_44_node, LENGHT_out}));
  Multiplexer #(.width(8)) multiplexer_1 (
    .in0(pull_resistor_1_node), .in1(INT_IN), .out(multiplexer_1_out), .sel(CALL_IRQ));
  Pull_Resistor pull_resistor_45 (.node({pull_resistor_45_node, pull_resistor_1_node}));
  Pull_Resistor pull_resistor_46 (.node({pull_resistor_46_node, pull_resistor_1_node, pull_resistor_2_node}));
  Pull_Resistor pull_resistor_47 (.node({pull_resistor_47_node, pull_resistor_3_node}));
  Pull_Resistor pull_resistor_48 (.node({pull_resistor_48_node, pull_resistor_3_node, pull_resistor_4_node}));
  Pull_Resistor pull_resistor_49 (.node({pull_resistor_49_node, pull_resistor_2_node}));
  Register #(.width(32)) IDT (.D(multiplexer_12_out), .en(and_2_out), .clk(and_1_out), .Q(IDT_q), .clr(RESET));
  and and_2 (and_2_out, WREG, decoder_2_out36);
  Pull_Resistor pull_resistor_50 (.node({pull_resistor_50_node, pull_resistor_3_node, pull_resistor_4_node}));
  Pull_Resistor pull_resistor_51 (.node({pull_resistor_51_node, pull_resistor_3_node}));
  Pull_Resistor pull_resistor_52 (.node({pull_resistor_52_node, pull_resistor_5_node}));
  Pull_Resistor pull_resistor_53 (.node({pull_resistor_53_node, pull_resistor_5_node}));
  Pull_Resistor pull_resistor_54 (.node({pull_resistor_54_node, pull_resistor_4_node}));
  Pull_Resistor pull_resistor_55 (.node(pull_resistor_55_node));
  Pull_Resistor pull_resistor_56 (.node(pull_resistor_56_node));
  Pull_Resistor pull_resistor_57 (.node(pull_resistor_57_node));
  Pull_Resistor pull_resistor_58 (.node(pull_resistor_58_node));
  Pull_Resistor pull_resistor_59 (.node(pull_resistor_59_node));
  Pull_Resistor pull_resistor_60 (.node(pull_resistor_60_node));
  Pull_Resistor pull_resistor_61 (.node(pull_resistor_61_node));
  Pull_Resistor pull_resistor_62 (.node(pull_resistor_62_node));
  Pull_Resistor pull_resistor_63 (.node(pull_resistor_63_node));
  Pull_Resistor pull_resistor_64 (.node(pull_resistor_64_node));
  Pull_Resistor pull_resistor_65 (.node(pull_resistor_65_node));
  Pull_Resistor pull_resistor_66 (.node(pull_resistor_66_node));
  Pull_Resistor pull_resistor_67 (.node(pull_resistor_67_node));
  Pull_Resistor pull_resistor_68 (.node(pull_resistor_68_node));
  Pull_Resistor pull_resistor_69 (.node(pull_resistor_69_node));
  Pull_Resistor pull_resistor_70 (.node(pull_resistor_70_node));
  Pull_Resistor pull_resistor_71 (.node(pull_resistor_71_node));
  Pull_Resistor pull_resistor_72 (.node(pull_resistor_72_node));
  Pull_Resistor pull_resistor_73 (.node(pull_resistor_73_node));
  Pull_Resistor pull_resistor_74 (.node(pull_resistor_74_node));
  Pull_Resistor pull_resistor_75 (.node(pull_resistor_75_node));
  Pull_Resistor pull_resistor_76 (.node(pull_resistor_76_node));
  Pull_Resistor pull_resistor_77 (.node(pull_resistor_77_node));
  Pull_Resistor pull_resistor_78 (.node(pull_resistor_78_node));
  Pull_Resistor pull_resistor_79 (.node(pull_resistor_79_node));
  Pull_Resistor pull_resistor_80 (.node(pull_resistor_80_node));
  Pull_Resistor pull_resistor_81 (.node({pull_resistor_81_node, pull_resistor_4_node}));
  Pull_Resistor pull_resistor_82 (.node(pull_resistor_82_node));
  Pull_Resistor pull_resistor_83 (.node(pull_resistor_83_node));
  Pull_Resistor pull_resistor_84 (.node(pull_resistor_84_node));
  Pull_Resistor pull_resistor_85 (.node(pull_resistor_85_node));
  Pull_Resistor pull_resistor_86 (.node(pull_resistor_86_node));
  Pull_Resistor pull_resistor_87 (.node(pull_resistor_87_node));
  Pull_Resistor pull_resistor_88 (.node(pull_resistor_88_node));
  Pull_Resistor pull_resistor_89 (.node(pull_resistor_89_node));
  Pull_Resistor pull_resistor_90 (.node(pull_resistor_90_node));
  Pull_Resistor pull_resistor_91 (.node(pull_resistor_91_node));
  Pull_Resistor pull_resistor_92 (.node(pull_resistor_92_node));
  Pull_Resistor pull_resistor_93 (.node(pull_resistor_93_node));
  Pull_Resistor pull_resistor_94 (.node(pull_resistor_94_node));
  Pull_Resistor pull_resistor_95 (.node(pull_resistor_95_node));
  Pull_Resistor pull_resistor_96 (.node(pull_resistor_96_node));
  Pull_Resistor pull_resistor_97 (.node(pull_resistor_97_node));
  Pull_Resistor pull_resistor_98 (.node(pull_resistor_98_node));
  Pull_Resistor pull_resistor_99 (.node(pull_resistor_99_node));
  Pull_Resistor pull_resistor_100 (.node(pull_resistor_100_node));
  Pull_Resistor pull_resistor_101 (.node(pull_resistor_101_node));
  Pull_Resistor pull_resistor_102 (.node(pull_resistor_102_node));
  Pull_Resistor pull_resistor_103 (.node(pull_resistor_103_node));
  Pull_Resistor pull_resistor_104 (.node(pull_resistor_104_node));
  Pull_Resistor pull_resistor_105 (.node(pull_resistor_105_node));
  Pull_Resistor pull_resistor_106 (.node(pull_resistor_106_node));
  Pull_Resistor pull_resistor_107 (.node(pull_resistor_107_node));
  Pull_Resistor pull_resistor_108 (.node(pull_resistor_108_node));
  Pull_Resistor pull_resistor_109 (.node(pull_resistor_109_node));
  Pull_Resistor pull_resistor_110 (.node(pull_resistor_110_node));
  Pull_Resistor pull_resistor_111 (.node(pull_resistor_111_node));
  Pull_Resistor pull_resistor_112 (.node(pull_resistor_112_node));
  Pull_Resistor pull_resistor_113 (.node(pull_resistor_113_node));
  Pull_Resistor pull_resistor_114 (.node(pull_resistor_114_node));
  Pull_Resistor pull_resistor_115 (.node(pull_resistor_115_node));
  Pull_Resistor pull_resistor_116 (.node(pull_resistor_116_node));
  Pull_Resistor pull_resistor_117 (.node(pull_resistor_117_node));
  Pull_Resistor pull_resistor_118 (.node(pull_resistor_118_node));
  Pull_Resistor pull_resistor_119 (.node(pull_resistor_119_node));
  Pull_Resistor pull_resistor_120 (.node(pull_resistor_120_node));
  Pull_Resistor pull_resistor_121 (.node(pull_resistor_121_node));
  Pull_Resistor pull_resistor_122 (.node(pull_resistor_122_node));
  Pull_Resistor pull_resistor_123 (.node(pull_resistor_123_node));
  Pull_Resistor pull_resistor_124 (.node(pull_resistor_124_node));
  Pull_Resistor pull_resistor_125 (.node(pull_resistor_125_node));
  Pull_Resistor pull_resistor_126 (.node(pull_resistor_126_node));
  Pull_Resistor pull_resistor_127 (.node(pull_resistor_127_node));
  Pull_Resistor pull_resistor_128 (.node(pull_resistor_128_node));
  Pull_Resistor pull_resistor_129 (.node(pull_resistor_129_node));
  Pull_Resistor pull_resistor_130 (.node(pull_resistor_130_node));
  Pull_Resistor pull_resistor_131 (.node(pull_resistor_131_node));
  Pull_Resistor pull_resistor_132 (.node(pull_resistor_132_node));
  Pull_Resistor pull_resistor_133 (.node(pull_resistor_133_node));
  Pull_Resistor pull_resistor_134 (.node(pull_resistor_134_node));
  Pull_Resistor pull_resistor_135 (.node(pull_resistor_135_node));
  Pull_Resistor pull_resistor_136 (.node(pull_resistor_136_node));
  Pull_Resistor pull_resistor_137 (.node(pull_resistor_137_node));
  Pull_Resistor pull_resistor_138 (.node(pull_resistor_138_node));
  Pull_Resistor pull_resistor_139 (.node(pull_resistor_139_node));
  Pull_Resistor pull_resistor_140 (.node(pull_resistor_140_node));
  Pull_Resistor pull_resistor_141 (.node(pull_resistor_141_node));
  Pull_Resistor pull_resistor_142 (.node(pull_resistor_142_node));
  Pull_Resistor pull_resistor_143 (.node(pull_resistor_143_node));
  Pull_Resistor pull_resistor_144 (.node(pull_resistor_144_node));
  Pull_Resistor pull_resistor_145 (.node(pull_resistor_145_node));
  Pull_Resistor pull_resistor_146 (.node(pull_resistor_146_node));
  Pull_Resistor pull_resistor_147 (.node(pull_resistor_147_node));
  Pull_Resistor pull_resistor_148 (.node(pull_resistor_148_node));
  Pull_Resistor pull_resistor_149 (.node(pull_resistor_149_node));
  Pull_Resistor pull_resistor_150 (.node(pull_resistor_150_node));
  Pull_Resistor pull_resistor_151 (.node(pull_resistor_151_node));
  Pull_Resistor pull_resistor_152 (.node(pull_resistor_152_node));
  Pull_Resistor pull_resistor_153 (.node(pull_resistor_153_node));
  Pull_Resistor pull_resistor_154 (.node(pull_resistor_154_node));
  Pull_Resistor pull_resistor_155 (.node(pull_resistor_155_node));
  Pull_Resistor pull_resistor_156 (.node(pull_resistor_156_node));
  Multiplexer #(.select(5), .width(32)) multiplexer_2 (
    .in0(pull_resistor_55_node), .in1(pull_resistor_56_node), .in2(pull_resistor_57_node),
    .in3(pull_resistor_58_node), .in4({pull_resistor_45_node, pull_resistor_1_node}),
    .in5({pull_resistor_46_node, pull_resistor_1_node, pull_resistor_2_node}),
    .in6({pull_resistor_1_node, pull_resistor_2_node, pull_resistor_3_node, pull_resistor_4_node}),
    .in7(pull_resistor_59_node), .in8({pull_resistor_47_node, pull_resistor_3_node}),
    .in9({pull_resistor_48_node, pull_resistor_3_node, pull_resistor_4_node}),
    .in10({pull_resistor_3_node, pull_resistor_4_node, pull_resistor_5_node, pull_resistor_6_node}),
    .in11(pull_resistor_60_node), .in12(pull_resistor_61_node), .in13(pull_resistor_62_node),
    .in14({pull_resistor_49_node, pull_resistor_2_node}), .in15(pull_resistor_63_node),
    .in16({pull_resistor_51_node, pull_resistor_3_node}),
    .in17({pull_resistor_50_node, pull_resistor_3_node, pull_resistor_4_node}),
    .in18({pull_resistor_3_node, pull_resistor_4_node, pull_resistor_5_node, pull_resistor_6_node}),
    .in19({pull_resistor_3_node, pull_resistor_4_node, pull_resistor_5_node, pull_resistor_6_node}),
    .in20(pull_resistor_64_node), .in21(pull_resistor_65_node),
    .in22({pull_resistor_52_node, pull_resistor_5_node}),
    .in23({pull_resistor_54_node, pull_resistor_4_node}),
    .in24({pull_resistor_3_node, pull_resistor_4_node, pull_resistor_5_node, pull_resistor_6_node}),
    .in25(pull_resistor_66_node), .in26(pull_resistor_67_node),
    .in27({pull_resistor_53_node, pull_resistor_5_node}),
    .in28({pull_resistor_81_node, pull_resistor_4_node}), .in29(pull_resistor_68_node),
    .in30(pull_resistor_69_node), .in31(pull_resistor_70_node), .out(multiplexer_2_out),
    .sel(pla_1_out[15:11]));
  Multiplexer #(.select(5), .width(6)) multiplexer_3 (
    .in0(pull_resistor_71_node), .in1(pull_resistor_1_node[5:0]), .in2(pull_resistor_72_node),
    .in3(pull_resistor_1_node[5:0]), .in4(pull_resistor_73_node), .in5(pull_resistor_74_node),
    .in6(pull_resistor_75_node), .in7(pull_resistor_2_node[5:0]), .in8(pull_resistor_2_node[5:0]),
    .in9(pull_resistor_2_node[5:0]), .in10(pull_resistor_2_node[5:0]), .in11(pull_resistor_76_node),
    .in12(pull_resistor_77_node), .in13(pull_resistor_78_node), .in14(pull_resistor_1_node[5:0]),
    .in15(pull_resistor_2_node[5:0]), .in16(pull_resistor_2_node[5:0]), .in17(pull_resistor_2_node[5:0]),
    .in18(pull_resistor_2_node[5:0]), .in19(pull_resistor_79_node), .in20(pull_resistor_80_node),
    .in21(pull_resistor_82_node), .in22(pull_resistor_83_node), .in23(pull_resistor_84_node),
    .in24(pull_resistor_2_node[5:0]), .in25(pull_resistor_2_node[5:0]), .in26(pull_resistor_2_node[5:0]),
    .in27(pull_resistor_2_node[5:0]), .in28(pull_resistor_2_node[5:0]), .in29(pull_resistor_85_node),
    .in30(pull_resistor_86_node), .in31(pull_resistor_87_node), .out(multiplexer_3_out),
    .sel(pla_1_out[15:11]));
  Multiplexer #(.select(5), .width(6)) multiplexer_4 (
    .in0(pull_resistor_88_node), .in1(pull_resistor_89_node), .in2(pull_resistor_1_node[5:0]),
    .in3(pull_resistor_1_node[5:0]), .in4(pull_resistor_90_node), .in5(pull_resistor_91_node),
    .in6(pull_resistor_92_node), .in7(pull_resistor_2_node[5:0]), .in8(pull_resistor_2_node[5:0]),
    .in9(pull_resistor_2_node[5:0]), .in10(pull_resistor_2_node[5:0]), .in11(pull_resistor_93_node),
    .in12(pull_resistor_2_node[5:0]), .in13(pull_resistor_94_node), .in14(pull_resistor_1_node[5:0]),
    .in15(pull_resistor_3_node[5:0]), .in16(pull_resistor_95_node), .in17(pull_resistor_96_node),
    .in18(pull_resistor_97_node), .in19(pull_resistor_2_node[5:0]), .in20(pull_resistor_2_node[5:0]),
    .in21(pull_resistor_2_node[5:0]), .in22(pull_resistor_2_node[5:0]), .in23(pull_resistor_2_node[5:0]),
    .in24(pull_resistor_98_node), .in25(pull_resistor_99_node), .in26(pull_resistor_100_node),
    .in27(pull_resistor_101_node), .in28(pull_resistor_102_node), .in29(pull_resistor_103_node),
    .in30(pull_resistor_104_node), .in31(pull_resistor_105_node), .out(multiplexer_4_out),
    .sel(pla_1_out[15:11]));
  Multiplexer #(.select(5), .width(6)) multiplexer_5 (
    .in0(pull_resistor_106_node), .in1(pull_resistor_107_node), .in2(pull_resistor_108_node),
    .in3(pull_resistor_109_node), .in4(pull_resistor_110_node), .in5(pull_resistor_111_node),
    .in6(pull_resistor_112_node), .in7(pull_resistor_3_node[5:0]), .in8(pull_resistor_113_node),
    .in9(pull_resistor_114_node), .in10(pull_resistor_115_node), .in11(pull_resistor_116_node),
    .in12(pull_resistor_117_node), .in13(pull_resistor_118_node), .in14(pull_resistor_119_node),
    .in15(pull_resistor_120_node), .in16(pull_resistor_121_node), .in17(pull_resistor_122_node),
    .in18(pull_resistor_123_node), .in19(pull_resistor_124_node), .in20(pull_resistor_3_node[5:0]),
    .in21(pull_resistor_3_node[5:0]), .in22(pull_resistor_3_node[5:0]), .in23(pull_resistor_3_node[5:0]),
    .in24(pull_resistor_125_node), .in25(pull_resistor_3_node[5:0]), .in26(pull_resistor_3_node[5:0]),
    .in27(pull_resistor_3_node[5:0]), .in28(pull_resistor_3_node[5:0]), .in29(pull_resistor_126_node),
    .in30(pull_resistor_127_node), .in31(pull_resistor_128_node), .out(multiplexer_5_out),
    .sel(pla_1_out[15:11]));
  Multiplexer #(.select(5), .width(6)) multiplexer_6 (
    .in0(pull_resistor_129_node), .in1(pull_resistor_130_node), .in2(pull_resistor_131_node),
    .in3(pull_resistor_132_node), .in4(pull_resistor_133_node), .in5(pull_resistor_134_node),
    .in6(pull_resistor_135_node), .in7(pull_resistor_136_node), .in8(pull_resistor_137_node),
    .in9(pull_resistor_138_node), .in10(pull_resistor_139_node), .in11(pull_resistor_140_node),
    .in12(pull_resistor_141_node), .in13(pull_resistor_142_node), .in14(pull_resistor_143_node),
    .in15(pull_resistor_144_node), .in16(pull_resistor_145_node), .in17(pull_resistor_146_node),
    .in18(pull_resistor_147_node), .in19(pull_resistor_148_node), .in20(pull_resistor_4_node[5:0]),
    .in21(pull_resistor_149_node), .in22(pull_resistor_4_node[5:0]), .in23(pull_resistor_150_node),
    .in24(pull_resistor_151_node), .in25(pull_resistor_4_node[5:0]), .in26(pull_resistor_152_node),
    .in27(pull_resistor_4_node[5:0]), .in28(pull_resistor_153_node), .in29(pull_resistor_154_node),
    .in30(pull_resistor_155_node), .in31(pull_resistor_156_node), .out(multiplexer_6_out),
    .sel(pla_1_out[15:11]));
  Multiplexer #(.width(32)) multiplexer_7 (
    .in0({pull_resistor_2_node, pull_resistor_3_node, pull_resistor_4_node, pull_resistor_5_node}),
    .in1(multiplexer_2_out), .out(multiplexer_7_out), .sel(BSW2IMM));
  D_Flip_Flop INT_EN (.D(or_9_out), .clk(and_1_out), .Q(INT_EN_q), .Qn(IRQ_EN), .reset(or_10_out));  // open: preset
  or or_9 (or_9_out, INT_EN_q, DISIRQ);
  or or_10 (or_10_out, RESET, ENIRQ);
  Multiplexer #(.width(4)) multiplexer_8 (
    .in0(pull_resistor_1_node[3:0]), .in1(pull_resistor_1_node[3:0]), .out(multiplexer_8_out), .sel(INDB));
  and and_3 (and_3_out, IRQ_EN, CALL_IRQ);
  ROM #(.addrWidth(6), .dataWidth(3)) rom_1 (.addr(multiplexer_3_out), .data(rom_1_data));
  Demultiplexer #(.width(32)) demultiplexer_1 (
    .out0(demultiplexer_1_out0), .out1(demultiplexer_1_out1), .in(multiplexer_7_out), .sel(and_4_out));
  or or_11 (or_11_out, ABSB, and_3_out);
  or or_12 (or_12_out, CALLINT, and_3_out);
  Multiplexer #(.width(32)) multiplexer_9 (
    .in0(multiplexer_45_out), .in1(multiplexer_26_out), .out(multiplexer_9_out), .sel(SREG));
  Multiplexer #(.width(32)) multiplexer_10 (
    .in0(demultiplexer_1_out1), .in1(multiplexer_26_out), .out(multiplexer_10_out), .sel(INDB));
  Multiplexer #(.width(32)) multiplexer_11 (
    .in0(multiplexer_9_out), .in1(multiplexer_2_out), .out(multiplexer_11_out), .sel(SIMM));
  Multiplexer #(.width(32)) multiplexer_12 (
    .in0(multiplexer_11_out), .in1(DATA_IN), .out(multiplexer_12_out), .sel(SMEM));
  Adder #(.width(32)) adder_1 (
    .a({pull_resistor_44_node, LENGHT_out}), .b(demultiplexer_1_out0), .out(adder_1_out), .cin(RELB));  // open: cout
  Multiplexer #(.width(32)) multiplexer_13 (
    .in0(adder_2_out), .in1(multiplexer_14_out), .out(multiplexer_13_out), .sel(and_4_out));
  Multiplexer #(.width(32)) multiplexer_14 (
    .in0(multiplexer_10_out), .in1(DATA_IN), .out(multiplexer_14_out), .sel(or_12_out));
  and and_4 (and_4_out, or_11_out, multiplexer_18_out);
  Decoder #(.select(6)) decoder_2 (
    .out1(decoder_2_out1), .out2(decoder_2_out2), .out3(decoder_2_out3), .out4(decoder_2_out4),
    .out5(decoder_2_out5), .out6(decoder_2_out6), .out7(decoder_2_out7), .out8(decoder_2_out8),
    .out9(decoder_2_out9), .out10(decoder_2_out10), .out11(decoder_2_out11), .out12(decoder_2_out12),
    .out13(decoder_2_out13), .out14(decoder_2_out14), .out15(decoder_2_out15), .out16(decoder_2_out16),
    .out17(decoder_2_out17), .out18(decoder_2_out18), .out19(decoder_2_out19), .out20(decoder_2_out20),
    .out21(decoder_2_out21), .out23(decoder_2_out23), .out24(decoder_2_out24), .out25(decoder_2_out25),
    .out26(decoder_2_out26), .out27(decoder_2_out27), .out28(decoder_2_out28), .out29(decoder_2_out29),
    .out30(decoder_2_out30), .out31(decoder_2_out31), .out32(decoder_2_out32), .out33(decoder_2_out33),
    .out34(decoder_2_out34), .out35(decoder_2_out35), .out36(decoder_2_out36), .sel(multiplexer_3_out));  // open: out0, out22, out37, out38, out39, out40, out41, out42, out43, out44, out45, out46, out47, out48, out49, out50, out51, out52, out53, out54, out55, out56, out57, out58, out59, out60, out61, out62, out63, en
  Multiplexer #(.width(32)) multiplexer_15 (
    .in0(multiplexer_13_out), .in1(IC_BKUP_q), .out(multiplexer_15_out), .sel(RETINT));
  and and_5 (and_5_out, RELB, multiplexer_18_out);
  or or_13 (or_13_out, not_2_out, not_1_out);
  not not_1 (not_1_out, RELB);
  not not_2 (not_2_out, and_5_out);
  Adder #(.width(32)) adder_2 (.a(IC_OUT), .b(multiplexer_16_out), .out(adder_2_out), .cin(or_13_out));  // open: cout
  Multiplexer #(.width(32)) multiplexer_16 (
    .in0({pull_resistor_44_node, LENGHT_out}), .in1(adder_1_out), .out(multiplexer_16_out), .sel(and_5_out));
  Register #(.width(32)) IC (.D(multiplexer_17_out), .clk(and_1_out), .Q(IC_OUT), .clr(RESET));  // open: en
  Multiplexer #(.width(32)) multiplexer_17 (
    .in0(multiplexer_15_out), .in1(DATA_IN), .out(multiplexer_17_out), .sel(SPWRIC));
  Pull_Resistor pull_resistor_157 (.node(pull_resistor_157_node));
  assign pull_resistor_157_node = USEFL ? multiplexer_8_out : 4'bz;  // Controlled_Buffer controlled_buffer_8
  Multiplexer #(.select(4)) multiplexer_18 (
    .in0(pull_resistor_158_node), .in1(FLAGS_OUT[0]), .in2(FLAGS_OUT[1]), .in3(FLAGS_OUT[2]),
    .in4(FLAGS_OUT[3]), .in5(FLAGS_OUT[4]), .in6(not_3_out), .in7(FLAGS_OUT[5]), .in8(or_14_out),
    .in9(FLAGS_OUT[7]), .in10(or_15_out), .in11(FLAGS_OUT[6]), .in12(not_4_out),
    .in13(pull_resistor_159_node), .in14(pull_resistor_159_node), .in15(pull_resistor_159_node),
    .out(multiplexer_18_out), .sel(pull_resistor_157_node));
  Pull_Resistor #(.pull(1)) pull_resistor_158 (.node(pull_resistor_158_node));
  not not_3 (not_3_out, FLAGS_OUT[4]);
  or or_14 (or_14_out, FLAGS_OUT[5], FLAGS_OUT[6]);
  or or_15 (or_15_out, FLAGS_OUT[7], FLAGS_OUT[6]);
  not not_4 (not_4_out, FLAGS_OUT[6]);
  Pull_Resistor pull_resistor_159 (.node(pull_resistor_159_node));
  Register #(.width(32)) IC_BKUP (.D(multiplexer_19_out), .en(or_12_out), .clk(and_1_out), .Q(IC_BKUP_q), .clr(RESET));
  Multiplexer #(.width(32)) multiplexer_19 (.in0(adder_3_out), .in1(IC_OUT), .out(multiplexer_19_out), .sel(and_3_out));
  Adder #(.width(32)) adder_3 (.a(32'h2), .b(IC_OUT), .out(adder_3_out));  // open: cin, cout
  and and_6 (and_6_out, WREG, or_16_out);
  or or_16 (or_16_out, decoder_2_out15, decoder_2_out8, decoder_2_out1);
  and and_7 (and_7_out, WREG, or_17_out);
  or or_17 (or_17_out, decoder_2_out8, decoder_2_out1);
  and and_8 (and_8_out, WREG, decoder_2_out1);
  and and_9 (and_9_out, WREG, decoder_2_out26);
  and and_10 (and_10_out, WREG, decoder_2_out27);
  assign not_5_out = ~32'h4;  // NOT_Gate not_5, 32 bits wide
  Register XL1 (.D(multiplexer_12_out[7:0]), .en(and_6_out), .clk(and_1_out), .Q(XL1_q), .clr(RESET));
  Register X1 (.D(multiplexer_12_out[15:8]), .en(and_7_out), .clk(and_1_out), .Q(X1_q), .clr(RESET));
  Register #(.width(16)) EX1 (.D(multiplexer_12_out[31:16]), .en(and_8_out), .clk(and_1_out), .Q(EX1_q), .clr(RESET));
  Register #(.width(32)) IX (.D(multiplexer_12_out), .en(and_9_out), .clk(and_1_out), .Q(IX_q), .clr(RESET));
  Register #(.width(32)) IY (.D(multiplexer_12_out), .en(and_10_out), .clk(and_1_out), .Q(IY_q), .clr(RESET));
  Adder #(.width(32)) adder_4 (.a(SP_q), .b(multiplexer_20_out), .out(adder_4_out), .cin(DCSP));  // open: cout
  Multiplexer #(.width(32)) multiplexer_20 (.in0(32'h4), .in1(not_5_out), .out(multiplexer_20_out), .sel(DCSP));
  or or_18 (or_18_out, decoder_2_out16, decoder_2_out9, decoder_2_out2);
  or or_19 (or_19_out, decoder_2_out9, decoder_2_out2);
  Register #(.width(32)) SP (.D(multiplexer_21_out), .en(or_20_out), .clk(and_1_out), .Q(SP_q), .clr(RESET));
  Multiplexer #(.width(32)) multiplexer_21 (
    .in0(adder_4_out), .in1(multiplexer_12_out), .out(multiplexer_21_out), .sel(decoder_2_out24));
  and and_11 (and_11_out, decoder_2_out24, WREG);
  or or_20 (or_20_out, and_11_out, UPDSP);
  Register XL2 (.D(multiplexer_12_out[7:0]), .en(and_12_out), .clk(and_1_out), .Q(XL2_q), .clr(RESET));
  and and_12 (and_12_out, WREG, or_18_out);
  Register X2 (.D(multiplexer_12_out[15:8]), .en(and_13_out), .clk(and_1_out), .Q(X2_q), .clr(RESET));
  and and_13 (and_13_out, WREG, or_19_out);
  Register #(.width(16)) EX2 (.D(multiplexer_12_out[31:16]), .en(and_14_out), .clk(and_1_out), .Q(EX2_q), .clr(RESET));
  and and_14 (and_14_out, WREG, decoder_2_out2);
  Register #(.width(32)) A0 (.D(multiplexer_12_out), .en(and_15_out), .clk(and_1_out), .Q(A0_q), .clr(RESET));
  and and_15 (and_15_out, WREG, decoder_2_out28);
  Register #(.width(32)) A4 (.D(multiplexer_12_out), .en(and_16_out), .clk(and_1_out), .Q(A4_q), .clr(RESET));
  and and_16 (and_16_out, WREG, decoder_2_out32);
  assign and_17_out = {multiplexer_46_out, multiplexer_42_out} & pla_1_out[10:3];  // AND_Gate and_17, 8 bits wide
  assign and_18_out = ~pla_1_out[10:3] & FLAGS_OUT;  // AND_Gate and_18, 8 bits wide
  Register FLAGS (.D(multiplexer_22_out), .en(or_22_out), .clk(and_1_out), .Q(FLAGS_OUT), .clr(RESET));
  assign or_21_out = and_17_out | and_18_out;  // OR_Gate or_21, 8 bits wide
  Multiplexer #(.width(8)) multiplexer_22 (
    .in0(or_21_out), .in1(multiplexer_12_out[7:0]), .out(multiplexer_22_out), .sel(decoder_2_out23));
  and and_19 (and_19_out, decoder_2_out23, WREG);
  or or_22 (or_22_out, and_19_out, UPDFL);
  and and_20 (and_20_out, WREG, or_23_out);
  or or_23 (or_23_out, decoder_2_out17, decoder_2_out10, decoder_2_out3);
  and and_21 (and_21_out, WREG, or_24_out);
  or or_24 (or_24_out, decoder_2_out10, decoder_2_out3);
  and and_22 (and_22_out, WREG, decoder_2_out3);
  and and_23 (and_23_out, WREG, decoder_2_out29);
  and and_24 (and_24_out, WREG, decoder_2_out33);
  Register XL3 (.D(multiplexer_12_out[7:0]), .en(and_20_out), .clk(and_1_out), .Q(XL3_q), .clr(RESET));
  Register X3 (.D(multiplexer_12_out[15:8]), .en(and_21_out), .clk(and_1_out), .Q(X3_q), .clr(RESET));
  Register #(.width(16)) EX3 (.D(multiplexer_12_out[31:16]), .en(and_22_out), .clk(and_1_out), .Q(EX3_q), .clr(RESET));
  Register #(.width(32)) A1 (.D(multiplexer_12_out), .en(and_23_out), .clk(and_1_out), .Q(A1_q), .clr(RESET));
  Register #(.width(32)) A5 (.D(multiplexer_12_out), .en(and_24_out), .clk(and_1_out), .Q(A5_q), .clr(RESET));
  Subtractor #(.width(32)) subtractor_1 (.a(SP_q), .b(32'h4), .out(subtractor_1_out));  // open: bin, bout
  Multiplexer #(.width(32)) multiplexer_23 (.in0(SP_q), .in1(subtractor_1_out), .out(multiplexer_23_out), .sel(DCSP));
  or or_25 (or_25_out, decoder_2_out18, decoder_2_out11, decoder_2_out4);
  or or_26 (or_26_out, decoder_2_out11, decoder_2_out4);
  Register XL4 (.D(multiplexer_12_out[7:0]), .en(and_25_out), .clk(and_1_out), .Q(XL4_q), .clr(RESET));
  and and_25 (and_25_out, WREG, or_25_out);
  Register X4 (.D(multiplexer_12_out[15:8]), .en(and_26_out), .clk(and_1_out), .Q(X4_q), .clr(RESET));
  and and_26 (and_26_out, WREG, or_26_out);
  Register #(.width(16)) EX4 (.D(multiplexer_12_out[31:16]), .en(and_27_out), .clk(and_1_out), .Q(EX4_q), .clr(RESET));
  and and_27 (and_27_out, WREG, decoder_2_out4);
  Register #(.width(32)) A2 (.D(multiplexer_12_out), .en(and_28_out), .clk(and_1_out), .Q(A2_q), .clr(RESET));
  and and_28 (and_28_out, WREG, decoder_2_out30);
  Register #(.width(32)) A6 (.D(multiplexer_12_out), .en(and_29_out), .clk(and_1_out), .Q(A6_q), .clr(RESET));
  and and_29 (and_29_out, WREG, decoder_2_out34);
  Comparator #(.width(3)) comparator_1 (.a(pla_1_out[2:0]), .b(3'b100), .eq(comparator_1_eq));  // open: gt, lt
  Multiplexer #(.width(3)) multiplexer_24 (
    .in0(pla_1_out[2:0]), .in1(rom_1_data), .out(multiplexer_24_out), .sel(comparator_1_eq));
  or or_27 (or_27_out, decoder_2_out19, decoder_2_out12, decoder_2_out5);
  or or_28 (or_28_out, decoder_2_out12, decoder_2_out5);
  Register XL5 (.D(multiplexer_12_out[7:0]), .en(and_30_out), .clk(and_1_out), .Q(XL5_q), .clr(RESET));
  and and_30 (and_30_out, WREG, or_27_out);
  Register X5 (.D(multiplexer_12_out[15:8]), .en(and_31_out), .clk(and_1_out), .Q(X5_q), .clr(RESET));
  and and_31 (and_31_out, WREG, or_28_out);
  Register #(.width(16)) EX5 (.D(multiplexer_12_out[31:16]), .en(and_32_out), .clk(and_1_out), .Q(EX5_q), .clr(RESET));
  and and_32 (and_32_out, WREG, decoder_2_out5);
  Register #(.width(32)) A3 (.D(multiplexer_12_out), .en(and_33_out), .clk(and_1_out), .Q(A3_q), .clr(RESET));
  and and_33 (and_33_out, WREG, decoder_2_out31);
  Register #(.width(32)) A7 (.D(multiplexer_12_out), .en(and_34_out), .clk(and_1_out), .Q(A7_q), .clr(RESET));
  and and_34 (and_34_out, WREG, decoder_2_out35);
  and and_35 (and_35_out, WREG, or_29_out);
  or or_29 (or_29_out, decoder_2_out20, decoder_2_out13, decoder_2_out6);
  and and_36 (and_36_out, WREG, or_30_out);
  or or_30 (or_30_out, decoder_2_out13, decoder_2_out6);
  and and_37 (and_37_out, WREG, decoder_2_out6);
  and and_38 (and_38_out, WREG, decoder_2_out25);
  Register XL6 (.D(multiplexer_12_out[7:0]), .en(and_35_out), .clk(and_1_out), .Q(XL6_q), .clr(RESET));
  Register X6 (.D(multiplexer_12_out[15:8]), .en(and_36_out), .clk(and_1_out), .Q(X6_q), .clr(RESET));
  Register #(.width(16)) EX6 (.D(multiplexer_12_out[31:16]), .en(and_37_out), .clk(and_1_out), .Q(EX6_q), .clr(RESET));
  Register #(.width(32)) BP (.D(multiplexer_12_out), .en(and_38_out), .clk(and_1_out), .Q(BP_q), .clr(RESET));
  Pull_Resistor pull_resistor_160 (.node({pull_resistor_160_node, X1_q, XL1_q}));
  Pull_Resistor pull_resistor_161 (.node({pull_resistor_161_node, X2_q, XL2_q}));
  Pull_Resistor pull_resistor_162 (.node({pull_resistor_162_node, X3_q, XL3_q}));
  Pull_Resistor pull_resistor_163 (.node({pull_resistor_163_node, X4_q, XL4_q}));
  Pull_Resistor pull_resistor_164 (.node({pull_resistor_164_node, X5_q, XL5_q}));
  Pull_Resistor pull_resistor_165 (.node({pull_resistor_165_node, X6_q, XL6_q}));
  Pull_Resistor pull_resistor_166 (.node({pull_resistor_166_node_2, pull_resistor_166_node, pull_resistor_166_node_3}));
  Pull_Resistor pull_resistor_167 (.node({pull_resistor_167_node, XL1_q}));
  Pull_Resistor pull_resistor_168 (.node({pull_resistor_168_node, XL2_q}));
  Pull_Resistor pull_resistor_169 (.node({pull_resistor_169_node, XL3_q}));
  Pull_Resistor pull_resistor_170 (.node({pull_resistor_170_node, XL4_q}));
  Pull_Resistor pull_resistor_171 (.node({pull_resistor_171_node, XL5_q}));
  Pull_Resistor pull_resistor_172 (.node({pull_resistor_172_node, XL6_q}));
  Pull_Resistor pull_resistor_173 (.node({pull_resistor_173_node, pull_resistor_166_node_3}));
  or or_31 (or_31_out, decoder_2_out21, decoder_2_out14, decoder_2_out7);
  or or_32 (or_32_out, decoder_2_out14, decoder_2_out7);
  Register XL7 (
    .D(multiplexer_12_out[7:0]), .en(and_39_out), .clk(and_1_out), .Q(pull_resistor_166_node_3), .clr(RESET));
  and and_39 (and_39_out, WREG, or_31_out);
  Register X7 (.D(multiplexer_12_out[15:8]), .en(and_40_out), .clk(and_1_out), .Q(pull_resistor_166_node), .clr(RESET));
  and and_40 (and_40_out, WREG, or_32_out);
  Register #(.width(16)) EX7 (.D(multiplexer_12_out[31:16]), .en(and_41_out), .clk(and_1_out), .Q(EX7_q), .clr(RESET));
  and and_41 (and_41_out, WREG, decoder_2_out7);
  Multiplexer #(.width(32)) multiplexer_25 (.in0(32'h5), .in1(32'h2), .out(multiplexer_25_out), .sel(SPRINC));
  Pull_Resistor pull_resistor_174 (.node(pull_resistor_174_node));
  Pull_Resistor pull_resistor_175 (.node({pull_resistor_175_node, FLAGS_OUT}));
  Adder #(.width(32)) adder_5 (.a(multiplexer_25_out), .b(IC_OUT), .out(adder_5_out));  // open: cin, cout
  Pull_Resistor pull_resistor_176 (.node(pull_resistor_176_node));
  Multiplexer #(.select(6), .width(32)) multiplexer_26 (
    .in0(pull_resistor_174_node), .in1({EX1_q, X1_q, XL1_q}), .in2({EX2_q, X2_q, XL2_q}),
    .in3({EX3_q, X3_q, XL3_q}), .in4({EX4_q, X4_q, XL4_q}), .in5({EX5_q, X5_q, XL5_q}),
    .in6({EX6_q, X6_q, XL6_q}), .in7({EX7_q, pull_resistor_166_node, pull_resistor_166_node_3}),
    .in8({pull_resistor_160_node, X1_q, XL1_q}), .in9({pull_resistor_161_node, X2_q, XL2_q}),
    .in10({pull_resistor_162_node, X3_q, XL3_q}), .in11({pull_resistor_163_node, X4_q, XL4_q}),
    .in12({pull_resistor_164_node, X5_q, XL5_q}), .in13({pull_resistor_165_node, X6_q, XL6_q}),
    .in14({pull_resistor_166_node_2, pull_resistor_166_node, pull_resistor_166_node_3}),
    .in15({pull_resistor_167_node, XL1_q}), .in16({pull_resistor_168_node, XL2_q}),
    .in17({pull_resistor_169_node, XL3_q}), .in18({pull_resistor_170_node, XL4_q}),
    .in19({pull_resistor_171_node, XL5_q}), .in20({pull_resistor_172_node, XL6_q}),
    .in21({pull_resistor_173_node, pull_resistor_166_node_3}), .in22(IC_OUT),
    .in23({pull_resistor_175_node, FLAGS_OUT}), .in24(multiplexer_23_out), .in25(BP_q), .in26(IX_q),
    .in27(IY_q), .in28(A0_q), .in29(A1_q), .in30(A2_q), .in31(A3_q), .in32(A4_q), .in33(A5_q), .in34(A6_q),
    .in35(A7_q), .in36(IDT_q), .out(multiplexer_26_out), .sel(multiplexer_4_out));  // open: in37, in38, in39, in40, in41, in42, in43, in44, in45, in46, in47, in48, in49, in50, in51, in52, in53, in54, in55, in56, in57, in58, in59, in60, in61, in62, in63
  Pull_Resistor pull_resistor_177 (.node(pull_resistor_177_node));
  Multiplexer #(.select(6), .width(32)) multiplexer_27 (
    .in0(pull_resistor_176_node), .in1({EX1_q, X1_q, XL1_q}), .in2({EX2_q, X2_q, XL2_q}),
    .in3({EX3_q, X3_q, XL3_q}), .in4({EX4_q, X4_q, XL4_q}), .in5({EX5_q, X5_q, XL5_q}),
    .in6({EX6_q, X6_q, XL6_q}), .in7({EX7_q, pull_resistor_166_node, pull_resistor_166_node_3}),
    .in8({pull_resistor_160_node, X1_q, XL1_q}), .in9({pull_resistor_161_node, X2_q, XL2_q}),
    .in10({pull_resistor_162_node, X3_q, XL3_q}), .in11({pull_resistor_163_node, X4_q, XL4_q}),
    .in12({pull_resistor_164_node, X5_q, XL5_q}), .in13({pull_resistor_165_node, X6_q, XL6_q}),
    .in14({pull_resistor_166_node_2, pull_resistor_166_node, pull_resistor_166_node_3}),
    .in15({pull_resistor_167_node, XL1_q}), .in16({pull_resistor_168_node, XL2_q}),
    .in17({pull_resistor_169_node, XL3_q}), .in18({pull_resistor_170_node, XL4_q}),
    .in19({pull_resistor_171_node, XL5_q}), .in20({pull_resistor_172_node, XL6_q}),
    .in21({pull_resistor_173_node, pull_resistor_166_node_3}), .in22(IC_OUT),
    .in23({pull_resistor_175_node, FLAGS_OUT}), .in24(multiplexer_23_out), .in25(BP_q), .in26(IX_q),
    .in27(IY_q), .in28(A0_q), .in29(A1_q), .in30(A2_q), .in31(A3_q), .in32(A4_q), .in33(A5_q), .in34(A6_q),
    .in35(A7_q), .in36(IDT_q), .out(multiplexer_27_out), .sel(multiplexer_5_out));  // open: in37, in38, in39, in40, in41, in42, in43, in44, in45, in46, in47, in48, in49, in50, in51, in52, in53, in54, in55, in56, in57, in58, in59, in60, in61, in62, in63
  assign not_6_out = ~multiplexer_24_out[1:0];  // NOT_Gate not_6, 2 bits wide
  Decoder #(.select(2)) decoder_3 (
    .out1(LE0), .out2(decoder_3_out2), .out3(decoder_3_out3), .sel(not_6_out));  // open: out0, en
  Multiplexer #(.width(32)) multiplexer_28 (.in0(multiplexer_26_out), .in1(adder_5_out), .out(DATA_OUT), .sel(SPOUTIC));
  Multiplexer #(.select(6), .width(32)) multiplexer_29 (
    .in0(pull_resistor_177_node), .in1({EX1_q, X1_q, XL1_q}), .in2({EX2_q, X2_q, XL2_q}),
    .in3({EX3_q, X3_q, XL3_q}), .in4({EX4_q, X4_q, XL4_q}), .in5({EX5_q, X5_q, XL5_q}),
    .in6({EX6_q, X6_q, XL6_q}), .in7({EX7_q, pull_resistor_166_node, pull_resistor_166_node_3}),
    .in8({pull_resistor_160_node, X1_q, XL1_q}), .in9({pull_resistor_161_node, X2_q, XL2_q}),
    .in10({pull_resistor_162_node, X3_q, XL3_q}), .in11({pull_resistor_163_node, X4_q, XL4_q}),
    .in12({pull_resistor_164_node, X5_q, XL5_q}), .in13({pull_resistor_165_node, X6_q, XL6_q}),
    .in14({pull_resistor_166_node_2, pull_resistor_166_node, pull_resistor_166_node_3}),
    .in15({pull_resistor_167_node, XL1_q}), .in16({pull_resistor_168_node, XL2_q}),
    .in17({pull_resistor_169_node, XL3_q}), .in18({pull_resistor_170_node, XL4_q}),
    .in19({pull_resistor_171_node, XL5_q}), .in20({pull_resistor_172_node, XL6_q}),
    .in21({pull_resistor_173_node, pull_resistor_166_node_3}), .in22(IC_OUT),
    .in23({pull_resistor_175_node, FLAGS_OUT}), .in24(multiplexer_23_out), .in25(BP_q), .in26(IX_q),
    .in27(IY_q), .in28(A0_q), .in29(A1_q), .in30(A2_q), .in31(A3_q), .in32(A4_q), .in33(A5_q), .in34(A6_q),
    .in35(A7_q), .in36(IDT_q), .out(multiplexer_29_out), .sel(multiplexer_6_out));  // open: in37, in38, in39, in40, in41, in42, in43, in44, in45, in46, in47, in48, in49, in50, in51, in52, in53, in54, in55, in56, in57, in58, in59, in60, in61, in62, in63
  Multiplexer #(.width(32)) multiplexer_30 (
    .in0(multiplexer_27_out), .in1(multiplexer_2_out), .out(multiplexer_30_out), .sel(SWB2I));
  PLA #(.in_width(8), .out_width(4), .\table ("00000011 0000 # ADD\n00000100 0000 # ADC\n00000101 0001 # SUB\n00000110 0001 # SBB\n00000111 0010 # MUL\n00001000 0010 # IMUL\n00001001 0011 # DIV\n00001010 0011 # IDIV\n00101001 0011 # REM\n00101010 0011 # IREM\n00011001 0100 # AND\n00011010 0101 # OR\n00011011 0110 # XOR\n00001011 0111 # NOT\n00001100 0000 # INC\n00001101 0001 # DEC\n00011100 0001 # CMP\n00011101 0001 # ICMP\n00010100 1000 # LSL\n00010101 1001 # LSR\n00010110 1010 # ASR\n00010111 1011 # ROL\n00011000 1100 # ROR")) pla_2 (
    .in(INST_IN[63:56]), .out(pla_2_out));
  assign bit_extender_1_out = {{24{multiplexer_2_out[7]}}, multiplexer_2_out[7:0]};  // Bit_Extender bit_extender_1
  or or_33 (LE2, LE0, decoder_3_out2);
  or or_34 (or_34_out, FLAGS_OUT[1], USEBR);
  and and_42 (and_42_out, CNSB, or_34_out);
  Pull_Resistor pull_resistor_178 (.node(pull_resistor_178_node));
  assign pull_resistor_178_node = USEC ? multiplexer_29_out : 32'bz;  // Controlled_Buffer controlled_buffer_9
  Pull_Resistor pull_resistor_179 (.node({pull_resistor_179_node, multiplexer_1_out}));
  Shifter #(.width(32)) shifter_1 (
    .in({pull_resistor_179_node, multiplexer_1_out}), .\dist (5'b00010), .out(shifter_1_out));
  or or_35 (LE3, LE2, decoder_3_out3);
  or or_36 (or_36_out, FLAGS_OUT[0], USECR);
  and and_43 (and_43_out, CNSC, or_36_out);
  Adder #(.width(32)) adder_6 (
    .a(multiplexer_26_out), .b(multiplexer_30_out), .out(adder_6_out), .cin(and_43_out), .cout(adder_6_cout));
  Subtractor #(.width(32)) subtractor_2 (
    .a(multiplexer_26_out), .b(multiplexer_30_out), .out(subtractor_2_out), .bin(and_42_out),
    .bout(subtractor_2_bout));
  Multiplier #(.width(32)) multiplier_1 (
    .a(multiplexer_26_out), .b(multiplexer_30_out), .out(multiplier_1_out));  // open: cin, cout
  Multiplier #(.mode("twosComplement"), .width(32)) multiplier_2 (
    .a(multiplexer_26_out), .b(multiplexer_30_out), .out(multiplier_2_out));  // open: cin, cout
  Divider #(.width(32)) divider_1 (
    .a(multiplexer_26_out), .b(multiplexer_30_out), .out(divider_1_out), .rem(divider_1_rem));  // open: upper
  Divider #(.mode("twosComplement"), .width(32)) divider_2 (
    .a(multiplexer_26_out), .b(multiplexer_30_out), .out(divider_2_out), .rem(divider_2_rem));  // open: upper
  assign not_7_out = ~multiplexer_26_out;  // NOT_Gate not_7, 32 bits wide
  assign and_44_out = multiplexer_26_out & multiplexer_30_out;  // AND_Gate and_44, 32 bits wide
  assign or_37_out = multiplexer_26_out | multiplexer_30_out;  // OR_Gate or_37, 32 bits wide
  assign xor_1_out = multiplexer_26_out ^ multiplexer_30_out;  // XOR_Gate xor_1, 32 bits wide
  Shifter #(.width(32)) shifter_2 (.in(multiplexer_26_out), .\dist (multiplexer_30_out[4:0]), .out(shifter_2_out));
  Shifter #(.shift("lr"), .width(32)) shifter_3 (
    .in(multiplexer_26_out), .\dist (multiplexer_30_out[4:0]), .out(shifter_3_out));
  Shifter #(.shift("ar"), .width(32)) shifter_4 (
    .in(multiplexer_26_out), .\dist (multiplexer_30_out[4:0]), .out(shifter_4_out));
  Shifter #(.shift("rl"), .width(32)) shifter_5 (
    .in(multiplexer_26_out), .\dist (multiplexer_30_out[4:0]), .out(shifter_5_out));
  Shifter #(.shift("rr"), .width(32)) shifter_6 (
    .in(multiplexer_26_out), .\dist (multiplexer_30_out[4:0]), .out(shifter_6_out));
  Comparator #(.mode("unsigned")) comparator_2 (
    .a(multiplexer_26_out[7:0]), .b(multiplexer_30_out[7:0]), .gt(comparator_2_gt[0]),
    .eq(comparator_2_gt[1]), .lt(comparator_2_gt[2]));
  Comparator #(.mode("unsigned"), .width(16)) comparator_3 (
    .a(multiplexer_26_out[15:0]), .b(multiplexer_30_out[15:0]), .gt(comparator_3_gt[0]),
    .eq(comparator_3_gt[1]), .lt(comparator_3_gt[2]));
  Comparator #(.mode("unsigned"), .width(32)) comparator_4 (
    .a(multiplexer_26_out), .b(multiplexer_30_out), .gt(comparator_4_gt[0]), .eq(comparator_4_gt[1]),
    .lt(comparator_4_gt[2]));
  Comparator comparator_5 (
    .a(multiplexer_26_out[7:0]), .b(multiplexer_30_out[7:0]), .gt(comparator_5_gt[0]),
    .eq(comparator_5_gt[1]), .lt(comparator_5_gt[2]));
  Comparator #(.width(16)) comparator_6 (
    .a(multiplexer_26_out[15:0]), .b(multiplexer_30_out[15:0]), .gt(comparator_6_gt[0]),
    .eq(comparator_6_gt[1]), .lt(comparator_6_gt[2]));
  Comparator #(.width(32)) comparator_7 (
    .a(multiplexer_26_out), .b(multiplexer_30_out), .gt(comparator_7_gt[0]), .eq(comparator_7_gt[1]),
    .lt(comparator_7_gt[2]));
  Adder #(.width(32)) adder_7 (
    .a(multiplexer_30_out), .b(pull_resistor_178_node), .out(adder_7_out));  // open: cin, cout
  Adder #(.width(32)) adder_8 (.a(adder_7_out), .b(pull_resistor_180_node), .out(adder_8_out));  // open: cin, cout
  Pull_Resistor pull_resistor_180 (.node(pull_resistor_180_node));
  assign pull_resistor_180_node = CNSDISP ? bit_extender_1_out : 32'bz;  // Controlled_Buffer controlled_buffer_10
  Adder #(.width(32)) adder_9 (.a(IDT_q), .b(shifter_1_out), .out(adder_9_out));  // open: cin, cout
  Multiplexer multiplexer_31 (
    .in0(subtractor_2_out[8]), .in1(subtractor_2_out[16]), .out(multiplexer_31_out),
    .sel(multiplexer_24_out[0]));
  Multiplexer multiplexer_32 (
    .in0(adder_6_out[8]), .in1(adder_6_out[16]), .out(multiplexer_32_out), .sel(multiplexer_24_out[0]));
  Multiplexer #(.width(32)) multiplexer_33 (
    .in0(multiplier_1_out), .in1(multiplier_2_out), .out(multiplexer_33_out), .sel(SETSG));
  Multiplexer #(.width(32)) multiplexer_34 (
    .in0(divider_1_out), .in1(divider_2_out), .out(multiplexer_34_out), .sel(SETSG));
  Multiplexer #(.width(32)) multiplexer_35 (
    .in0(multiplexer_34_out), .in1(multiplexer_36_out), .out(multiplexer_35_out), .sel(SWD2R));
  Multiplexer #(.width(32)) multiplexer_36 (
    .in0(divider_1_rem), .in1(divider_2_rem), .out(multiplexer_36_out), .sel(SETSG));
  Multiplexer #(.width(3)) multiplexer_37 (
    .in0(comparator_2_gt), .in1(comparator_5_gt), .out(multiplexer_37_out), .sel(SETSG));
  Multiplexer #(.width(3)) multiplexer_38 (
    .in0(comparator_3_gt), .in1(comparator_6_gt), .out(multiplexer_38_out), .sel(SETSG));
  Multiplexer #(.width(3)) multiplexer_39 (
    .in0(comparator_4_gt), .in1(comparator_7_gt), .out(multiplexer_39_out), .sel(SETSG));
  Multiplexer #(.width(32)) multiplexer_40 (
    .in0(adder_8_out), .in1(multiplexer_23_out), .out(multiplexer_40_out), .sel(RADDR2SP));
  Multiplexer multiplexer_41 (
    .in0(multiplexer_31_out), .in1(subtractor_2_bout), .out(multiplexer_42_out[1]),
    .sel(multiplexer_24_out[1]));
  Multiplexer multiplexer_42 (
    .in0(multiplexer_32_out), .in1(adder_6_cout), .out(multiplexer_42_out[0]), .sel(multiplexer_24_out[1]));
  Multiplexer #(.width(3)) multiplexer_43 (
    .in0(multiplexer_37_out), .in1(multiplexer_38_out), .out(multiplexer_43_out), .sel(multiplexer_24_out[0]));
  Multiplexer #(.width(32)) multiplexer_44 (
    .in0(multiplexer_40_out), .in1(adder_9_out), .out(ADDR_OUT), .sel(or_38_out));
  or or_38 (or_38_out, and_3_out, RIDT);
  Multiplexer #(.enable("true"), .select(4), .width(32)) multiplexer_45 (
    .in0(adder_6_out), .in1(subtractor_2_out), .in2(multiplexer_33_out), .in3(multiplexer_35_out),
    .in4(and_44_out), .in5(or_37_out), .in6(xor_1_out), .in7(not_7_out), .in8(shifter_2_out),
    .in9(shifter_3_out), .in10(shifter_4_out), .in11(shifter_5_out), .in12(shifter_6_out),
    .out(multiplexer_45_out), .sel(pla_2_out), .en(ALUEN));  // open: in13, in14, in15
  Multiplexer #(.width(3)) multiplexer_46 (
    .in0(multiplexer_43_out), .in1(multiplexer_39_out), .out(multiplexer_46_out), .sel(multiplexer_24_out[1]));
  Comparator #(.width(32)) comparator_8 (
    .a(multiplexer_45_out), .b({32{1'b0}}), .eq(multiplexer_42_out[4]), .lt(multiplexer_42_out[2]));  // open: gt
  Pull_Resistor pull_resistor_181 (.node(multiplexer_42_out[3]));

  assign LE1 = LE0;

  // Notes on the sheet:
  //   contents of rom_1 (hex, n*v repeats v):
  //   0 7*2 7*1 7*0 2 0 13*2
endmodule

module TEST (
  input  EN,
  input  CLK,
  input  in_3
);

  wire cpu_1_le0, cpu_1_le1, cpu_1_le2, cpu_1_le3, cpu_1_mwe;
  wire [31:0] cpu_1_addr_out, cpu_1_data_out, cpu_1_ic_out, undriven;
  wire [63:0] dualram_1_p16;

  CPU cpu_1 (
    .INST_IN(dualram_1_p16), .DATA_IN(undriven), .ENABLE(EN), .CLK(CLK), .RESET(in_3), .LE0(cpu_1_le0),
    .LE1(cpu_1_le1), .LE2(cpu_1_le2), .LE3(cpu_1_le3), .DATA_OUT(cpu_1_data_out), .MWE(cpu_1_mwe),
    .ADDR_OUT(cpu_1_addr_out), .IC_OUT(cpu_1_ic_out));  // open: INT_IN, CALL_IRQ, MOE, FLAGS_OUT, IRQ_EN
  // DualRAM #(.addrWidth(24), .clearpin("true"), .enables("line"), .line("octo"), .misaligned("true")) dualram_1: pin names not known; wires that end beside it: CLK, cpu_1_addr_out[23:0], cpu_1_mwe, cpu_1_le0, cpu_1_le1, cpu_1_le2, cpu_1_le3, in_3, dualram_1_p16[63:56], dualram_1_p16[55:48], dualram_1_p16[47:40], dualram_1_p16[39:32], dualram_1_p16[31:24], dualram_1_p16[23:16], dualram_1_p16[15:8], dualram_1_p16[7:0]
endmodule
