// Logisim project i8046.circ as structural Verilog: 2 circuits, main circuit CPU
module CPU (
  input  [7:0] LDIN_BYTE0,
  input  [7:0] MDIN_BYTE1,
  input  [7:0] HDIN_BYTE2,
  input  [7:0] INST_BYTE7,
  input  [7:0] INST_BYTE6,
  input  [7:0] INST_BYTE5,
  input  [7:0] INST_BYTE4,
  input  [7:0] INST_BYTE3,
  input  [7:0] INST_BYTE2,
  input  [7:0] INST_BYTE1,
  input  [7:0] INST_BYTE0,
  input  [7:0] IRQ_ID,
  input  IRQ_IN,
  input  ENABLE,
  input  CLK,
  input  RESET,
  output HCE0,
  output MCE1,
  output LCE2,
  output [7:0] LDOUT_BYTE0,
  output [7:0] MDOUT_BYTE1,
  output [7:0] HDOUT_BYTE2,
  output IRQ_EN,
  output IRQ_IN_PROCESS,
  output [23:0] DATA_ADDR,
  output [23:0] INST_ADDR,
  output RAM_WE,
  output RAM_OE
);

  wire adder_10_cout, adder_11_cout, adder_12_cout, ALU_IMM, and_1_out, and_2_out, and_3_out, and_4_out,
       and_6_out, and_7_out, and_9_out, and_10_out, and_11_out, and_12_out, and_13_out, and_14_out,
       and_15_out, and_16_out, and_17_out, and_18_out, and_19_out, and_20_out, and_21_out, and_22_out,
       and_23_out, and_24_out, and_25_out, and_26_out, and_27_out, and_28_out, and_29_out, and_30_out,
       and_31_out, and_32_out, and_33_out, and_34_out, and_35_out, and_36_out, and_37_out, and_38_out,
       and_39_out, and_40_out, and_41_out, and_42_out, and_43_out, and_44_out, and_45_out, and_46_out,
       and_47_out, and_48_out, and_49_out, and_50_out, and_51_out, and_52_out, and_53_out, and_54_out,
       and_55_out, and_56_out, and_57_out, and_58_out, and_59_out, and_60_out, and_61_out, and_62_out,
       and_63_out, and_64_out, and_65_out, and_66_out, and_67_out, and_68_out, and_69_out, and_70_out,
       and_71_out, and_72_out, and_73_out, and_74_out, and_75_out, and_76_out, and_77_out, and_78_out,
       and_79_out, and_80_out, and_81_out, and_82_out, and_83_out, and_84_out, and_85_out, BR, CALL_AIC_WE,
       CCARRY, comparator_1_eq, comparator_2_eq, comparator_2_lt, comparator_3_eq, comparator_3_gt,
       comparator_4_eq, comparator_4_lt, comparator_5_eq, comparator_5_gt, comparator_5_lt, comparator_6_eq,
       comparator_6_gt, comparator_6_lt, comparator_7_eq, comparator_7_gt, comparator_7_lt, comparator_8_eq,
       comparator_8_gt, comparator_8_lt, comparator_9_eq, comparator_9_gt, comparator_9_lt, comparator_10_eq,
       comparator_10_gt, comparator_10_lt, comparator_11_lt, comparator_12_lt, comparator_13_lt, CONSBORROW,
       CONTEXT_q, CONTEXT_qn, d_ff_1_q, d_ff_2_q, d_ff_3_q, d_ff_4_q, d_ff_5_q, d_ff_6_q, d_ff_7_q, d_ff_8_q,
       d_ff_9_q, d_ff_10_q, d_ff_11_q, d_ff_12_q, d_ff_13_q, d_ff_14_q, d_ff_15_q, d_ff_16_q, d_ff_17_q,
       d_ff_18_q, d_ff_19_q, d_ff_20_q, d_ff_21_q, d_ff_22_q, d_ff_23_q, d_ff_24_q, d_ff_25_q, DBORROW,
       decoder_1_out2, decoder_1_out3, decoder_1_out4, decoder_1_out5, decoder_1_out6, decoder_1_out7,
       decoder_2_out1, decoder_2_out2, decoder_2_out3, decoder_2_out4, decoder_2_out5, decoder_2_out6,
       decoder_2_out7, decoder_2_out8, decoder_2_out9, decoder_2_out10, decoder_2_out11, decoder_2_out12,
       decoder_2_out13, decoder_2_out14, decoder_2_out15, decoder_2_out16, decoder_2_out17, decoder_2_out18,
       decoder_2_out19, decoder_2_out20, decoder_2_out21, decoder_2_out22, decoder_2_out23, decoder_2_out24,
       decoder_2_out25, decoder_2_out26, decoder_2_out27, decoder_2_out28, decoder_2_out29, decoder_2_out30,
       decoder_3_out1, decoder_3_out2, decoder_4_out0, decoder_4_out1, decoder_4_out2, decoder_5_out1,
       decoder_5_out2, DIS_IRQ, EN_IRQ, ENALU, ENSP, HALT, ICARRY, IE_q, IE_qn, IEND, LICB, MKICB,
       multiplexer_23_out, multiplexer_24_out, multiplexer_49_out, multiplexer_64_out, multiplexer_65_out,
       multiplexer_66_out, multiplexer_67_out, multiplexer_68_out, multiplexer_69_out, multiplexer_70_out,
       multiplexer_71_out, multiplexer_72_out, MWE, MWEA, nor_1_out, not_2_out, not_3_out, not_4_out,
       not_5_out, or_1_out, or_2_out, or_3_out, or_4_out, or_5_out, or_6_out, or_7_out, or_8_out, or_9_out,
       or_11_out, or_12_out, or_13_out, or_14_out, or_15_out, or_16_out, or_17_out, or_18_out, or_19_out,
       or_20_out, or_21_out, or_22_out, or_23_out, or_24_out, or_25_out, or_26_out, or_27_out, or_28_out,
       or_29_out, or_30_out, or_31_out, or_32_out, or_33_out, or_34_out, or_35_out, or_36_out, or_37_out,
       or_38_out, or_39_out, or_40_out, or_41_out, or_42_out, or_43_out, or_44_out, or_45_out, or_46_out,
       or_47_out, or_48_out, or_49_out, or_50_out, or_51_out, or_52_out, or_53_out, or_54_out, or_55_out,
       or_56_out, or_57_out, or_58_out, or_59_out, or_60_out, or_61_out, or_62_out, or_63_out, or_64_out,
       or_65_out, or_66_out, or_67_out, or_68_out, or_69_out, or_70_out, or_71_out, or_72_out, or_73_out,
       or_74_out, or_75_out, or_76_out, or_77_out, or_78_out, or_79_out, or_80_out, or_84_out, or_85_out,
       or_86_out, or_87_out, or_88_out, or_92_out, or_93_out, or_94_out, or_95_out, pull_resistor_239_node,
       pull_resistor_240_node, pull_resistor_241_node, pull_resistor_242_node, RDENIDT, REPADDR, RET_AIC_WE,
       RLOCK, RUNLOCK, RWE, SAC, SETDDSP, SSIGN, STSP, subtractor_5_bout, subtractor_6_bout,
       subtractor_7_bout, SW2BSU, UPDFL, UPDSP, WRENIDT, WRFM, WRFR, WRIMM;
  wire [1:0] multiplexer_33_out, rom_1_data;
  wire [2:0] adder_1_out, LENGHT_out, subtractor_1_out;
  wire [3:0] ALU_out;
  wire [7:0] adder_10_out, adder_11_out, adder_12_out, and_5_out, and_8_out, and_87_out, and_88_out,
       and_89_out, controlled_buffer_1_out, controlled_buffer_2_out, controlled_buffer_3_out,
       controlled_buffer_4_out, controlled_buffer_5_out, controlled_buffer_6_out, divider_1_out,
       divider_1_rem, divider_2_out, divider_2_rem, divider_3_out, divider_4_out, divider_4_rem,
       divider_5_out, divider_5_rem, divider_6_out, FL_q, multiplexer_1_out, multiplexer_2_out,
       multiplexer_3_out, multiplexer_4_out, multiplexer_5_out, multiplexer_6_out, multiplexer_7_out,
       multiplexer_8_out, multiplexer_9_out, multiplexer_12_out, multiplexer_13_out, multiplexer_14_out,
       multiplexer_15_out, multiplexer_16_out, multiplexer_17_out, multiplexer_18_out, multiplexer_19_out,
       multiplexer_20_out, multiplexer_21_out, multiplexer_22_out, multiplexer_30_out, multiplexer_30_out_2,
       multiplexer_30_out_3, multiplexer_31_out, multiplexer_31_out_2, multiplexer_31_out_3,
       multiplexer_32_out, multiplexer_32_out_2, multiplexer_32_out_3, multiplexer_34_out,
       multiplexer_35_out, multiplexer_36_out, multiplexer_37_out, multiplexer_38_out, multiplexer_39_out,
       multiplexer_40_out, multiplexer_41_out, multiplexer_42_out, multiplexer_43_out, multiplexer_44_out,
       multiplexer_45_out, multiplexer_56_out, multiplexer_58_out, multiplexer_59_out, multiplexer_60_out,
       multiplexer_61_out, multiplexer_62_out, multiplexer_63_out, multiplexer_77_out, multiplexer_78_out,
       multiplexer_79_out, multiplexer_80_out, multiplexer_81_out, multiplexer_82_out, multiplier_1_cout,
       multiplier_1_out, multiplier_2_cout, multiplier_2_out, multiplier_3_out, multiplier_4_cout,
       multiplier_4_out, multiplier_5_cout, multiplier_5_out, multiplier_6_out, not_6_out, not_7_out,
       not_8_out, or_10_out, or_81_out, or_82_out, or_83_out, pull_resistor_42_node, pull_resistor_49_node,
       pull_resistor_50_node, pull_resistor_51_node, pull_resistor_52_node, pull_resistor_53_node,
       pull_resistor_54_node, pull_resistor_55_node, pull_resistor_56_node, pull_resistor_57_node,
       pull_resistor_58_node, pull_resistor_59_node, pull_resistor_60_node, pull_resistor_61_node,
       pull_resistor_62_node, pull_resistor_63_node, pull_resistor_64_node, pull_resistor_65_node,
       pull_resistor_66_node, pull_resistor_67_node, pull_resistor_68_node, pull_resistor_69_node,
       pull_resistor_70_node, pull_resistor_71_node, pull_resistor_72_node, pull_resistor_73_node,
       pull_resistor_74_node, pull_resistor_75_node, pull_resistor_76_node, pull_resistor_77_node,
       pull_resistor_78_node, pull_resistor_79_node, pull_resistor_80_node, pull_resistor_81_node,
       pull_resistor_82_node, pull_resistor_83_node, pull_resistor_84_node, pull_resistor_85_node,
       pull_resistor_86_node, pull_resistor_87_node, pull_resistor_88_node, pull_resistor_89_node,
       pull_resistor_90_node, pull_resistor_91_node, pull_resistor_92_node, pull_resistor_93_node,
       pull_resistor_94_node, pull_resistor_95_node, pull_resistor_96_node, pull_resistor_97_node,
       pull_resistor_98_node, pull_resistor_99_node, pull_resistor_100_node, pull_resistor_101_node,
       pull_resistor_102_node, pull_resistor_103_node, pull_resistor_104_node, pull_resistor_105_node,
       pull_resistor_106_node, pull_resistor_107_node, pull_resistor_108_node, pull_resistor_109_node,
       pull_resistor_110_node, pull_resistor_111_node, pull_resistor_112_node, pull_resistor_113_node,
       pull_resistor_114_node, pull_resistor_115_node, pull_resistor_116_node, pull_resistor_117_node,
       pull_resistor_118_node, pull_resistor_119_node, pull_resistor_120_node, pull_resistor_121_node,
       pull_resistor_122_node, pull_resistor_123_node, pull_resistor_124_node, pull_resistor_125_node,
       pull_resistor_126_node, pull_resistor_127_node, pull_resistor_128_node, pull_resistor_129_node,
       pull_resistor_130_node, pull_resistor_131_node, pull_resistor_132_node, pull_resistor_133_node,
       pull_resistor_134_node, pull_resistor_135_node, pull_resistor_136_node, pull_resistor_137_node,
       pull_resistor_138_node, pull_resistor_139_node, pull_resistor_140_node, pull_resistor_141_node,
       pull_resistor_142_node, pull_resistor_143_node, pull_resistor_144_node, pull_resistor_145_node,
       pull_resistor_146_node, pull_resistor_147_node, pull_resistor_148_node, pull_resistor_149_node,
       pull_resistor_150_node, pull_resistor_151_node, pull_resistor_152_node, pull_resistor_153_node,
       pull_resistor_154_node, pull_resistor_155_node, pull_resistor_156_node, pull_resistor_157_node,
       pull_resistor_158_node, pull_resistor_159_node, pull_resistor_160_node, pull_resistor_161_node,
       pull_resistor_162_node, pull_resistor_163_node, pull_resistor_164_node, pull_resistor_165_node,
       pull_resistor_166_node, pull_resistor_167_node, pull_resistor_168_node, pull_resistor_169_node,
       pull_resistor_170_node, pull_resistor_171_node, pull_resistor_172_node, pull_resistor_173_node,
       pull_resistor_174_node, pull_resistor_175_node, pull_resistor_176_node, pull_resistor_177_node,
       pull_resistor_178_node, pull_resistor_179_node, pull_resistor_180_node, pull_resistor_181_node,
       pull_resistor_182_node, pull_resistor_183_node, pull_resistor_184_node, pull_resistor_185_node,
       pull_resistor_186_node, pull_resistor_187_node, pull_resistor_188_node, pull_resistor_189_node,
       pull_resistor_190_node, pull_resistor_191_node, pull_resistor_192_node, pull_resistor_193_node,
       pull_resistor_194_node, pull_resistor_195_node, pull_resistor_196_node, pull_resistor_197_node,
       pull_resistor_198_node, pull_resistor_199_node, pull_resistor_200_node, pull_resistor_201_node,
       pull_resistor_202_node, pull_resistor_203_node, pull_resistor_204_node, pull_resistor_205_node,
       pull_resistor_206_node, pull_resistor_207_node, pull_resistor_208_node, pull_resistor_209_node,
       pull_resistor_210_node, pull_resistor_215_node, pull_resistor_216_node, pull_resistor_217_node,
       pull_resistor_218_node, pull_resistor_219_node, pull_resistor_220_node, pull_resistor_221_node,
       pull_resistor_222_node, pull_resistor_223_node, pull_resistor_224_node, pull_resistor_225_node,
       pull_resistor_226_node, pull_resistor_227_node, pull_resistor_228_node, pull_resistor_229_node,
       pull_resistor_230_node, pull_resistor_231_node, pull_resistor_232_node, pull_resistor_233_node,
       pull_resistor_234_node, pull_resistor_235_node, pull_resistor_236_node, pull_resistor_237_node,
       pull_resistor_238_node, SS_q, SS_q_2, SS_q_3, SSS_q, SSS_q_2, SSS_q_3, subtractor_5_out,
       subtractor_6_out, subtractor_7_out, undriven, XH1_q, XH2_q, XH3_q, XH4_q, XH5_q, XL1_q, XL2_q, XL3_q,
       XL4_q, XL5_q, xor_1_out, xor_2_out, xor_3_out;
  wire [15:0] MICROCODE_out;
  wire [23:0] A0_q, A1_q, A_IC_q, adder_2_out, adder_3_out, adder_4_out, adder_5_out, adder_6_out,
       adder_7_out, adder_9_out, BP_q, CS_A_q, CS_q, DS_q, ES_q, IC_BACKUP_q, IC_q, IX_q, IY_q,
       multiplexer_10_out, multiplexer_11_out, multiplexer_25_out, multiplexer_26_out, multiplexer_27_out,
       multiplexer_28_out, multiplexer_29_out, multiplexer_46_out, multiplexer_50_out, multiplexer_51_out,
       multiplexer_73_out, pull_resistor_211_node, pull_resistor_213_node, pull_resistor_214_node,
       ram_1_dout, SCS_q, SDS_q, SES_q, shifter_1_out, shifter_2_out, shifter_3_out, shifter_4_out,
       shifter_5_out, SP_q, subtractor_2_out, subtractor_3_out, subtractor_4_out;
  wire [23:3] pull_resistor_48_node;
  wire [47:0] demultiplexer_1_out1, demultiplexer_1_out2, demultiplexer_1_out3, demultiplexer_1_out4,
       demultiplexer_1_out5, demultiplexer_1_out6, demultiplexer_1_out7, demultiplexer_1_out8,
       demultiplexer_1_out9, demultiplexer_1_out10, demultiplexer_1_out11, demultiplexer_1_out12,
       demultiplexer_1_out13, demultiplexer_1_out14, demultiplexer_1_out15, demultiplexer_1_out16,
       demultiplexer_1_out17, demultiplexer_1_out18, demultiplexer_1_out19, demultiplexer_1_out20,
       demultiplexer_1_out21, demultiplexer_1_out22, demultiplexer_1_out23, demultiplexer_1_out24;

  Decoder #(.select(3)) decoder_1 (
    .out2(decoder_1_out2), .out3(decoder_1_out3), .out4(decoder_1_out4), .out5(decoder_1_out5),
    .out6(decoder_1_out6), .out7(decoder_1_out7), .sel(subtractor_1_out));  // open: out0, out1, en
  assign controlled_buffer_1_out = or_2_out ? INST_BYTE5 : 8'bz;  // Controlled_Buffer controlled_buffer_1
  assign controlled_buffer_2_out = or_3_out ? INST_BYTE4 : 8'bz;  // Controlled_Buffer controlled_buffer_2
  assign controlled_buffer_3_out = or_4_out ? INST_BYTE3 : 8'bz;  // Controlled_Buffer controlled_buffer_3
  assign controlled_buffer_4_out = or_5_out ? INST_BYTE2 : 8'bz;  // Controlled_Buffer controlled_buffer_4
  assign controlled_buffer_5_out = or_6_out ? INST_BYTE1 : 8'bz;  // Controlled_Buffer controlled_buffer_5
  assign controlled_buffer_6_out = decoder_1_out7 ? INST_BYTE0 : 8'bz;  // Controlled_Buffer controlled_buffer_6
  and and_1 (and_1_out, ENABLE, CLK);
  and and_2 (and_2_out, and_1_out, ~d_ff_1_q);  // AND_Gate
  D_Flip_Flop d_ff_1 (.D(and_3_out), .clk(CLK), .Q(d_ff_1_q), .reset(RESET));  // open: Qn, preset
  and and_3 (and_3_out, d_ff_2_q, or_1_out);
  or or_1 (or_1_out, HALT, or_79_out);
  PLA #(.in_width(16), .out_width(16), .\table ("0000000000000000 0000000000000000 # NOP\n00100100xxxxxxxx 0000000000000000 # IRET\n00100011xxxxxxxx 0010000000000000 # INT\n00011111xxxxxxxx 0000000000000000 # CLI\n00100000xxxxxxxx 0000000000000000 # STI\n00000001xxxxxxxx 0000000000000000 # HALT\n0000001000000000 0011100011101100 # ADD\n0000001000000001 0100000011101000 # ADD.b\n0000001000000010 0100100011101001 # ADD.w\n0000001000000011 0101000011101010 # ADD.a\n0000001100000000 0011100011101100 # ADC\n0000010000000000 0011100011110100 # SUB\n0000010000000001 0100000011110000 # SUB.b\n0000010000000010 0100100011110001 # SUB.w\n0000010000000011 0101000011110010 # SUB.a\n0000010100000000 0011100011110100 # SBB\n0000011000000000 0011100011100100 # MUL\n0000011000000001 0100000011100000 # MUL.b\n0000011000000010 0100100011100001 # MUL.w\n0000011000000011 0101000011100010 # MUL.a\n0000011100000000 0011100011100100 # IMUL\n0000011100000001 0100000011100000 # IMUL.b\n0000011100000010 0100100011100001 # IMUL.w\n0000011100000011 0101000011100010 # IMUL.a\n0000100000000000 0011100011100100 # DIV\n0000100000000001 0100000011100000 # DIV.b\n0000100000000010 0100100011100001 # DIV.w\n0000100000000011 0101000011100010 # DIV.a\n0000100100000000 0011100011100100 # IDIV\n0000100100000001 0100000011100000 # IDIV.b\n0000100100000010 0100100011100001 # IDIV.w\n0000100100000011 0101000011100010 # IDIV.a\n00001010xxxxxxxx 0011100011100100 # AND\n00001011xxxxxxxx 0011100011100100 # OR\n00001100xxxxxxxx 0011100011100100 # XOR\n00001101xxxxxxxx 0001100011100100 # NOT\n00001110xxxxxxxx 0001100011101100 # INC\n00001111xxxxxxxx 0001100011110100 # DEC\n0001000000000000 0011111100000100 # CMP\n0001000000000001 0100011100000000 # CMP.b\n0001000000000010 0100111100000001 # CMP.w\n0001000000000011 0101011100000010 # CMP.a\n0001000100000000 0011111100000100 # ICMP\n0001000100000001 0100011100000000 # ICMP.b\n0001000100000010 0100111100000001 # ICMP.w\n0001000100000011 0101011100000010 # ICMP.a\n00010010xxxxxxxx 0101100000000000 # JMP\n00010011xxxxxxxx 0001000000000010 # PUSH\n00010100xxxxxxxx 0000100000000010 # POP\n00010101xxxxxxxx 0011000000000010 # CALL\n00010110xxxxxxxx 0000000000000010 # RET\n0001011100000000 0110000000000100 # MOV (MOVE)\n0001011100000001 0110100000000000 # MOV.b (LDI)\n0001011100000010 0111000000000001 # MOV.w (LDI)\n0001011100000011 0111100000000010 # MOV.a (LDI)\n0001100000000100 1000000000000000 # MOV.b (STR) 0\n0001100000000101 1000100000000000 # MOV.b (STR) 1\n0001100000000111 1001100000000000 # MOV.b (STR) 3\n0001100001000100 1000000000000001 # MOV.w (STR) 0\n0001100001000101 1000100000000001 # MOV.w (STR) 1\n0001100001000111 1001100000000001 # MOV.w (STR) 3\n0001100010000100 1000000000000010 # MOV.a (STR) 0\n0001100010000101 1000100000000010 # MOV.a (STR) 1\n0001100010000111 1001100000000010 # MOV.a (STR) 3\n0001100100001000 1010000000000000 # MOV.b (LOD) 0\n0001100100001001 1010100000000000 # MOV.b (LOD) 1\n0001100100001011 1011100000000000 # MOV.b (LOD) 3\n0001100101001000 1010000000000001 # MOV.w (LOD) 0\n0001100101001001 1010100000000001 # MOV.w (LOD) 1\n0001100101001011 1011100000000001 # MOV.w (LOD) 3\n0001100110001000 1010000000000010 # MOV.a (LOD) 0\n0001100110001001 1010100000000010 # MOV.a (LOD) 1\n0001100110001011 1011100000000010 # MOV.a (LOD) 3\n00011010xxxxxxxx 0100000011100100 # LSL\n00011011xxxxxxxx 0100000011100100 # LSR\n00011100xxxxxxxx 0100000011100100 # ASR\n00011101xxxxxxxx 0100000011100100 # ROL\n00011110xxxxxxxx 0100000011100100 # ROR\n00100101xxxxxxxx 1100000000000000 # WRINT\n00100110xxxxxxxx 0000100000000000 # LOCK\n00100111xxxxxxxx 0000100000000000 # UNLOCK")) MICROCODE (
    .in({INST_BYTE7, INST_BYTE6}), .out(MICROCODE_out));
  Pull_Resistor pull_resistor_1 (.node(controlled_buffer_1_out));
  Pull_Resistor pull_resistor_2 (.node(controlled_buffer_2_out));
  Pull_Resistor pull_resistor_3 (.node(controlled_buffer_3_out));
  Pull_Resistor pull_resistor_4 (.node(controlled_buffer_4_out));
  Pull_Resistor pull_resistor_5 (.node(controlled_buffer_5_out));
  Pull_Resistor pull_resistor_6 (.node(controlled_buffer_6_out));
  or or_2 (or_2_out, decoder_1_out2, decoder_1_out3, decoder_1_out4, decoder_1_out5, decoder_1_out6, decoder_1_out7);
  or or_3 (or_3_out, decoder_1_out3, decoder_1_out4, decoder_1_out5, decoder_1_out6, decoder_1_out7);
  or or_4 (or_4_out, decoder_1_out4, decoder_1_out5, decoder_1_out6, decoder_1_out7);
  or or_5 (or_5_out, decoder_1_out5, decoder_1_out6, decoder_1_out7);
  or or_6 (or_6_out, decoder_1_out6, decoder_1_out7);
  D_Flip_Flop d_ff_2 (.D(and_2_out), .clk(and_2_out), .Q(d_ff_2_q), .reset(RESET));  // open: Qn, preset
  PLA #(.in_width(5), .out_width(3), .\table ("00000 000 # S0\n00001 001 # S1 (rD)\n00010 001 # S2 (rS)\n00011 001 # S3 (rS/D)\n00100 001 # S4 (imm8)\n00101 010 # S5 (imm16)\n00110 011 # S6 (imm24)\n00111 010 # A0 (rA = rA + rB)\n01000 010 # A1 (rS + imm8)\n01001 011 # A2 (rS + imm16)\n01010 100 # A3 (rS + imm24)\n01011 100 # J0\n01100 010 # D0 (rD <- rS)\n01101 010 # D1B (rD <- imm8)\n01110 011 # D1W (rD <- imm16)\n01111 100 # D1A (rD <- imm24)\n10000 100 # D2F (rS -> addr24)\n10001 011 # D2S (rS _> rB+rA)\n10010 101 # D2SI (rS -> rB+imm24)\n10011 010 # D2R (rS -> rA)\n10100 100 # D3F (rD <- addr24)\n10101 011 # D3S (rD <- rB+rA)\n10110 101 # D3SI (rD <-rB+imm24)\n10111 010 # D3R (rD <- rA)\n11000 100 # I0")) LENGHT (
    .in(MICROCODE_out[15:11]), .out(LENGHT_out));
  Adder #(.width(3)) adder_1 (.a(LENGHT_out), .b(3'b010), .out(adder_1_out));  // open: cin, cout
  Subtractor #(.width(3)) subtractor_1 (.a(adder_1_out), .b(3'b001), .out(subtractor_1_out));  // open: bin, bout
  Demultiplexer #(.select(5), .width(48)) demultiplexer_1 (
    .out1(demultiplexer_1_out1), .out2(demultiplexer_1_out2), .out3(demultiplexer_1_out3),
    .out4(demultiplexer_1_out4), .out5(demultiplexer_1_out5), .out6(demultiplexer_1_out6),
    .out7(demultiplexer_1_out7), .out8(demultiplexer_1_out8), .out9(demultiplexer_1_out9),
    .out10(demultiplexer_1_out10), .out11(demultiplexer_1_out11), .out12(demultiplexer_1_out12),
    .out13(demultiplexer_1_out13), .out14(demultiplexer_1_out14), .out15(demultiplexer_1_out15),
    .out16(demultiplexer_1_out16), .out17(demultiplexer_1_out17), .out18(demultiplexer_1_out18),
    .out19(demultiplexer_1_out19), .out20(demultiplexer_1_out20), .out21(demultiplexer_1_out21),
    .out22(demultiplexer_1_out22), .out23(demultiplexer_1_out23), .out24(demultiplexer_1_out24),
    .in({controlled_buffer_1_out, controlled_buffer_2_out, controlled_buffer_3_out, controlled_buffer_4_out, controlled_buffer_5_out, controlled_buffer_6_out}),
    .sel(MICROCODE_out[15:11]));  // open: out0, out25, out26, out27, out28, out29, out30, out31
  PLA #(.in_width(16), .out_width(35), .\table ("0000000000000000 00000000000000000000000000000000000 # NOP\n00000001xxxxxxxx 00000000010000000000000000000000000 # HALT\n00100100xxxxxxxx 00001000000000000000000101000000000 # IRET\n00100011xxxxxxxx 00000100000000000100000010100000000 # INT\n00011111xxxxxxxx 00000000000000000000000010000000000 # CLI\n00100000xxxxxxxx 00000000000000000000000100000000000 # STI\n0000001000000000 00000000000000000000010000000000101 # ADD\n0000001000000001 00000001000000000000010000000000101 # ADD.b\n0000001000000010 00000001000000000000010000000000101 # ADD.w\n0000001000000011 00000001000000000000010000000000101 # ADD.a\n00000011xxxxxxxx 00000000000000010000010000000000101 # ADC\n0000010000000000 00000000000000000000010000000000101 # SUB\n0000010000000001 00000001000000000000010000000000101 # SUB,b\n0000010000000010 00000001000000000000010000000000101 # SUB.w\n0000010000000011 00000001000000000000010000000000101 # SUB.a\n00000101xxxxxxxx 00000000000000010000010000000000101 # SBB\n0000011000000000 00000000000000000000010000000000101 # MUL\n0000011000000001 00000001000000000000010000000000101 # MUL.b\n0000011000000010 00000001000000000000010000000000101 # MUL.w\n0000011000000011 00000001000000000000010000000000101 # MUL.a\n0000011100000000 00000000100000000000010000000000101 # IMUL\n0000011100000001 00000001100000000000010000000000101 # IMUL.b\n0000011100000010 00000001100000000000010000000000101 # IMUL.w\n0000011100000011 00000001100000000000010000000000101 # IMUL.a\n0000100000000000 00000000000000000000010000000000101 # DIV\n0000100000000001 00000001000000000000010000000000101 # DIV.b\n0000100000000010 00000001000000000000010000000000101 # DIV.w\n0000100000000011 00000001000000000000010000000000101 # DIV.a\n0000100100000000 00000000100000000000010000000000101 # IDIV\n0000100100000001 00000001100000000000010000000000101 # IDIV.b\n0000100100000010 00000001100000000000010000000000101 # IDIV.w\n0000100100000011 00000001100000000000010000000000101 # IDIV.a\n00001010xxxxxxxx 00000000000000000000010000000000101 # AND\n00001011xxxxxxxx 00000000000000000000010000000000101 # OR\n00001100xxxxxxxx 00000000000000000000010000000000101 # XOR\n00001101xxxxxxxx 00000000000000000000010000000000101 # NOT\n00001110xxxxxxxx 00000000000001000000010000000000101 # INC\n00001111xxxxxxxx 00000000000010000000010000000000101 # DEC\n0001000000000000 00000000000000000000010000000000000 # CMP\n0001000000000001 00000001000000000000010000000000000 # CMP.b\n0001000000000010 00000001000000000000010000000000000 # CMP.w\n0001000000000011 00000001000000000000010000000000000 # CMP.a\n0001000100000000 00000000100000000000010000000000000 # ICMP\n0001000100000001 00000001100000000000010000000000000 # ICMP.b\n0001000100000010 00000001100000000000010000000000000 # ICMP.w\n0001000100000011 00000001100000000000010000000000000 # ICMP.a\n00010010xxxxxxxx 00000000000000000000001000000000000 # JMP\n00010011xxxxxxxx 00000010000100000010100000000000000 # PUSH\n00010100xxxxxxxx 00000010001000000011100000001000100 # POP\n00010101xxxxxxxx 00010010000100000010101000000000000 # CALL\n00010110xxxxxxxx 00100010001000000011101000000000000 # RET\n0001011100000000 00000000000000000000000000000100100 # MOV\n0001011100000001 00000000000000000000000000010000100 # LDI.b\n0001011100000010 00000000000000000000000000010000100 # LDI.w\n0001011100000011 00000000000000000000000000010000100 # LDI.a\n0001100000000100 01000000000100000000000000000000000 # STR.b 0\n0001100000000101 00000000000100000000000000000000000 # STR.b 1\n0001100000000111 10000000000100000000000000000000000 # STR.b 3\n0001100001000100 01000000000100000000000000000000000 # STR.w 0\n0001100001000101 00000000000100000000000000000000000 # STR.w 1\n0001100001000111 10000000000100000000000000000000000 # STR.w 3\n0001100010000100 01000000000100000000000000000000000 # STR.a 0\n0001100010000101 00000000000100000000000000000000000 # STR.a 1\n0001100010000111 10000000000100000000000000000000000 # STR.a 3\n0001100100001000 01000000001000000000000000001000100 # LOD.b 0\n0001100100001001 00000000001000000000000000001000100 # LOD.b 1\n0001100100001011 00000000001000000000000000001000100 # LOD.b 3\n0001100101001000 01000000001000000000000000001000100 # LOD.w 0\n0001100101001001 00000000001000000000000000001000100 # LOD.w 1\n0001100101001011 00000000001000000000000000001000100 # LOD.w 3\n0001100110001000 01000000001000000000000000001000100 # LOD.a 0\n0001100110001001 00000000001000000000000000001000100 # LOD.a 1\n0001100110001011 00000000001000000000000000001000100 # LOD.a 3\n00011010xxxxxxxx 00000001000000000000000000000000111 # LSL\n00011011xxxxxxxx 00000001000000000000000000000000111 # LSR\n00011100xxxxxxxx 00000001000000000000000000000000111 # ASR\n00011101xxxxxxxx 00000001000000000000000000000000111 # ROL\n00011110xxxxxxxx 00000001000000000000000000000000111 # ROR\n00100101xxxxxxxx 00000000000000001000000000000000000 # WRINT\n00100110xxxxxxxx 00000000000000000000000000000001000 # LOCK\n00100111xxxxxxxx 00000000000000000000000000000010000 # UNLOCK")) CU (
    .in({INST_BYTE7, INST_BYTE6}),
    .out({MWEA, REPADDR, RET_AIC_WE, CALL_AIC_WE, LICB, MKICB, STSP, ALU_IMM, SSIGN, HALT, RAM_OE, MWE, DBORROW, ICARRY, CONSBORROW, CCARRY, WRENIDT, RDENIDT, UPDSP, SETDDSP, ENSP, UPDFL, BR, EN_IRQ, DIS_IRQ, IEND, SAC, WRIMM, WRFM, WRFR, RUNLOCK, RLOCK, RWE, SW2BSU, ENALU}));
  Pull_Resistor pull_resistor_7 (.node(ENALU));
  LED ALU_ENABLE (.in(ENALU));
  Pull_Resistor pull_resistor_8 (.node(SW2BSU));
  LED SWITCH_2_BSU (.in(SW2BSU));
  Pull_Resistor pull_resistor_9 (.node(RWE));
  LED REG_WE (.in(RWE));
  Pull_Resistor pull_resistor_10 (.node(RLOCK));
  LED REG_LOCK (.in(RLOCK));
  Pull_Resistor pull_resistor_11 (.node(RUNLOCK));
  LED REG_UNLOCK (.in(RUNLOCK));
  Pull_Resistor pull_resistor_12 (.node(WRFR));
  LED WR_FROM_R (.in(WRFR));
  Pull_Resistor pull_resistor_13 (.node(WRFM));
  LED WR_FROM_M (.in(WRFM));
  Pull_Resistor pull_resistor_14 (.node(WRIMM));
  LED WR_IMM (.in(WRIMM));
  Pull_Resistor pull_resistor_15 (.node(SAC));
  LED SET_ALT_CONTEXT (.in(SAC));
  Pull_Resistor pull_resistor_16 (.node(IEND));
  LED INTERRUPT_END (.in(IEND));
  Pull_Resistor pull_resistor_17 (.node(DIS_IRQ));
  LED DISABLE_INT_REQ (.in(DIS_IRQ));
  Pull_Resistor pull_resistor_18 (.node(EN_IRQ));
  LED ENABLE_INT_IRQ (.in(EN_IRQ));
  Pull_Resistor pull_resistor_19 (.node(BR));
  LED BRANCH (.in(BR));
  Pull_Resistor pull_resistor_20 (.node(UPDFL));
  LED UPDATE_FLAGS (.in(UPDFL));
  Pull_Resistor pull_resistor_21 (.node(ENSP));
  LED ENABLE_SP (.in(ENSP));
  Pull_Resistor pull_resistor_22 (.node(SETDDSP));
  LED SET_DEC_DIRECTIONAL_SP (.in(SETDDSP));
  Pull_Resistor pull_resistor_23 (.node(UPDSP));
  LED UPDATE_SP (.in(UPDSP));
  Pull_Resistor pull_resistor_24 (.node(RDENIDT));
  LED READ_ENABLE_IDT (.in(RDENIDT));
  Pull_Resistor pull_resistor_25 (.node(WRENIDT));
  LED WRITE_ENABLE_IDT (.in(WRENIDT));
  Pull_Resistor pull_resistor_26 (.node(CCARRY));
  LED CONSIDE_CARRY (.in(CCARRY));
  Pull_Resistor pull_resistor_27 (.node(CONSBORROW));
  LED CONSIDE_BORROW (.in(CONSBORROW));
  Pull_Resistor pull_resistor_28 (.node(ICARRY));
  LED INC_CARRY (.in(ICARRY));
  Pull_Resistor pull_resistor_29 (.node(DBORROW));
  LED DEC_BORROW (.in(DBORROW));
  Pull_Resistor pull_resistor_30 (.node(MWE));
  LED MEM_WE (.in(MWE));
  Pull_Resistor pull_resistor_31 (.node(RAM_OE));
  LED MEM_OE (.in(RAM_OE));
  Pull_Resistor pull_resistor_32 (.node(HALT));
  LED HALT_CLOCK (.in(HALT));
  Pull_Resistor pull_resistor_33 (.node(SSIGN));
  LED SET_SIGN (.in(SSIGN));
  Pull_Resistor pull_resistor_34 (.node(ALU_IMM));
  LED u_ALU_IMM (.in(ALU_IMM));
  Pull_Resistor pull_resistor_35 (.node(STSP));
  LED SWAP_TO_SP (.in(STSP));
  Pull_Resistor pull_resistor_36 (.node(MKICB));
  LED MAKE_IC_BACKUP (.in(MKICB));
  Pull_Resistor pull_resistor_37 (.node(LICB));
  LED LOAD_IC_BACKUP (.in(LICB));
  Pull_Resistor pull_resistor_38 (.node(CALL_AIC_WE));
  LED CALL_SUBROUTINE (.in(CALL_AIC_WE));
  Pull_Resistor pull_resistor_39 (.node(RET_AIC_WE));
  LED RETURN_FROM_SUBR (.in(RET_AIC_WE));
  Pull_Resistor pull_resistor_40 (.node(REPADDR));
  LED REPLACE_ADDR (.in(REPADDR));
  Pull_Resistor pull_resistor_41 (.node(MWEA));
  LED MWE_ANYWAY (.in(MWEA));
  Multiplexer #(.width(8)) multiplexer_1 (
    .in0(multiplexer_3_out), .in1(demultiplexer_1_out24[47:40]), .out(multiplexer_1_out), .sel(WRENIDT));
  RAM #(.dataWidth(24)) ram_1 (
    .addr(multiplexer_2_out), .we(WRENIDT), .oe(RDENIDT), .clk(and_2_out),
    .din(demultiplexer_1_out24[39:16]), .dout(ram_1_dout));
  Multiplexer #(.width(8)) multiplexer_2 (
    .in0(multiplexer_1_out), .in1(IRQ_ID), .out(multiplexer_2_out), .sel(IRQ_IN_PROCESS));
  Pull_Resistor pull_resistor_42 (.node(pull_resistor_42_node));
  Multiplexer #(.select(5), .width(8)) multiplexer_3 (
    .in0(pull_resistor_42_node), .in1(pull_resistor_42_node), .in2(pull_resistor_42_node),
    .in3(pull_resistor_42_node), .in4(demultiplexer_1_out4[47:40]), .in5(demultiplexer_1_out5[39:32]),
    .in6(demultiplexer_1_out6[31:24]), .in7(pull_resistor_42_node), .in8(demultiplexer_1_out8[39:32]),
    .in9(demultiplexer_1_out9[31:24]), .in10(demultiplexer_1_out10[23:16]), .in11(pull_resistor_42_node),
    .in12(pull_resistor_42_node), .in13(demultiplexer_1_out13[39:32]), .in14(demultiplexer_1_out14[31:24]),
    .in15(demultiplexer_1_out15[23:16]), .in16(demultiplexer_1_out16[23:16]), .in17(pull_resistor_42_node),
    .in18(demultiplexer_1_out18[15:8]), .in19(pull_resistor_42_node), .in20(demultiplexer_1_out20[23:16]),
    .in21(pull_resistor_42_node), .in22(demultiplexer_1_out22[15:8]), .in23(pull_resistor_42_node),
    .in24(pull_resistor_42_node), .in25(pull_resistor_42_node), .in26(pull_resistor_42_node),
    .in27(pull_resistor_42_node), .in28(pull_resistor_42_node), .in29(pull_resistor_42_node),
    .in30(pull_resistor_42_node), .in31(pull_resistor_42_node), .out(multiplexer_3_out),
    .sel(MICROCODE_out[15:11]));
  Multiplexer #(.select(5), .width(8)) multiplexer_4 (
    .in0(pull_resistor_42_node), .in1(pull_resistor_42_node), .in2(pull_resistor_42_node),
    .in3(pull_resistor_42_node), .in4(pull_resistor_42_node), .in5(demultiplexer_1_out5[47:40]),
    .in6(demultiplexer_1_out6[39:32]), .in7(pull_resistor_42_node), .in8(pull_resistor_42_node),
    .in9(demultiplexer_1_out9[39:32]), .in10(demultiplexer_1_out10[31:24]), .in11(pull_resistor_42_node),
    .in12(pull_resistor_42_node), .in13(pull_resistor_42_node), .in14(demultiplexer_1_out14[39:32]),
    .in15(demultiplexer_1_out15[31:24]), .in16(demultiplexer_1_out16[31:24]), .in17(pull_resistor_42_node),
    .in18(demultiplexer_1_out18[23:16]), .in19(pull_resistor_42_node), .in20(demultiplexer_1_out20[31:24]),
    .in21(pull_resistor_42_node), .in22(demultiplexer_1_out22[23:16]), .in23(pull_resistor_42_node),
    .in24(pull_resistor_42_node), .in25(pull_resistor_42_node), .in26(pull_resistor_42_node),
    .in27(pull_resistor_42_node), .in28(pull_resistor_42_node), .in29(pull_resistor_42_node),
    .in30(pull_resistor_42_node), .in31(pull_resistor_42_node), .out(multiplexer_4_out),
    .sel(MICROCODE_out[15:11]));
  Multiplexer #(.select(5), .width(8)) multiplexer_5 (
    .in0(pull_resistor_42_node), .in1(pull_resistor_42_node), .in2(pull_resistor_42_node),
    .in3(pull_resistor_42_node), .in4(pull_resistor_42_node), .in5(pull_resistor_42_node),
    .in6(demultiplexer_1_out6[47:40]), .in7(pull_resistor_42_node), .in8(pull_resistor_42_node),
    .in9(pull_resistor_42_node), .in10(demultiplexer_1_out10[39:32]), .in11(pull_resistor_42_node),
    .in12(pull_resistor_42_node), .in13(pull_resistor_42_node), .in14(pull_resistor_42_node),
    .in15(demultiplexer_1_out15[39:32]), .in16(demultiplexer_1_out16[39:32]), .in17(pull_resistor_42_node),
    .in18(demultiplexer_1_out18[31:24]), .in19(demultiplexer_1_out20[39:32]), .in20(pull_resistor_42_node),
    .in21(pull_resistor_42_node), .in22(demultiplexer_1_out22[31:24]), .in23(pull_resistor_42_node),
    .in24(pull_resistor_42_node), .in25(pull_resistor_42_node), .in26(pull_resistor_42_node),
    .in27(pull_resistor_42_node), .in28(pull_resistor_42_node), .in29(pull_resistor_42_node),
    .in30(pull_resistor_42_node), .in31(pull_resistor_42_node), .out(multiplexer_5_out),
    .sel(MICROCODE_out[15:11]));
  Multiplexer #(.select(5), .width(8)) multiplexer_6 (
    .in0(pull_resistor_42_node), .in1(demultiplexer_1_out1[47:40]), .in2(pull_resistor_42_node),
    .in3(demultiplexer_1_out3[47:40]), .in4(pull_resistor_42_node), .in5(pull_resistor_42_node),
    .in6(pull_resistor_42_node), .in7(demultiplexer_1_out7[47:40]), .in8(demultiplexer_1_out8[47:40]),
    .in9(demultiplexer_1_out9[47:40]), .in10(demultiplexer_1_out10[47:40]), .in11(pull_resistor_42_node),
    .in12(demultiplexer_1_out12[47:40]), .in13(demultiplexer_1_out13[47:40]),
    .in14(demultiplexer_1_out14[47:40]), .in15(demultiplexer_1_out15[47:40]), .in16(pull_resistor_42_node),
    .in17(pull_resistor_42_node), .in18(pull_resistor_42_node), .in19(pull_resistor_42_node),
    .in20(demultiplexer_1_out20[47:40]), .in21(demultiplexer_1_out21[47:40]),
    .in22(demultiplexer_1_out22[47:40]), .in23(demultiplexer_1_out23[47:40]), .in24(pull_resistor_42_node),
    .in25(pull_resistor_42_node), .in26(pull_resistor_42_node), .in27(pull_resistor_42_node),
    .in28(pull_resistor_42_node), .in29(pull_resistor_42_node), .in30(pull_resistor_42_node),
    .in31(pull_resistor_42_node), .out(multiplexer_6_out), .sel(MICROCODE_out[15:11]));
  Multiplexer #(.select(5), .width(8)) multiplexer_7 (
    .in0(pull_resistor_42_node), .in1(pull_resistor_42_node), .in2(demultiplexer_1_out2[47:40]),
    .in3(demultiplexer_1_out3[47:40]), .in4(pull_resistor_42_node), .in5(pull_resistor_42_node),
    .in6(pull_resistor_42_node), .in7(demultiplexer_1_out7[47:40]), .in8(demultiplexer_1_out8[47:40]),
    .in9(demultiplexer_1_out9[47:40]), .in10(demultiplexer_1_out10[47:40]), .in11(pull_resistor_42_node),
    .in12(demultiplexer_1_out12[39:32]), .in13(pull_resistor_42_node), .in14(pull_resistor_42_node),
    .in15(pull_resistor_42_node), .in16(demultiplexer_1_out16[47:40]), .in17(demultiplexer_1_out17[47:40]),
    .in18(demultiplexer_1_out18[47:40]), .in19(demultiplexer_1_out19[47:40]), .in20(pull_resistor_42_node),
    .in21(pull_resistor_42_node), .in22(pull_resistor_42_node), .in23(pull_resistor_42_node),
    .in24(pull_resistor_42_node), .in25(pull_resistor_42_node), .in26(pull_resistor_42_node),
    .in27(pull_resistor_42_node), .in28(pull_resistor_42_node), .in29(pull_resistor_42_node),
    .in30(pull_resistor_42_node), .in31(pull_resistor_42_node), .out(multiplexer_7_out),
    .sel(MICROCODE_out[15:11]));
  Multiplexer #(.select(5), .width(8)) multiplexer_8 (
    .in0(pull_resistor_42_node), .in1(pull_resistor_42_node), .in2(pull_resistor_42_node),
    .in3(pull_resistor_42_node), .in4(pull_resistor_42_node), .in5(pull_resistor_42_node),
    .in6(pull_resistor_42_node), .in7(demultiplexer_1_out7[39:32]), .in8(pull_resistor_42_node),
    .in9(pull_resistor_42_node), .in10(pull_resistor_42_node), .in11(pull_resistor_42_node),
    .in12(pull_resistor_42_node), .in13(pull_resistor_42_node), .in14(pull_resistor_42_node),
    .in15(pull_resistor_42_node), .in16(pull_resistor_42_node), .in17(demultiplexer_1_out17[31:24]),
    .in18(pull_resistor_42_node), .in19(demultiplexer_1_out19[39:32]), .in20(pull_resistor_42_node),
    .in21(demultiplexer_1_out21[31:24]), .in22(demultiplexer_1_out22[39:32]),
    .in23(demultiplexer_1_out23[39:32]), .in24(pull_resistor_42_node), .in25(pull_resistor_42_node),
    .in26(pull_resistor_42_node), .in27(pull_resistor_42_node), .in28(pull_resistor_42_node),
    .in29(pull_resistor_42_node), .in30(pull_resistor_42_node), .in31(pull_resistor_42_node),
    .out(multiplexer_8_out), .sel(MICROCODE_out[15:11]));
  Multiplexer #(.select(5), .width(8)) multiplexer_9 (
    .in0(pull_resistor_42_node), .in1(pull_resistor_42_node), .in2(pull_resistor_42_node),
    .in3(pull_resistor_42_node), .in4(pull_resistor_42_node), .in5(pull_resistor_42_node),
    .in6(pull_resistor_42_node), .in7(pull_resistor_42_node), .in8(pull_resistor_42_node),
    .in9(pull_resistor_42_node), .in10(pull_resistor_42_node), .in11(pull_resistor_42_node),
    .in12(pull_resistor_42_node), .in13(pull_resistor_42_node), .in14(pull_resistor_42_node),
    .in15(pull_resistor_42_node), .in16(pull_resistor_42_node), .in17(demultiplexer_1_out17[39:32]),
    .in18(demultiplexer_1_out18[39:32]), .in19(pull_resistor_42_node), .in20(pull_resistor_42_node),
    .in21(demultiplexer_1_out21[39:32]), .in22(pull_resistor_42_node), .in23(pull_resistor_42_node),
    .in24(pull_resistor_42_node), .in25(pull_resistor_42_node), .in26(pull_resistor_42_node),
    .in27(pull_resistor_42_node), .in28(pull_resistor_42_node), .in29(pull_resistor_42_node),
    .in30(pull_resistor_42_node), .in31(pull_resistor_42_node), .out(multiplexer_9_out),
    .sel(MICROCODE_out[15:11]));
  Pull_Resistor pull_resistor_43 (.node(ram_1_dout));
  Pull_Resistor pull_resistor_44 (.node(multiplexer_7_out[4:0]));
  Pull_Resistor pull_resistor_45 (.node(multiplexer_8_out[4:0]));
  Pull_Resistor pull_resistor_46 (.node(multiplexer_9_out[4:0]));
  Multiplexer #(.width(24)) multiplexer_10 (
    .in0(demultiplexer_1_out11[39:16]), .in1(demultiplexer_1_out6[47:24]), .out(multiplexer_10_out),
    .sel(CALL_AIC_WE));
  D_Flip_Flop IRQ (.D(and_4_out), .clk(and_4_out), .Q(IRQ_IN_PROCESS), .reset(or_7_out));  // open: Qn, preset
  and and_4 (and_4_out, IRQ_IN, IE_qn);
  or or_7 (or_7_out, IEND, RESET);
  Multiplexer #(.width(24)) multiplexer_11 (
    .in0(multiplexer_10_out), .in1({HDIN_BYTE2, MDIN_BYTE1, LDIN_BYTE0}), .out(multiplexer_11_out),
    .sel(RET_AIC_WE));
  Multiplexer #(.width(8)) multiplexer_12 (
    .in0(multiplexer_80_out), .in1(multiplexer_34_out), .out(multiplexer_12_out), .sel(WRFR));
  Multiplexer #(.width(8)) multiplexer_13 (
    .in0(multiplexer_12_out), .in1(LDIN_BYTE0), .out(multiplexer_13_out), .sel(WRFM));
  Multiplexer #(.width(8)) multiplexer_14 (
    .in0(multiplexer_81_out), .in1(multiplexer_35_out), .out(multiplexer_14_out), .sel(WRFR));
  Multiplexer #(.width(8)) multiplexer_15 (
    .in0(multiplexer_14_out), .in1(MDIN_BYTE1), .out(multiplexer_15_out), .sel(WRFM));
  Multiplexer #(.width(8)) multiplexer_16 (
    .in0(multiplexer_82_out), .in1(multiplexer_36_out), .out(multiplexer_16_out), .sel(WRFR));
  Multiplexer #(.width(8)) multiplexer_17 (
    .in0(multiplexer_16_out), .in1(HDIN_BYTE2), .out(multiplexer_17_out), .sel(WRFM));
  Multiplexer #(.width(8)) multiplexer_18 (
    .in0(multiplexer_13_out), .in1(multiplexer_3_out), .out(multiplexer_18_out), .sel(WRIMM));
  Multiplexer #(.width(8)) multiplexer_19 (
    .in0(multiplexer_15_out), .in1(multiplexer_4_out), .out(multiplexer_19_out), .sel(WRIMM));
  Multiplexer #(.width(8)) multiplexer_20 (
    .in0(multiplexer_17_out), .in1(multiplexer_5_out), .out(multiplexer_20_out), .sel(WRIMM));
  Pull_Resistor pull_resistor_47 (.node(multiplexer_6_out[4:0]));
  Decoder #(.select(5)) decoder_2 (
    .out1(decoder_2_out1), .out2(decoder_2_out2), .out3(decoder_2_out3), .out4(decoder_2_out4),
    .out5(decoder_2_out5), .out6(decoder_2_out6), .out7(decoder_2_out7), .out8(decoder_2_out8),
    .out9(decoder_2_out9), .out10(decoder_2_out10), .out11(decoder_2_out11), .out12(decoder_2_out12),
    .out13(decoder_2_out13), .out14(decoder_2_out14), .out15(decoder_2_out15), .out16(decoder_2_out16),
    .out17(decoder_2_out17), .out18(decoder_2_out18), .out19(decoder_2_out19), .out20(decoder_2_out20),
    .out21(decoder_2_out21), .out22(decoder_2_out22), .out23(decoder_2_out23), .out24(decoder_2_out24),
    .out25(decoder_2_out25), .out26(decoder_2_out26), .out27(decoder_2_out27), .out28(decoder_2_out28),
    .out29(decoder_2_out29), .out30(decoder_2_out30), .sel(multiplexer_6_out[4:0]));  // open: out0, out31, en
  Multiplexer #(.width(8)) multiplexer_21 (
    .in0(multiplexer_19_out), .in1(multiplexer_18_out), .out(multiplexer_21_out), .sel(or_8_out));
  Pull_Resistor pull_resistor_48 (.node({pull_resistor_48_node, adder_1_out}));
  ROM #(.addrWidth(5), .dataWidth(2)) rom_1 (.addr(multiplexer_6_out[4:0]), .data(rom_1_data));
  or or_8 (or_8_out, decoder_2_out3, decoder_2_out6, decoder_2_out9, decoder_2_out12, decoder_2_out15);
  D_Flip_Flop IE (.D(DIS_IRQ), .clk(DIS_IRQ), .Q(IE_q), .Qn(IE_qn), .reset(or_9_out));  // open: preset
  or or_9 (or_9_out, EN_IRQ, RESET);
  assign and_5_out = MICROCODE_out[10:3] & multiplexer_56_out;  // AND_Gate and_5, 8 bits wide
  not not_1 (IRQ_EN, IE_q);
  and and_6 (and_6_out, IRQ_IN, IE_qn);
  Register FL (.D(multiplexer_22_out), .en(or_11_out), .clk(and_2_out), .Q(FL_q), .clr(RESET));
  assign or_10_out = and_8_out | and_5_out;  // OR_Gate or_10, 8 bits wide
  Multiplexer #(.width(8)) multiplexer_22 (
    .in0(or_10_out), .in1(multiplexer_18_out), .out(multiplexer_22_out), .sel(decoder_2_out30));
  or or_11 (or_11_out, decoder_2_out30, UPDFL);
  not not_2 (not_2_out, FL_q[4]);
  or or_12 (or_12_out, FL_q[5], FL_q[6]);
  or or_13 (or_13_out, FL_q[7], FL_q[6]);
  not not_3 (not_3_out, FL_q[6]);
  D_Flip_Flop CONTEXT (
    .D(or_14_out), .clk(and_2_out), .Q(CONTEXT_q), .Qn(CONTEXT_qn), .reset(or_15_out));  // open: preset
  or or_14 (or_14_out, CONTEXT_q, SAC);
  nor nor_1 (nor_1_out, and_6_out, and_3_out, SAC);
  Multiplexer #(.select(4)) multiplexer_23 (
    .in0(1'b1), .in1(FL_q[0]), .in2(FL_q[1]), .in3(FL_q[2]), .in4(FL_q[3]), .in5(FL_q[4]), .in6(not_2_out),
    .in7(FL_q[5]), .in8(or_12_out), .in9(FL_q[7]), .in10(or_13_out), .in11(FL_q[6]), .in12(not_3_out),
    .out(multiplexer_23_out), .sel(demultiplexer_1_out11[43:40]));  // open: in13, in14, in15
  or or_15 (or_15_out, RESET, IEND);
  not not_4 (not_4_out, CONTEXT_qn);
  Multiplexer multiplexer_24 (.in0(not_4_out), .in1(and_7_out), .out(multiplexer_24_out), .sel(and_7_out));
  and and_7 (and_7_out, IRQ_IN_PROCESS, IE_qn);
  assign and_8_out = ~multiplexer_56_out & FL_q;  // AND_Gate and_8, 8 bits wide
  and and_9 (and_9_out, RWE, decoder_2_out18);
  Adder #(.width(24)) adder_2 (.a(SP_q), .b(24'h3), .out(adder_2_out));  // open: cin, cout
  Subtractor #(.width(24)) subtractor_2 (.a(SP_q), .b(24'h3), .out(subtractor_2_out));  // open: bin, bout
  or or_16 (or_16_out, decoder_2_out2, decoder_2_out1);
  or or_17 (or_17_out, decoder_2_out2, decoder_2_out1);
  or or_18 (or_18_out, decoder_2_out3, decoder_2_out1);
  Multiplexer #(.width(24)) multiplexer_25 (
    .in0(adder_2_out), .in1(subtractor_2_out), .out(multiplexer_25_out), .sel(SETDDSP));
  Multiplexer #(.width(24)) multiplexer_26 (
    .in0(multiplexer_25_out), .in1({multiplexer_20_out, multiplexer_19_out, multiplexer_18_out}),
    .out(multiplexer_26_out), .sel(RWE));
  and and_10 (and_10_out, ENSP, UPDSP);
  or or_19 (or_19_out, decoder_2_out2, decoder_2_out1);
  D_Flip_Flop d_ff_3 (.D(and_11_out), .clk(and_11_out), .Q(d_ff_3_q), .reset(or_20_out));  // open: Qn, preset
  and and_11 (and_11_out, or_16_out, RLOCK);
  or or_20 (or_20_out, and_12_out, RESET);
  and and_12 (and_12_out, RUNLOCK, or_17_out);
  or or_21 (or_21_out, decoder_2_out3, decoder_2_out1);
  D_Flip_Flop d_ff_4 (.D(and_13_out), .clk(and_13_out), .Q(d_ff_4_q), .reset(or_22_out));  // open: Qn, preset
  and and_13 (and_13_out, or_18_out, RLOCK);
  or or_22 (or_22_out, and_14_out, RESET);
  and and_14 (and_14_out, RUNLOCK, or_23_out);
  or or_23 (or_23_out, decoder_2_out3, decoder_2_out1);
  D_Flip_Flop d_ff_5 (.D(and_15_out), .clk(and_15_out), .Q(d_ff_5_q), .reset(or_24_out));  // open: Qn, preset
  and and_15 (and_15_out, decoder_2_out16, RLOCK);
  or or_24 (or_24_out, and_16_out, RESET);
  and and_16 (and_16_out, RUNLOCK, decoder_2_out16);
  D_Flip_Flop d_ff_6 (.D(and_17_out), .clk(and_17_out), .Q(d_ff_6_q), .reset(or_25_out));  // open: Qn, preset
  and and_17 (and_17_out, decoder_2_out17, RLOCK);
  or or_25 (or_25_out, and_18_out, RESET);
  and and_18 (and_18_out, RUNLOCK, decoder_2_out17);
  D_Flip_Flop d_ff_7 (.D(and_19_out), .clk(and_19_out), .Q(d_ff_7_q), .reset(or_26_out));  // open: Qn, preset
  and and_19 (and_19_out, decoder_2_out28, RLOCK);
  or or_26 (or_26_out, and_20_out, RESET);
  and and_20 (and_20_out, RUNLOCK, decoder_2_out28);
  Register #(.width(24)) SP (.D(multiplexer_26_out), .en(or_27_out), .clk(and_2_out), .Q(SP_q), .clr(RESET));
  or or_27 (or_27_out, and_9_out, and_10_out);
  and and_21 (and_21_out, or_19_out, RWE, ~d_ff_3_q);  // AND_Gate
  and and_22 (and_22_out, or_21_out, RWE, ~d_ff_4_q);  // AND_Gate
  and and_23 (and_23_out, decoder_2_out16, RWE, ~d_ff_5_q);  // AND_Gate
  and and_24 (and_24_out, decoder_2_out17, RWE, ~d_ff_6_q);  // AND_Gate
  and and_25 (and_25_out, decoder_2_out28, RWE, ~d_ff_7_q);  // AND_Gate
  Register XL1 (.D(multiplexer_18_out), .en(and_21_out), .clk(and_2_out), .Q(XL1_q), .clr(RESET));
  Register XH1 (.D(multiplexer_21_out), .en(and_22_out), .clk(and_2_out), .Q(XH1_q), .clr(RESET));
  Register #(.width(24)) IX (
    .D({multiplexer_20_out, multiplexer_19_out, multiplexer_18_out}), .en(and_23_out), .clk(and_2_out),
    .Q(IX_q), .clr(RESET));
  Register #(.width(24)) IY (
    .D({multiplexer_20_out, multiplexer_19_out, multiplexer_18_out}), .en(and_24_out), .clk(and_2_out),
    .Q(IY_q), .clr(RESET));
  Register #(.width(24)) A0 (
    .D({multiplexer_20_out, multiplexer_19_out, multiplexer_18_out}), .en(and_25_out), .clk(and_2_out),
    .Q(A0_q), .clr(RESET));
  Adder #(.width(24)) adder_3 (
    .a(IC_q), .b({pull_resistor_48_node, adder_1_out}), .out(adder_3_out));  // open: cin, cout
  not not_5 (not_5_out, multiplexer_24_out);
  and and_26 (and_26_out, ENABLE, multiplexer_24_out);
  and and_27 (and_27_out, BR, multiplexer_23_out);
  Multiplexer #(.width(24)) multiplexer_27 (
    .in0(adder_3_out), .in1(multiplexer_11_out), .out(multiplexer_27_out), .sel(and_27_out));
  and and_28 (and_28_out, not_5_out, ENABLE, nor_1_out);
  Adder #(.width(24)) adder_4 (
    .a(A_IC_q), .b({pull_resistor_48_node, adder_1_out}), .out(adder_4_out));  // open: cin, cout
  or or_28 (or_28_out, CALL_AIC_WE, RET_AIC_WE, and_26_out);
  or or_29 (or_29_out, CALL_AIC_WE, RET_AIC_WE);
  Register #(.width(24)) IC (.D(multiplexer_28_out), .en(or_30_out), .clk(and_2_out), .Q(IC_q), .clr(RESET));
  Multiplexer #(.width(24)) multiplexer_28 (
    .in0(multiplexer_27_out), .in1(IC_BACKUP_q), .out(multiplexer_28_out), .sel(LICB));
  or or_30 (or_30_out, and_28_out, or_29_out, LICB);
  Register #(.width(24)) A_IC (.D(multiplexer_29_out), .en(and_29_out), .clk(and_2_out), .Q(A_IC_q), .clr(or_31_out));
  Multiplexer #(.width(24)) multiplexer_29 (
    .in0(adder_4_out), .in1(multiplexer_11_out), .out(multiplexer_29_out), .sel(and_27_out));
  and and_29 (and_29_out, or_28_out, multiplexer_24_out);
  or or_31 (or_31_out, RESET, IEND);
  or or_32 (or_32_out, decoder_2_out5, decoder_2_out4);
  or or_33 (or_33_out, decoder_2_out6, decoder_2_out4);
  Multiplexer #(.width(24)) multiplexer_30 (
    .in0(IC_q), .in1(A_IC_q), .out({multiplexer_30_out_3, multiplexer_30_out_2, multiplexer_30_out}),
    .sel(multiplexer_24_out));
  D_Flip_Flop d_ff_8 (.D(and_30_out), .clk(and_30_out), .Q(d_ff_8_q), .reset(or_37_out));  // open: Qn, preset
  and and_30 (and_30_out, or_32_out, RLOCK);
  and and_31 (and_31_out, RUNLOCK, or_34_out);
  or or_34 (or_34_out, decoder_2_out5, decoder_2_out4);
  D_Flip_Flop d_ff_9 (.D(and_32_out), .clk(and_32_out), .Q(d_ff_9_q), .reset(or_39_out));  // open: Qn, preset
  and and_32 (and_32_out, or_33_out, RLOCK);
  and and_33 (and_33_out, RUNLOCK, or_35_out);
  or or_35 (or_35_out, decoder_2_out6, decoder_2_out4);
  D_Flip_Flop d_ff_10 (.D(and_34_out), .clk(and_34_out), .Q(d_ff_10_q), .reset(or_40_out));  // open: Qn, preset
  and and_34 (and_34_out, decoder_2_out20, RLOCK);
  and and_35 (and_35_out, RUNLOCK, decoder_2_out20);
  D_Flip_Flop d_ff_11 (.D(and_36_out), .clk(and_36_out), .Q(d_ff_11_q), .reset(or_41_out));  // open: Qn, preset
  and and_36 (and_36_out, decoder_2_out22, RLOCK);
  and and_37 (and_37_out, RUNLOCK, decoder_2_out22);
  D_Flip_Flop d_ff_12 (.D(and_38_out), .clk(and_38_out), .Q(d_ff_12_q), .reset(or_42_out));  // open: Qn, preset
  and and_38 (and_38_out, decoder_2_out29, RLOCK);
  and and_39 (and_39_out, RUNLOCK, decoder_2_out29);
  or or_36 (or_36_out, decoder_2_out5, decoder_2_out4);
  or or_37 (or_37_out, and_31_out, RESET);
  or or_38 (or_38_out, decoder_2_out6, decoder_2_out4);
  or or_39 (or_39_out, and_33_out, RESET);
  or or_40 (or_40_out, and_35_out, RESET);
  or or_41 (or_41_out, and_37_out, RESET);
  or or_42 (or_42_out, and_39_out, RESET);
  Register #(.width(24)) IC_BACKUP (.D(adder_5_out), .en(MKICB), .clk(and_2_out), .Q(IC_BACKUP_q), .clr(RESET));
  Adder #(.width(24)) adder_5 (.a(IC_q), .b(24'h3), .out(adder_5_out));  // open: cin, cout
  Adder #(.width(24)) adder_6 (
    .a({multiplexer_30_out_3, multiplexer_30_out_2, multiplexer_30_out}), .b(24'h5), .out(adder_6_out));  // open: cin, cout
  Register XL2 (.D(multiplexer_18_out), .en(and_40_out), .clk(and_2_out), .Q(XL2_q), .clr(RESET));
  and and_40 (and_40_out, or_36_out, RWE, ~d_ff_8_q);  // AND_Gate
  Register XH2 (.D(multiplexer_21_out), .en(and_41_out), .clk(and_2_out), .Q(XH2_q), .clr(RESET));
  and and_41 (and_41_out, or_38_out, RWE, ~d_ff_9_q);  // AND_Gate
  Register #(.width(24)) CS (
    .D({multiplexer_20_out, multiplexer_19_out, multiplexer_18_out}), .en(and_42_out), .clk(and_2_out),
    .Q(CS_q), .clr(RESET));
  and and_42 (and_42_out, decoder_2_out20, RWE, ~d_ff_10_q);  // AND_Gate
  Register #(.width(24)) SS (
    .D({multiplexer_20_out, multiplexer_19_out, multiplexer_18_out}), .en(and_43_out), .clk(and_2_out),
    .Q({SS_q_3, SS_q_2, SS_q}), .clr(RESET));
  and and_43 (and_43_out, decoder_2_out22, RWE, ~d_ff_11_q);  // AND_Gate
  Register #(.width(24)) A1 (
    .D({multiplexer_20_out, multiplexer_19_out, multiplexer_18_out}), .en(and_44_out), .clk(and_2_out),
    .Q(A1_q), .clr(RESET));
  and and_44 (and_44_out, decoder_2_out29, RWE, ~d_ff_12_q);  // AND_Gate
  Register #(.width(24)) CS_A (.D(ram_1_dout), .en(RDENIDT), .clk(and_2_out), .Q(CS_A_q), .clr(or_43_out));
  or or_43 (or_43_out, RESET, IEND);
  Multiplexer #(.width(24)) multiplexer_31 (
    .in0(CS_q), .in1(CS_A_q), .out({multiplexer_31_out_3, multiplexer_31_out_2, multiplexer_31_out}),
    .sel(multiplexer_24_out));
  or or_44 (or_44_out, decoder_2_out8, decoder_2_out7);
  or or_45 (or_45_out, decoder_2_out9, decoder_2_out7);
  and and_45 (and_45_out, or_44_out, RLOCK);
  or or_46 (or_46_out, decoder_2_out8, decoder_2_out7);
  and and_46 (and_46_out, or_45_out, RLOCK);
  or or_47 (or_47_out, decoder_2_out9, decoder_2_out7);
  and and_47 (and_47_out, decoder_2_out21, RLOCK);
  and and_48 (and_48_out, decoder_2_out23, RLOCK);
  and and_49 (and_49_out, decoder_2_out19, RLOCK);
  or or_48 (or_48_out, decoder_2_out8, decoder_2_out7);
  D_Flip_Flop d_ff_13 (.D(and_45_out), .clk(and_45_out), .Q(d_ff_13_q), .reset(or_49_out));  // open: Qn, preset
  or or_49 (or_49_out, and_50_out, RESET);
  and and_50 (and_50_out, RUNLOCK, or_46_out);
  or or_50 (or_50_out, decoder_2_out9, decoder_2_out7);
  D_Flip_Flop d_ff_14 (.D(and_46_out), .clk(and_46_out), .Q(d_ff_14_q), .reset(or_51_out));  // open: Qn, preset
  or or_51 (or_51_out, and_51_out, RESET);
  and and_51 (and_51_out, RUNLOCK, or_47_out);
  D_Flip_Flop d_ff_15 (.D(and_47_out), .clk(and_47_out), .Q(d_ff_15_q), .reset(or_52_out));  // open: Qn, preset
  or or_52 (or_52_out, and_52_out, RESET);
  and and_52 (and_52_out, RUNLOCK, decoder_2_out21);
  D_Flip_Flop d_ff_16 (.D(and_48_out), .clk(and_48_out), .Q(d_ff_16_q), .reset(or_53_out));  // open: Qn, preset
  or or_53 (or_53_out, and_53_out, RESET);
  and and_53 (and_53_out, RUNLOCK, decoder_2_out23);
  D_Flip_Flop d_ff_17 (.D(and_49_out), .clk(and_49_out), .Q(d_ff_17_q), .reset(or_54_out));  // open: Qn, preset
  or or_54 (or_54_out, and_54_out, RESET);
  and and_54 (and_54_out, RUNLOCK, decoder_2_out19);
  Register XL3 (.D(multiplexer_18_out), .en(and_55_out), .clk(and_2_out), .Q(XL3_q), .clr(RESET));
  and and_55 (and_55_out, or_48_out, RWE, ~d_ff_13_q);  // AND_Gate
  Register XH3 (.D(multiplexer_21_out), .en(and_56_out), .clk(and_2_out), .Q(XH3_q), .clr(RESET));
  and and_56 (and_56_out, or_50_out, RWE, ~d_ff_14_q);  // AND_Gate
  Register #(.width(24)) DS (
    .D({multiplexer_20_out, multiplexer_19_out, multiplexer_18_out}), .en(and_57_out), .clk(and_2_out),
    .Q(DS_q), .clr(RESET));
  and and_57 (and_57_out, decoder_2_out21, RWE, ~d_ff_15_q);  // AND_Gate
  Register #(.width(24)) ES (
    .D({multiplexer_20_out, multiplexer_19_out, multiplexer_18_out}), .en(and_58_out), .clk(and_2_out),
    .Q(ES_q), .clr(RESET));
  and and_58 (and_58_out, decoder_2_out23, RWE, ~d_ff_16_q);  // AND_Gate
  Register #(.width(24)) BP (
    .D({multiplexer_20_out, multiplexer_19_out, multiplexer_18_out}), .en(and_59_out), .clk(and_2_out),
    .Q(BP_q), .clr(RESET));
  and and_59 (and_59_out, decoder_2_out19, RWE, ~d_ff_17_q);  // AND_Gate
  or or_55 (or_55_out, decoder_2_out11, decoder_2_out10);
  and and_60 (and_60_out, or_55_out, RLOCK);
  or or_56 (or_56_out, decoder_2_out11, decoder_2_out10);
  or or_57 (or_57_out, decoder_2_out12, decoder_2_out10);
  and and_61 (and_61_out, or_57_out, RLOCK);
  or or_58 (or_58_out, decoder_2_out12, decoder_2_out10);
  and and_62 (and_62_out, decoder_2_out24, RLOCK);
  and and_63 (and_63_out, decoder_2_out26, RLOCK);
  or or_59 (or_59_out, decoder_2_out11, decoder_2_out10);
  D_Flip_Flop d_ff_18 (.D(and_60_out), .clk(and_60_out), .Q(d_ff_18_q), .reset(or_60_out));  // open: Qn, preset
  or or_60 (or_60_out, and_64_out, RESET);
  and and_64 (and_64_out, RUNLOCK, or_56_out);
  or or_61 (or_61_out, decoder_2_out12, decoder_2_out10);
  D_Flip_Flop d_ff_19 (.D(and_61_out), .clk(and_61_out), .Q(d_ff_19_q), .reset(or_62_out));  // open: Qn, preset
  or or_62 (or_62_out, and_65_out, RESET);
  and and_65 (and_65_out, RUNLOCK, or_58_out);
  D_Flip_Flop d_ff_20 (.D(and_62_out), .clk(and_62_out), .Q(d_ff_20_q), .reset(or_63_out));  // open: Qn, preset
  or or_63 (or_63_out, and_66_out, RESET);
  and and_66 (and_66_out, RUNLOCK, decoder_2_out24);
  D_Flip_Flop d_ff_21 (.D(and_63_out), .clk(and_63_out), .Q(d_ff_21_q), .reset(or_64_out));  // open: Qn, preset
  or or_64 (or_64_out, and_67_out, RESET);
  and and_67 (and_67_out, RUNLOCK, decoder_2_out26);
  and and_68 (and_68_out, or_59_out, RWE, ~d_ff_18_q);  // AND_Gate
  and and_69 (and_69_out, or_61_out, RWE, ~d_ff_19_q);  // AND_Gate
  and and_70 (and_70_out, decoder_2_out24, RWE, ~d_ff_20_q);  // AND_Gate
  and and_71 (and_71_out, decoder_2_out26, RWE, ~d_ff_21_q);  // AND_Gate
  Register XL4 (.D(multiplexer_18_out), .en(and_68_out), .clk(and_2_out), .Q(XL4_q), .clr(RESET));
  Register XH4 (.D(multiplexer_21_out), .en(and_69_out), .clk(and_2_out), .Q(XH4_q), .clr(RESET));
  Register #(.width(24)) SCS (
    .D({multiplexer_20_out, multiplexer_19_out, multiplexer_18_out}), .en(and_70_out), .clk(and_2_out),
    .Q(SCS_q), .clr(RESET));
  Register #(.width(24)) SSS (
    .D({multiplexer_20_out, multiplexer_19_out, multiplexer_18_out}), .en(and_71_out), .clk(and_2_out),
    .Q({SSS_q_3, SSS_q_2, SSS_q}), .clr(RESET));
  Multiplexer #(.width(24)) multiplexer_32 (
    .in0(SCS_q), .in1({24{1'b1}}), .out({multiplexer_32_out_3, multiplexer_32_out_2, multiplexer_32_out}),
    .sel(multiplexer_24_out));
  or or_65 (or_65_out, decoder_2_out14, decoder_2_out13);
  or or_66 (or_66_out, decoder_2_out15, decoder_2_out13);
  or or_67 (or_67_out, decoder_2_out14, decoder_2_out13);
  D_Flip_Flop d_ff_22 (.D(and_72_out), .clk(and_72_out), .Q(d_ff_22_q), .reset(or_68_out));  // open: Qn, preset
  and and_72 (and_72_out, or_65_out, RLOCK);
  or or_68 (or_68_out, and_73_out, RESET);
  and and_73 (and_73_out, RUNLOCK, or_69_out);
  or or_69 (or_69_out, decoder_2_out13, decoder_2_out14);
  or or_70 (or_70_out, decoder_2_out15, decoder_2_out13);
  D_Flip_Flop d_ff_23 (.D(and_74_out), .clk(and_74_out), .Q(d_ff_23_q), .reset(or_71_out));  // open: Qn, preset
  and and_74 (and_74_out, or_66_out, RLOCK);
  or or_71 (or_71_out, and_75_out, RESET);
  and and_75 (and_75_out, RUNLOCK, or_72_out);
  or or_72 (or_72_out, decoder_2_out15, decoder_2_out13);
  D_Flip_Flop d_ff_24 (.D(and_76_out), .clk(and_76_out), .Q(d_ff_24_q), .reset(or_73_out));  // open: Qn, preset
  and and_76 (and_76_out, decoder_2_out25, RLOCK);
  or or_73 (or_73_out, and_77_out, RESET);
  and and_77 (and_77_out, RUNLOCK, decoder_2_out25);
  D_Flip_Flop d_ff_25 (.D(and_78_out), .clk(and_78_out), .Q(d_ff_25_q), .reset(or_74_out));  // open: Qn, preset
  and and_78 (and_78_out, decoder_2_out27, RLOCK);
  or or_74 (or_74_out, and_79_out, RESET);
  and and_79 (and_79_out, RUNLOCK, decoder_2_out27);
  and and_80 (and_80_out, or_67_out, RWE, ~d_ff_22_q);  // AND_Gate
  and and_81 (and_81_out, or_70_out, RWE, ~d_ff_23_q);  // AND_Gate
  and and_82 (and_82_out, decoder_2_out25, RWE, ~d_ff_24_q);  // AND_Gate
  and and_83 (and_83_out, decoder_2_out27, RWE, ~d_ff_25_q);  // AND_Gate
  Register XL5 (.D(multiplexer_18_out), .en(and_80_out), .clk(and_2_out), .Q(XL5_q), .clr(RESET));
  Register XH5 (.D(multiplexer_21_out), .en(and_81_out), .clk(and_2_out), .Q(XH5_q), .clr(RESET));
  Register #(.width(24)) SDS (
    .D({multiplexer_20_out, multiplexer_19_out, multiplexer_18_out}), .en(and_82_out), .clk(and_2_out),
    .Q(SDS_q), .clr(RESET));
  Register #(.width(24)) SES (
    .D({multiplexer_20_out, multiplexer_19_out, multiplexer_18_out}), .en(and_83_out), .clk(and_2_out),
    .Q(SES_q), .clr(RESET));
  Comparator #(.width(3)) comparator_1 (.a(MICROCODE_out[2:0]), .b(3'b100), .eq(comparator_1_eq));  // open: gt, lt
  Multiplexer #(.width(2)) multiplexer_33 (
    .in0(MICROCODE_out[1:0]), .in1(rom_1_data), .out(multiplexer_33_out), .sel(comparator_1_eq));
  Pull_Resistor pull_resistor_49 (.node(pull_resistor_49_node));
  Multiplexer #(.select(5), .width(8)) multiplexer_34 (
    .in0(pull_resistor_49_node), .in1(XL1_q), .in2(XL1_q), .in3(XH1_q), .in4(XL2_q), .in5(XL2_q),
    .in6(XH2_q), .in7(XL3_q), .in8(XL3_q), .in9(XH3_q), .in10(XL4_q), .in11(XL4_q), .in12(XH4_q),
    .in13(XL5_q), .in14(XL5_q), .in15(XH5_q), .in16(IX_q[7:0]), .in17(IY_q[7:0]), .in18(SP_q[7:0]),
    .in19(BP_q[7:0]), .in20(multiplexer_31_out), .in21(DS_q[7:0]), .in22(SS_q), .in23(ES_q[7:0]),
    .in24(multiplexer_32_out), .in25(SDS_q[7:0]), .in26(SSS_q), .in27(SES_q[7:0]), .in28(A0_q[7:0]),
    .in29(A1_q[7:0]), .in30(FL_q), .in31(multiplexer_30_out), .out(multiplexer_34_out),
    .sel(multiplexer_7_out[4:0]));
  Pull_Resistor pull_resistor_50 (.node(pull_resistor_50_node));
  Pull_Resistor pull_resistor_51 (.node(pull_resistor_51_node));
  Pull_Resistor pull_resistor_52 (.node(pull_resistor_52_node));
  Pull_Resistor pull_resistor_53 (.node(pull_resistor_53_node));
  Pull_Resistor pull_resistor_54 (.node(pull_resistor_54_node));
  Pull_Resistor pull_resistor_55 (.node(pull_resistor_55_node));
  Pull_Resistor pull_resistor_56 (.node(pull_resistor_56_node));
  Pull_Resistor pull_resistor_57 (.node(pull_resistor_57_node));
  Pull_Resistor pull_resistor_58 (.node(pull_resistor_58_node));
  Pull_Resistor pull_resistor_59 (.node(pull_resistor_59_node));
  Pull_Resistor pull_resistor_60 (.node(pull_resistor_60_node));
  Multiplexer #(.select(5), .width(8)) multiplexer_35 (
    .in0(pull_resistor_50_node), .in1(XH1_q), .in2(pull_resistor_51_node), .in3(pull_resistor_52_node),
    .in4(XH2_q), .in5(pull_resistor_53_node), .in6(pull_resistor_54_node), .in7(XH3_q),
    .in8(pull_resistor_55_node), .in9(pull_resistor_56_node), .in10(XH4_q), .in11(pull_resistor_57_node),
    .in12(pull_resistor_58_node), .in13(XH5_q), .in14(pull_resistor_59_node), .in15(pull_resistor_60_node),
    .in16(IX_q[15:8]), .in17(IY_q[15:8]), .in18(SP_q[23:16]), .in19(BP_q[15:8]), .in20(multiplexer_31_out_2),
    .in21(DS_q[15:8]), .in22(SS_q_2), .in23(ES_q[15:8]), .in24(multiplexer_32_out_2), .in25(SDS_q[15:8]),
    .in26(SSS_q_2), .in27(SES_q[15:8]), .in28(A0_q[15:8]), .in29(A1_q[15:8]), .in30(pull_resistor_61_node),
    .in31(multiplexer_30_out_2), .out(multiplexer_35_out), .sel(multiplexer_7_out[4:0]));
  Pull_Resistor pull_resistor_61 (.node(pull_resistor_61_node));
  Pull_Resistor pull_resistor_62 (.node(pull_resistor_62_node));
  Pull_Resistor pull_resistor_63 (.node(pull_resistor_63_node));
  Pull_Resistor pull_resistor_64 (.node(pull_resistor_64_node));
  Pull_Resistor pull_resistor_65 (.node(pull_resistor_65_node));
  Pull_Resistor pull_resistor_66 (.node(pull_resistor_66_node));
  Pull_Resistor pull_resistor_67 (.node(pull_resistor_67_node));
  Pull_Resistor pull_resistor_68 (.node(pull_resistor_68_node));
  Pull_Resistor pull_resistor_69 (.node(pull_resistor_69_node));
  Pull_Resistor pull_resistor_70 (.node(pull_resistor_70_node));
  Pull_Resistor pull_resistor_71 (.node(pull_resistor_71_node));
  Pull_Resistor pull_resistor_72 (.node(pull_resistor_72_node));
  Pull_Resistor pull_resistor_73 (.node(pull_resistor_73_node));
  Pull_Resistor pull_resistor_74 (.node(pull_resistor_74_node));
  Pull_Resistor pull_resistor_75 (.node(pull_resistor_75_node));
  Pull_Resistor pull_resistor_76 (.node(pull_resistor_76_node));
  Pull_Resistor pull_resistor_77 (.node(pull_resistor_77_node));
  Multiplexer #(.select(5), .width(8)) multiplexer_36 (
    .in0(pull_resistor_62_node), .in1(pull_resistor_63_node), .in2(pull_resistor_64_node),
    .in3(pull_resistor_65_node), .in4(pull_resistor_66_node), .in5(pull_resistor_67_node),
    .in6(pull_resistor_68_node), .in7(pull_resistor_69_node), .in8(pull_resistor_70_node),
    .in9(pull_resistor_71_node), .in10(pull_resistor_72_node), .in11(pull_resistor_73_node),
    .in12(pull_resistor_74_node), .in13(pull_resistor_75_node), .in14(pull_resistor_76_node),
    .in15(pull_resistor_77_node), .in16(IX_q[23:16]), .in17(IY_q[23:16]), .in18(SP_q[23:16]),
    .in19(BP_q[23:16]), .in20(multiplexer_31_out_3), .in21(DS_q[23:16]), .in22(SS_q_3), .in23(ES_q[23:16]),
    .in24(multiplexer_32_out_3), .in25(SDS_q[23:16]), .in26(SSS_q_3), .in27(SES_q[23:16]),
    .in28(A0_q[23:16]), .in29(A1_q[23:16]), .in30(pull_resistor_78_node), .in31(multiplexer_30_out_3),
    .out(multiplexer_36_out), .sel(multiplexer_7_out[4:0]));
  Pull_Resistor pull_resistor_78 (.node(pull_resistor_78_node));
  Pull_Resistor pull_resistor_79 (.node(pull_resistor_79_node));
  Multiplexer #(.select(5), .width(8)) multiplexer_37 (
    .in0(pull_resistor_79_node), .in1(XL1_q), .in2(XL1_q), .in3(XH1_q), .in4(XL2_q), .in5(XL2_q),
    .in6(XH2_q), .in7(XL3_q), .in8(XL3_q), .in9(XH3_q), .in10(XL4_q), .in11(XL4_q), .in12(XH4_q),
    .in13(XL5_q), .in14(XL5_q), .in15(XH5_q), .in16(IX_q[7:0]), .in17(IY_q[7:0]), .in18(SP_q[7:0]),
    .in19(BP_q[7:0]), .in20(multiplexer_31_out), .in21(DS_q[7:0]), .in22(SS_q), .in23(ES_q[7:0]),
    .in24(multiplexer_32_out), .in25(SDS_q[7:0]), .in26(SSS_q), .in27(SES_q[7:0]), .in28(A0_q[7:0]),
    .in29(A1_q[7:0]), .in30(FL_q), .in31(multiplexer_30_out), .out(multiplexer_37_out),
    .sel(multiplexer_8_out[4:0]));
  Pull_Resistor pull_resistor_80 (.node(pull_resistor_80_node));
  Pull_Resistor pull_resistor_81 (.node(pull_resistor_81_node));
  Pull_Resistor pull_resistor_82 (.node(pull_resistor_82_node));
  Pull_Resistor pull_resistor_83 (.node(pull_resistor_83_node));
  Pull_Resistor pull_resistor_84 (.node(pull_resistor_84_node));
  Pull_Resistor pull_resistor_85 (.node(pull_resistor_85_node));
  Pull_Resistor pull_resistor_86 (.node(pull_resistor_86_node));
  Pull_Resistor pull_resistor_87 (.node(pull_resistor_87_node));
  Pull_Resistor pull_resistor_88 (.node(pull_resistor_88_node));
  Pull_Resistor pull_resistor_89 (.node(pull_resistor_89_node));
  Pull_Resistor pull_resistor_90 (.node(pull_resistor_90_node));
  Multiplexer #(.select(5), .width(8)) multiplexer_38 (
    .in0(pull_resistor_80_node), .in1(pull_resistor_81_node), .in2(pull_resistor_82_node), .in3(XH1_q),
    .in4(pull_resistor_83_node), .in5(pull_resistor_84_node), .in6(XH2_q), .in7(pull_resistor_85_node),
    .in8(pull_resistor_86_node), .in9(XH3_q), .in10(pull_resistor_87_node), .in11(pull_resistor_88_node),
    .in12(XH4_q), .in13(pull_resistor_89_node), .in14(pull_resistor_90_node), .in15(XH5_q),
    .in16(IX_q[15:8]), .in17(IY_q[15:8]), .in18(SP_q[15:8]), .in19(BP_q[15:8]), .in20(multiplexer_31_out_2),
    .in21(DS_q[15:8]), .in22(SS_q_2), .in23(ES_q[15:8]), .in24(multiplexer_32_out_2), .in25(SDS_q[15:8]),
    .in26(SSS_q_2), .in27(SES_q[15:8]), .in28(A0_q[15:8]), .in29(A1_q[15:8]), .in30(pull_resistor_91_node),
    .in31(multiplexer_30_out_2), .out(multiplexer_38_out), .sel(multiplexer_8_out[4:0]));
  Pull_Resistor pull_resistor_91 (.node(pull_resistor_91_node));
  Pull_Resistor pull_resistor_92 (.node(pull_resistor_92_node));
  Pull_Resistor pull_resistor_93 (.node(pull_resistor_93_node));
  Pull_Resistor pull_resistor_94 (.node(pull_resistor_94_node));
  Pull_Resistor pull_resistor_95 (.node(pull_resistor_95_node));
  Pull_Resistor pull_resistor_96 (.node(pull_resistor_96_node));
  Pull_Resistor pull_resistor_97 (.node(pull_resistor_97_node));
  Pull_Resistor pull_resistor_98 (.node(pull_resistor_98_node));
  Pull_Resistor pull_resistor_99 (.node(pull_resistor_99_node));
  Pull_Resistor pull_resistor_100 (.node(pull_resistor_100_node));
  Pull_Resistor pull_resistor_101 (.node(pull_resistor_101_node));
  Pull_Resistor pull_resistor_102 (.node(pull_resistor_102_node));
  Pull_Resistor pull_resistor_103 (.node(pull_resistor_103_node));
  Pull_Resistor pull_resistor_104 (.node(pull_resistor_104_node));
  Pull_Resistor pull_resistor_105 (.node(pull_resistor_105_node));
  Pull_Resistor pull_resistor_106 (.node(pull_resistor_106_node));
  Pull_Resistor pull_resistor_107 (.node(pull_resistor_107_node));
  Multiplexer #(.select(5), .width(8)) multiplexer_39 (
    .in0(pull_resistor_92_node), .in1(pull_resistor_93_node), .in2(pull_resistor_94_node),
    .in3(pull_resistor_95_node), .in4(pull_resistor_96_node), .in5(pull_resistor_97_node),
    .in6(pull_resistor_98_node), .in7(pull_resistor_99_node), .in8(pull_resistor_100_node),
    .in9(pull_resistor_101_node), .in10(pull_resistor_102_node), .in11(pull_resistor_103_node),
    .in12(pull_resistor_104_node), .in13(pull_resistor_105_node), .in14(pull_resistor_106_node),
    .in15(pull_resistor_107_node), .in16(IX_q[23:16]), .in17(IY_q[23:16]), .in18(SP_q[23:16]),
    .in19(BP_q[23:16]), .in20(multiplexer_31_out_3), .in21(DS_q[23:16]), .in22(SS_q_3), .in23(ES_q[23:16]),
    .in24(multiplexer_32_out_3), .in25(SDS_q[23:16]), .in26(SSS_q_3), .in27(SES_q[23:16]),
    .in28(A0_q[23:16]), .in29(A1_q[23:16]), .in30(pull_resistor_108_node), .in31(multiplexer_30_out_3),
    .out(multiplexer_39_out), .sel(multiplexer_8_out[4:0]));
  Pull_Resistor pull_resistor_108 (.node(pull_resistor_108_node));
  Pull_Resistor pull_resistor_109 (.node(pull_resistor_109_node));
  Multiplexer #(.select(5), .width(8)) multiplexer_40 (
    .in0(pull_resistor_109_node), .in1(XL1_q), .in2(XL1_q), .in3(XH1_q), .in4(XL2_q), .in5(XL2_q),
    .in6(XH2_q), .in7(XL3_q), .in8(XL3_q), .in9(XH3_q), .in10(XL4_q), .in11(XL4_q), .in12(XH4_q),
    .in13(XL5_q), .in14(XL5_q), .in15(XH5_q), .in16(IX_q[7:0]), .in17(IY_q[7:0]), .in18(SP_q[7:0]),
    .in19(BP_q[7:0]), .in20(multiplexer_31_out), .in21(DS_q[7:0]), .in22(SS_q), .in23(ES_q[7:0]),
    .in24(multiplexer_32_out), .in25(SDS_q[7:0]), .in26(SSS_q), .in27(SES_q[7:0]), .in28(A0_q[7:0]),
    .in29(A1_q[7:0]), .in30(FL_q), .in31(multiplexer_30_out), .out(multiplexer_40_out),
    .sel(multiplexer_9_out[4:0]));
  Pull_Resistor pull_resistor_110 (.node(pull_resistor_110_node));
  Pull_Resistor pull_resistor_111 (.node(pull_resistor_111_node));
  Pull_Resistor pull_resistor_112 (.node(pull_resistor_112_node));
  Pull_Resistor pull_resistor_113 (.node(pull_resistor_113_node));
  Pull_Resistor pull_resistor_114 (.node(pull_resistor_114_node));
  Pull_Resistor pull_resistor_115 (.node(pull_resistor_115_node));
  Pull_Resistor pull_resistor_116 (.node(pull_resistor_116_node));
  Pull_Resistor pull_resistor_117 (.node(pull_resistor_117_node));
  Pull_Resistor pull_resistor_118 (.node(pull_resistor_118_node));
  Pull_Resistor pull_resistor_119 (.node(pull_resistor_119_node));
  Pull_Resistor pull_resistor_120 (.node(pull_resistor_120_node));
  Multiplexer #(.select(5), .width(8)) multiplexer_41 (
    .in0(pull_resistor_110_node), .in1(XH1_q), .in2(pull_resistor_111_node), .in3(pull_resistor_112_node),
    .in4(XH2_q), .in5(pull_resistor_113_node), .in6(pull_resistor_114_node), .in7(XH3_q),
    .in8(pull_resistor_115_node), .in9(pull_resistor_116_node), .in10(XH4_q), .in11(pull_resistor_117_node),
    .in12(pull_resistor_118_node), .in13(XH5_q), .in14(pull_resistor_119_node),
    .in15(pull_resistor_120_node), .in16(IX_q[15:8]), .in17(IY_q[15:8]), .in18(SP_q[15:8]),
    .in19(BP_q[15:8]), .in20(multiplexer_31_out_2), .in21(DS_q[15:8]), .in22(SS_q_2), .in23(ES_q[15:8]),
    .in24(multiplexer_32_out_2), .in25(SDS_q[15:8]), .in26(SSS_q_2), .in27(SES_q[15:8]), .in28(SP_q[23:16]),
    .in29(A1_q[15:8]), .in30(pull_resistor_121_node), .in31(multiplexer_30_out_2), .out(multiplexer_41_out),
    .sel(multiplexer_9_out[4:0]));
  Pull_Resistor pull_resistor_121 (.node(pull_resistor_121_node));
  Pull_Resistor pull_resistor_122 (.node(pull_resistor_122_node));
  Pull_Resistor pull_resistor_123 (.node(pull_resistor_123_node));
  Pull_Resistor pull_resistor_124 (.node(pull_resistor_124_node));
  Pull_Resistor pull_resistor_125 (.node(pull_resistor_125_node));
  Pull_Resistor pull_resistor_126 (.node(pull_resistor_126_node));
  Pull_Resistor pull_resistor_127 (.node(pull_resistor_127_node));
  Pull_Resistor pull_resistor_128 (.node(pull_resistor_128_node));
  Pull_Resistor pull_resistor_129 (.node(pull_resistor_129_node));
  Pull_Resistor pull_resistor_130 (.node(pull_resistor_130_node));
  Pull_Resistor pull_resistor_131 (.node(pull_resistor_131_node));
  Pull_Resistor pull_resistor_132 (.node(pull_resistor_132_node));
  Pull_Resistor pull_resistor_133 (.node(pull_resistor_133_node));
  Pull_Resistor pull_resistor_134 (.node(pull_resistor_134_node));
  Pull_Resistor pull_resistor_135 (.node(pull_resistor_135_node));
  Pull_Resistor pull_resistor_136 (.node(pull_resistor_136_node));
  Pull_Resistor pull_resistor_137 (.node(pull_resistor_137_node));
  Multiplexer #(.select(5), .width(8)) multiplexer_42 (
    .in0(pull_resistor_122_node), .in1(pull_resistor_123_node), .in2(pull_resistor_124_node),
    .in3(pull_resistor_125_node), .in4(pull_resistor_126_node), .in5(pull_resistor_127_node),
    .in6(pull_resistor_128_node), .in7(pull_resistor_129_node), .in8(pull_resistor_130_node),
    .in9(pull_resistor_131_node), .in10(pull_resistor_132_node), .in11(pull_resistor_133_node),
    .in12(pull_resistor_134_node), .in13(pull_resistor_135_node), .in14(pull_resistor_136_node),
    .in15(pull_resistor_137_node), .in16(IX_q[23:16]), .in17(IY_q[23:16]), .in18(SP_q[23:16]),
    .in19(BP_q[23:16]), .in20(multiplexer_31_out_3), .in21(DS_q[23:16]), .in22(SS_q_3), .in23(ES_q[23:16]),
    .in24(multiplexer_32_out_3), .in25(SDS_q[23:16]), .in26(SSS_q_3), .in27(SES_q[23:16]),
    .in28(A0_q[23:16]), .in29(A1_q[23:16]), .in30(pull_resistor_138_node), .in31(multiplexer_30_out_3),
    .out(multiplexer_42_out), .sel(multiplexer_9_out[4:0]));
  Pull_Resistor pull_resistor_138 (.node(pull_resistor_138_node));
  Pull_Resistor pull_resistor_139 (.node(pull_resistor_139_node));
  Pull_Resistor pull_resistor_140 (.node(pull_resistor_140_node));
  Pull_Resistor pull_resistor_141 (.node(pull_resistor_141_node));
  Pull_Resistor pull_resistor_142 (.node(pull_resistor_142_node));
  Pull_Resistor pull_resistor_143 (.node(pull_resistor_143_node));
  Pull_Resistor pull_resistor_144 (.node(pull_resistor_144_node));
  Pull_Resistor pull_resistor_145 (.node(pull_resistor_145_node));
  Pull_Resistor pull_resistor_146 (.node(pull_resistor_146_node));
  Pull_Resistor pull_resistor_147 (.node(pull_resistor_147_node));
  Pull_Resistor pull_resistor_148 (.node(pull_resistor_148_node));
  Pull_Resistor pull_resistor_149 (.node(pull_resistor_149_node));
  Pull_Resistor pull_resistor_150 (.node(pull_resistor_150_node));
  Pull_Resistor pull_resistor_151 (.node(pull_resistor_151_node));
  Pull_Resistor pull_resistor_152 (.node(pull_resistor_152_node));
  Pull_Resistor pull_resistor_153 (.node(pull_resistor_153_node));
  Pull_Resistor pull_resistor_154 (.node(pull_resistor_154_node));
  Pull_Resistor pull_resistor_155 (.node(pull_resistor_155_node));
  Multiplexer #(.select(5), .width(8)) multiplexer_43 (
    .in0(pull_resistor_139_node), .in1(pull_resistor_140_node), .in2(pull_resistor_141_node),
    .in3(pull_resistor_142_node), .in4(pull_resistor_143_node), .in5(pull_resistor_144_node),
    .in6(pull_resistor_145_node), .in7(pull_resistor_146_node), .in8(pull_resistor_147_node),
    .in9(pull_resistor_148_node), .in10(pull_resistor_149_node), .in11(pull_resistor_150_node),
    .in12(pull_resistor_151_node), .in13(pull_resistor_152_node), .in14(pull_resistor_153_node),
    .in15(pull_resistor_154_node), .in16(pull_resistor_155_node), .in17(pull_resistor_156_node),
    .in18(pull_resistor_157_node), .in19(pull_resistor_158_node), .in20(multiplexer_32_out),
    .in21(SDS_q[7:0]), .in22(undriven), .in24(multiplexer_32_out), .in25(SDS_q[7:0]), .in26(SSS_q),
    .in27(SES_q[7:0]), .in28(pull_resistor_159_node), .in29(pull_resistor_160_node),
    .in30(pull_resistor_161_node), .in31(pull_resistor_162_node), .out(multiplexer_43_out),
    .sel(multiplexer_9_out[4:0]));  // open: in23
  Pull_Resistor pull_resistor_156 (.node(pull_resistor_156_node));
  Pull_Resistor pull_resistor_157 (.node(pull_resistor_157_node));
  Pull_Resistor pull_resistor_158 (.node(pull_resistor_158_node));
  Pull_Resistor pull_resistor_159 (.node(pull_resistor_159_node));
  Pull_Resistor pull_resistor_160 (.node(pull_resistor_160_node));
  Pull_Resistor pull_resistor_161 (.node(pull_resistor_161_node));
  Pull_Resistor pull_resistor_162 (.node(pull_resistor_162_node));
  Pull_Resistor pull_resistor_163 (.node(pull_resistor_163_node));
  Pull_Resistor pull_resistor_164 (.node(pull_resistor_164_node));
  Pull_Resistor pull_resistor_165 (.node(pull_resistor_165_node));
  Pull_Resistor pull_resistor_166 (.node(pull_resistor_166_node));
  Pull_Resistor pull_resistor_167 (.node(pull_resistor_167_node));
  Pull_Resistor pull_resistor_168 (.node(pull_resistor_168_node));
  Pull_Resistor pull_resistor_169 (.node(pull_resistor_169_node));
  Pull_Resistor pull_resistor_170 (.node(pull_resistor_170_node));
  Pull_Resistor pull_resistor_171 (.node(pull_resistor_171_node));
  Pull_Resistor pull_resistor_172 (.node(pull_resistor_172_node));
  Pull_Resistor pull_resistor_173 (.node(pull_resistor_173_node));
  Pull_Resistor pull_resistor_174 (.node(pull_resistor_174_node));
  Pull_Resistor pull_resistor_175 (.node(pull_resistor_175_node));
  Pull_Resistor pull_resistor_176 (.node(pull_resistor_176_node));
  Pull_Resistor pull_resistor_177 (.node(pull_resistor_177_node));
  Pull_Resistor pull_resistor_178 (.node(pull_resistor_178_node));
  Pull_Resistor pull_resistor_179 (.node(pull_resistor_179_node));
  Multiplexer #(.select(5), .width(8)) multiplexer_44 (
    .in0(pull_resistor_163_node), .in1(pull_resistor_164_node), .in2(pull_resistor_165_node),
    .in3(pull_resistor_166_node), .in4(pull_resistor_167_node), .in5(pull_resistor_168_node),
    .in6(pull_resistor_169_node), .in7(pull_resistor_170_node), .in8(pull_resistor_171_node),
    .in9(pull_resistor_172_node), .in10(pull_resistor_173_node), .in11(pull_resistor_174_node),
    .in12(pull_resistor_175_node), .in13(pull_resistor_176_node), .in14(pull_resistor_177_node),
    .in15(pull_resistor_178_node), .in16(pull_resistor_179_node), .in17(pull_resistor_180_node),
    .in18(pull_resistor_181_node), .in19(pull_resistor_182_node), .in20(multiplexer_32_out_2),
    .in21(SDS_q[15:8]), .in22(SSS_q_2), .in23(SES_q[15:8]), .in24(multiplexer_32_out_2), .in25(SDS_q[15:8]),
    .in26(SSS_q_2), .in27(SES_q[15:8]), .in28(pull_resistor_183_node), .in29(pull_resistor_184_node),
    .in30(pull_resistor_185_node), .in31(pull_resistor_186_node), .out(multiplexer_44_out),
    .sel(multiplexer_9_out[4:0]));
  Pull_Resistor pull_resistor_180 (.node(pull_resistor_180_node));
  Pull_Resistor pull_resistor_181 (.node(pull_resistor_181_node));
  Pull_Resistor pull_resistor_182 (.node(pull_resistor_182_node));
  Pull_Resistor pull_resistor_183 (.node(pull_resistor_183_node));
  Pull_Resistor pull_resistor_184 (.node(pull_resistor_184_node));
  Pull_Resistor pull_resistor_185 (.node(pull_resistor_185_node));
  Pull_Resistor pull_resistor_186 (.node(pull_resistor_186_node));
  Pull_Resistor pull_resistor_187 (.node(pull_resistor_187_node));
  Pull_Resistor pull_resistor_188 (.node(pull_resistor_188_node));
  Pull_Resistor pull_resistor_189 (.node(pull_resistor_189_node));
  Pull_Resistor pull_resistor_190 (.node(pull_resistor_190_node));
  Pull_Resistor pull_resistor_191 (.node(pull_resistor_191_node));
  Pull_Resistor pull_resistor_192 (.node(pull_resistor_192_node));
  Pull_Resistor pull_resistor_193 (.node(pull_resistor_193_node));
  Pull_Resistor pull_resistor_194 (.node(pull_resistor_194_node));
  Pull_Resistor pull_resistor_195 (.node(pull_resistor_195_node));
  Pull_Resistor pull_resistor_196 (.node(pull_resistor_196_node));
  Pull_Resistor pull_resistor_197 (.node(pull_resistor_197_node));
  Pull_Resistor pull_resistor_198 (.node(pull_resistor_198_node));
  Pull_Resistor pull_resistor_199 (.node(pull_resistor_199_node));
  Pull_Resistor pull_resistor_200 (.node(pull_resistor_200_node));
  Pull_Resistor pull_resistor_201 (.node(pull_resistor_201_node));
  Pull_Resistor pull_resistor_202 (.node(pull_resistor_202_node));
  Pull_Resistor pull_resistor_203 (.node(pull_resistor_203_node));
  Multiplexer #(.select(5), .width(8)) multiplexer_45 (
    .in0(pull_resistor_187_node), .in1(pull_resistor_188_node), .in2(pull_resistor_189_node),
    .in3(pull_resistor_190_node), .in4(pull_resistor_191_node), .in5(pull_resistor_192_node),
    .in6(pull_resistor_193_node), .in7(pull_resistor_194_node), .in8(pull_resistor_195_node),
    .in9(pull_resistor_196_node), .in10(pull_resistor_197_node), .in11(pull_resistor_198_node),
    .in12(pull_resistor_199_node), .in13(pull_resistor_200_node), .in14(pull_resistor_201_node),
    .in15(pull_resistor_202_node), .in16(pull_resistor_203_node), .in17(pull_resistor_204_node),
    .in18(pull_resistor_205_node), .in19(pull_resistor_206_node), .in20(multiplexer_32_out_3),
    .in21(SDS_q[23:16]), .in22(SSS_q_3), .in23(SES_q[23:16]), .in24(multiplexer_32_out_3),
    .in25(SDS_q[23:16]), .in26(SSS_q_3), .in27(SES_q[23:16]), .in28(pull_resistor_207_node),
    .in29(pull_resistor_208_node), .in30(pull_resistor_209_node), .in31(pull_resistor_210_node),
    .out(multiplexer_45_out), .sel(multiplexer_9_out[4:0]));
  Pull_Resistor pull_resistor_204 (.node(pull_resistor_204_node));
  Pull_Resistor pull_resistor_205 (.node(pull_resistor_205_node));
  Pull_Resistor pull_resistor_206 (.node(pull_resistor_206_node));
  Pull_Resistor pull_resistor_207 (.node(pull_resistor_207_node));
  Pull_Resistor pull_resistor_208 (.node(pull_resistor_208_node));
  Pull_Resistor pull_resistor_209 (.node(pull_resistor_209_node));
  Pull_Resistor pull_resistor_210 (.node(pull_resistor_210_node));
  or or_75 (or_75_out, comparator_2_eq, comparator_2_lt);
  Comparator #(.mode("unsigned"), .width(24)) comparator_2 (
    .a({multiplexer_39_out, multiplexer_38_out, multiplexer_37_out}),
    .b({multiplexer_45_out, multiplexer_44_out, multiplexer_43_out}), .eq(comparator_2_eq),
    .lt(comparator_2_lt));  // open: gt
  Adder #(.width(24)) adder_7 (
    .a({multiplexer_39_out, multiplexer_38_out, multiplexer_37_out}),
    .b({multiplexer_42_out, multiplexer_41_out, multiplexer_40_out}), .out(adder_7_out));  // open: cin, cout
  Adder #(.width(24)) adder_8 (
    .a({multiplexer_31_out_3, multiplexer_31_out_2, multiplexer_31_out}),
    .b({multiplexer_30_out_3, multiplexer_30_out_2, multiplexer_30_out}), .out(INST_ADDR));  // open: cin, cout
  Comparator #(.mode("unsigned"), .width(24)) comparator_3 (
    .a({multiplexer_30_out_3, multiplexer_30_out_2, multiplexer_30_out}),
    .b({multiplexer_32_out_3, multiplexer_32_out_2, multiplexer_32_out}), .gt(comparator_3_gt),
    .eq(comparator_3_eq));  // open: lt
  Adder #(.width(24)) adder_9 (
    .a({SS_q_3, SS_q_2, SS_q}), .b({multiplexer_39_out, multiplexer_38_out, multiplexer_37_out}),
    .out(adder_9_out));  // open: cin, cout
  or or_76 (or_76_out, comparator_4_eq, comparator_4_lt);
  Comparator #(.mode("unsigned"), .width(24)) comparator_4 (
    .a({multiplexer_39_out, multiplexer_38_out, multiplexer_37_out}), .b({SSS_q_3, SSS_q_2, SSS_q}),
    .eq(comparator_4_eq), .lt(comparator_4_lt));  // open: gt
  and and_84 (and_84_out, multiplexer_56_out[0], CCARRY);
  or or_77 (or_77_out, and_84_out, ICARRY);
  and and_85 (and_85_out, multiplexer_56_out[1], CONSBORROW);
  or or_78 (or_78_out, and_85_out, DBORROW);
  Multiplexer #(.width(8)) multiplexer_46 (
    .in0(multiplexer_37_out), .in1(multiplexer_3_out), .out(multiplexer_46_out[7:0]), .sel(ALU_IMM));
  Multiplexer #(.width(8)) multiplexer_47 (
    .in0(multiplexer_38_out), .in1(multiplexer_4_out), .out(multiplexer_46_out[15:8]), .sel(ALU_IMM));
  Multiplexer #(.width(8)) multiplexer_48 (
    .in0(multiplexer_39_out), .in1(multiplexer_5_out), .out(multiplexer_46_out[23:16]), .sel(ALU_IMM));
  Multiplexer multiplexer_49 (.in0(or_75_out), .in1(or_76_out), .out(multiplexer_49_out), .sel(STSP));
  Multiplexer #(.width(24)) multiplexer_50 (.in0(adder_7_out), .in1(adder_9_out), .out(multiplexer_50_out), .sel(STSP));
  Multiplexer #(.width(24)) multiplexer_51 (
    .in0(multiplexer_50_out), .in1({multiplexer_5_out, multiplexer_4_out, multiplexer_3_out}),
    .out(multiplexer_51_out), .sel(REPADDR));
  or or_79 (or_79_out, comparator_3_eq, comparator_3_gt);
  Multiplexer #(.width(8)) multiplexer_52 (
    .in0(multiplexer_34_out), .in1(adder_6_out[7:0]), .out(LDOUT_BYTE0), .sel(CALL_AIC_WE));
  Multiplexer #(.width(8)) multiplexer_53 (
    .in0(multiplexer_35_out), .in1(adder_6_out[15:8]), .out(MDOUT_BYTE1), .sel(CALL_AIC_WE));
  Multiplexer #(.width(8)) multiplexer_54 (
    .in0(multiplexer_36_out), .in1(adder_6_out[23:16]), .out(HDOUT_BYTE2), .sel(CALL_AIC_WE));
  PLA #(.in_width(8), .out_width(4), .\table ("00000010 0000 # ADD\n00000011 0000 # ADC\n00000100 0001 # SUB\n00000101 0001 # SBB\n00000110 0010 # MUL\n00000111 0010 # IMUL\n00001000 0011 # DIV\n00001001 0011 # IDIV\n00001010 0100 # AND\n00001011 0101 # OR\n00001100 0110 # XOR\n00001101 0111 # NOT\n00001110 0000 # INC (ADD)\n00001111 0001 # DEC (SUB)\n00011010 1000 # LSL\n00011011 1001 # LSR\n00011100 1010 # ASR\n00011101 1011 # ROL\n00011110 1100 # ROR")) ALU (
    .in(INST_BYTE7), .out(ALU_out));
  Subtractor #(.width(24)) subtractor_3 (.a(multiplexer_51_out), .b(24'h2), .out(subtractor_3_out));  // open: bin, bout
  Subtractor #(.width(24)) subtractor_4 (.a(multiplexer_51_out), .b(24'h1), .out(subtractor_4_out));  // open: bin, bout
  Multiplexer #(.select(2), .width(24)) multiplexer_55 (
    .in0(subtractor_3_out), .in1(subtractor_4_out), .in2(multiplexer_51_out), .in3(pull_resistor_211_node),
    .out(DATA_ADDR), .sel(multiplexer_33_out));
  Pull_Resistor pull_resistor_211 (.node(pull_resistor_211_node));
  Pull_Resistor pull_resistor_212 (.node(multiplexer_46_out[4:0]));
  or or_80 (or_80_out, REPADDR, MWEA, multiplexer_49_out);
  Shifter #(.width(24)) shifter_1 (
    .in({multiplexer_36_out, multiplexer_35_out, multiplexer_34_out}), .\dist (multiplexer_46_out[4:0]),
    .out(shifter_1_out));
  Shifter #(.shift("lr"), .width(24)) shifter_2 (
    .in({multiplexer_36_out, multiplexer_35_out, multiplexer_34_out}), .\dist (multiplexer_46_out[4:0]),
    .out(shifter_2_out));
  Shifter #(.shift("ar"), .width(24)) shifter_3 (
    .in({multiplexer_36_out, multiplexer_35_out, multiplexer_34_out}), .\dist (multiplexer_46_out[4:0]),
    .out(shifter_3_out));
  Shifter #(.shift("rl"), .width(24)) shifter_4 (
    .in({multiplexer_36_out, multiplexer_35_out, multiplexer_34_out}), .\dist (multiplexer_46_out[4:0]),
    .out(shifter_4_out));
  Shifter #(.shift("rr"), .width(24)) shifter_5 (
    .in({multiplexer_36_out, multiplexer_35_out, multiplexer_34_out}), .\dist (multiplexer_46_out[4:0]),
    .out(shifter_5_out));
  and and_86 (RAM_WE, or_80_out, MWE);
  Multiplexer #(.select(2)) multiplexer_56 (
    .in0(adder_10_cout), .in1(adder_11_cout), .in2(adder_12_cout), .out(multiplexer_56_out[0]),
    .sel(multiplexer_33_out));  // open: in3
  Adder adder_10 (
    .a(multiplexer_34_out), .b(multiplexer_46_out[7:0]), .out(adder_10_out), .cin(or_77_out),
    .cout(adder_10_cout));
  Adder adder_11 (
    .a(multiplexer_35_out), .b(multiplexer_46_out[15:8]), .out(adder_11_out), .cin(adder_10_cout),
    .cout(adder_11_cout));
  Adder adder_12 (
    .a(multiplexer_36_out), .b(multiplexer_46_out[23:16]), .out(adder_12_out), .cin(adder_11_cout),
    .cout(adder_12_cout));
  Subtractor subtractor_5 (
    .a(multiplexer_34_out), .b(multiplexer_46_out[7:0]), .out(subtractor_5_out), .bin(or_78_out),
    .bout(subtractor_5_bout));
  Subtractor subtractor_6 (
    .a(multiplexer_35_out), .b(multiplexer_46_out[15:8]), .out(subtractor_6_out), .bin(subtractor_5_bout),
    .bout(subtractor_6_bout));
  Subtractor subtractor_7 (
    .a(multiplexer_36_out), .b(multiplexer_46_out[23:16]), .out(subtractor_7_out), .bin(subtractor_6_bout),
    .bout(subtractor_7_bout));
  Multiplier #(.mode("twosComplement")) multiplier_1 (
    .a(multiplexer_34_out), .b(multiplexer_46_out[7:0]), .out(multiplier_1_out), .cout(multiplier_1_cout));  // open: cin
  Multiplier #(.mode("twosComplement")) multiplier_2 (
    .a(multiplexer_35_out), .b(multiplexer_46_out[15:8]), .out(multiplier_2_out), .cin(multiplier_1_cout),
    .cout(multiplier_2_cout));
  Multiplier #(.mode("twosComplement")) multiplier_3 (
    .a(multiplexer_36_out), .b(multiplexer_46_out[23:16]), .out(multiplier_3_out), .cin(multiplier_2_cout));  // open: cout
  Multiplier multiplier_4 (
    .a(multiplexer_34_out), .b(multiplexer_46_out[7:0]), .out(multiplier_4_out), .cout(multiplier_4_cout));  // open: cin
  Multiplier multiplier_5 (
    .a(multiplexer_35_out), .b(multiplexer_46_out[15:8]), .out(multiplier_5_out), .cin(multiplier_4_cout),
    .cout(multiplier_5_cout));
  Multiplier multiplier_6 (
    .a(multiplexer_36_out), .b(multiplexer_46_out[23:16]), .out(multiplier_6_out), .cin(multiplier_5_cout));  // open: cout
  Divider #(.mode("twosComplement")) divider_1 (
    .a(multiplexer_34_out), .b(multiplexer_46_out[7:0]), .out(divider_1_out), .rem(divider_1_rem));  // open: upper
  Divider #(.mode("twosComplement")) divider_2 (
    .a(multiplexer_35_out), .b(multiplexer_46_out[15:8]), .out(divider_2_out), .upper(divider_1_rem),
    .rem(divider_2_rem));
  Divider #(.mode("twosComplement")) divider_3 (
    .a(multiplexer_36_out), .b(multiplexer_46_out[23:16]), .out(divider_3_out), .upper(divider_2_rem));  // open: rem
  Divider divider_4 (
    .a(multiplexer_34_out), .b(multiplexer_46_out[7:0]), .out(divider_4_out), .rem(divider_4_rem));  // open: upper
  Divider divider_5 (
    .a(multiplexer_35_out), .b(multiplexer_46_out[15:8]), .out(divider_5_out), .upper(divider_4_rem),
    .rem(divider_5_rem));
  Divider divider_6 (
    .a(multiplexer_36_out), .b(multiplexer_46_out[23:16]), .out(divider_6_out), .upper(divider_5_rem));  // open: rem
  assign and_87_out = multiplexer_34_out & multiplexer_46_out[7:0];  // AND_Gate and_87, 8 bits wide
  assign and_88_out = multiplexer_35_out & multiplexer_46_out[15:8];  // AND_Gate and_88, 8 bits wide
  assign and_89_out = multiplexer_36_out & multiplexer_46_out[23:16];  // AND_Gate and_89, 8 bits wide
  assign not_6_out = ~multiplexer_34_out;  // NOT_Gate not_6, 8 bits wide
  assign or_81_out = multiplexer_34_out | multiplexer_46_out[7:0];  // OR_Gate or_81, 8 bits wide
  assign or_82_out = multiplexer_35_out | multiplexer_46_out[15:8];  // OR_Gate or_82, 8 bits wide
  assign or_83_out = multiplexer_36_out | multiplexer_46_out[23:16];  // OR_Gate or_83, 8 bits wide
  assign not_7_out = ~multiplexer_35_out;  // NOT_Gate not_7, 8 bits wide
  assign xor_1_out = multiplexer_34_out ^ multiplexer_46_out[7:0];  // XOR_Gate xor_1, 8 bits wide
  assign xor_2_out = multiplexer_35_out ^ multiplexer_46_out[15:8];  // XOR_Gate xor_2, 8 bits wide
  assign xor_3_out = multiplexer_36_out ^ multiplexer_46_out[23:16];  // XOR_Gate xor_3, 8 bits wide
  assign not_8_out = ~multiplexer_36_out;  // NOT_Gate not_8, 8 bits wide
  Comparator comparator_5 (
    .a(multiplexer_34_out), .b(multiplexer_46_out[7:0]), .gt(comparator_5_gt), .eq(comparator_5_eq),
    .lt(comparator_5_lt));
  Comparator #(.width(16)) comparator_6 (
    .a({multiplexer_35_out, multiplexer_34_out}), .b(multiplexer_46_out[15:0]), .gt(comparator_6_gt),
    .eq(comparator_6_eq), .lt(comparator_6_lt));
  Comparator #(.width(24)) comparator_7 (
    .a({multiplexer_36_out, multiplexer_35_out, multiplexer_34_out}), .b(multiplexer_46_out),
    .gt(comparator_7_gt), .eq(comparator_7_eq), .lt(comparator_7_lt));
  Comparator #(.mode("unsigned")) comparator_8 (
    .a(multiplexer_34_out), .b(multiplexer_46_out[7:0]), .gt(comparator_8_gt), .eq(comparator_8_eq),
    .lt(comparator_8_lt));
  Comparator #(.mode("unsigned"), .width(16)) comparator_9 (
    .a({multiplexer_35_out, multiplexer_34_out}), .b(multiplexer_46_out[15:0]), .gt(comparator_9_gt),
    .eq(comparator_9_eq), .lt(comparator_9_lt));
  Comparator #(.mode("unsigned"), .width(24)) comparator_10 (
    .a({multiplexer_36_out, multiplexer_35_out, multiplexer_34_out}), .b(multiplexer_46_out),
    .gt(comparator_10_gt), .eq(comparator_10_eq), .lt(comparator_10_lt));
  Multiplexer #(.select(2)) multiplexer_57 (
    .in0(subtractor_5_bout), .in1(subtractor_6_bout), .in2(subtractor_7_bout), .out(multiplexer_56_out[1]),
    .sel(multiplexer_33_out));  // open: in3
  Multiplexer #(.width(8)) multiplexer_58 (
    .in0(multiplier_1_out), .in1(multiplier_4_out), .out(multiplexer_58_out), .sel(SSIGN));
  Multiplexer #(.width(8)) multiplexer_59 (
    .in0(multiplier_2_out), .in1(multiplier_5_out), .out(multiplexer_59_out), .sel(SSIGN));
  Multiplexer #(.width(8)) multiplexer_60 (
    .in0(multiplier_3_out), .in1(multiplier_6_out), .out(multiplexer_60_out), .sel(SSIGN));
  Multiplexer #(.width(8)) multiplexer_61 (
    .in0(divider_1_out), .in1(divider_4_out), .out(multiplexer_61_out), .sel(SSIGN));
  Multiplexer #(.width(8)) multiplexer_62 (
    .in0(divider_2_out), .in1(divider_5_out), .out(multiplexer_62_out), .sel(SSIGN));
  Multiplexer #(.width(8)) multiplexer_63 (
    .in0(divider_3_out), .in1(divider_6_out), .out(multiplexer_63_out), .sel(SSIGN));
  Pull_Resistor pull_resistor_213 (.node(pull_resistor_213_node));
  Pull_Resistor pull_resistor_214 (.node(pull_resistor_214_node));
  Multiplexer multiplexer_64 (.in0(comparator_5_gt), .in1(comparator_8_gt), .out(multiplexer_64_out), .sel(SSIGN));
  Multiplexer multiplexer_65 (.in0(comparator_5_eq), .in1(comparator_8_eq), .out(multiplexer_65_out), .sel(SSIGN));
  Multiplexer multiplexer_66 (.in0(comparator_5_lt), .in1(comparator_8_lt), .out(multiplexer_66_out), .sel(SSIGN));
  Multiplexer multiplexer_67 (.in0(comparator_6_gt), .in1(comparator_9_gt), .out(multiplexer_67_out), .sel(SSIGN));
  Multiplexer multiplexer_68 (.in0(comparator_6_eq), .in1(comparator_9_eq), .out(multiplexer_68_out), .sel(SSIGN));
  Multiplexer multiplexer_69 (.in0(comparator_6_lt), .in1(comparator_9_lt), .out(multiplexer_69_out), .sel(SSIGN));
  Multiplexer multiplexer_70 (.in0(comparator_7_gt), .in1(comparator_10_gt), .out(multiplexer_70_out), .sel(SSIGN));
  Multiplexer multiplexer_71 (.in0(comparator_7_eq), .in1(comparator_10_eq), .out(multiplexer_71_out), .sel(SSIGN));
  Multiplexer multiplexer_72 (.in0(comparator_7_lt), .in1(comparator_10_lt), .out(multiplexer_72_out), .sel(SSIGN));
  Decoder #(.select(2)) decoder_3 (
    .out1(decoder_3_out1), .out2(decoder_3_out2), .sel(multiplexer_33_out));  // open: out0, out3, en
  Multiplexer #(.enable("true"), .select(4), .width(24)) multiplexer_73 (
    .in0(pull_resistor_213_node), .in1(pull_resistor_213_node), .in2(pull_resistor_213_node),
    .in3(pull_resistor_213_node), .in4(pull_resistor_213_node), .in5(pull_resistor_213_node),
    .in6(pull_resistor_213_node), .in7(pull_resistor_213_node), .in8(shifter_1_out), .in9(shifter_2_out),
    .in10(shifter_3_out), .in11(shifter_4_out), .in12(shifter_5_out), .in13(pull_resistor_214_node),
    .in14(pull_resistor_214_node), .in15(pull_resistor_214_node), .out(multiplexer_73_out), .sel(ALU_out),
    .en(ENALU));
  Decoder #(.select(2)) decoder_4 (
    .out0(decoder_4_out0), .out1(decoder_4_out1), .out2(decoder_4_out2), .sel(multiplexer_33_out));  // open: out3, en
  or or_84 (or_84_out, multiplexer_73_out[0], multiplexer_73_out[1], multiplexer_73_out[2], multiplexer_73_out[3], multiplexer_73_out[4], multiplexer_73_out[5], multiplexer_73_out[6], multiplexer_73_out[7]);
  or or_85 (or_85_out, decoder_3_out2, decoder_3_out1);
  or or_86 (or_86_out, multiplexer_73_out[8], multiplexer_73_out[9], multiplexer_73_out[10], multiplexer_73_out[11], multiplexer_73_out[12], multiplexer_73_out[13], multiplexer_73_out[14], multiplexer_73_out[15]);
  or or_87 (or_87_out, multiplexer_73_out[16], multiplexer_73_out[17], multiplexer_73_out[18], multiplexer_73_out[19], multiplexer_73_out[20], multiplexer_73_out[21], multiplexer_73_out[22], multiplexer_73_out[23]);
  Pull_Resistor pull_resistor_215 (.node(pull_resistor_215_node));
  Pull_Resistor pull_resistor_216 (.node(pull_resistor_216_node));
  Pull_Resistor pull_resistor_217 (.node(pull_resistor_217_node));
  Pull_Resistor pull_resistor_218 (.node(pull_resistor_218_node));
  Pull_Resistor pull_resistor_219 (.node(pull_resistor_219_node));
  Pull_Resistor pull_resistor_220 (.node(pull_resistor_220_node));
  Pull_Resistor pull_resistor_221 (.node(pull_resistor_221_node));
  Pull_Resistor pull_resistor_222 (.node(pull_resistor_222_node));
  Pull_Resistor pull_resistor_223 (.node(pull_resistor_223_node));
  Pull_Resistor pull_resistor_224 (.node(pull_resistor_224_node));
  Pull_Resistor pull_resistor_225 (.node(pull_resistor_225_node));
  Pull_Resistor pull_resistor_226 (.node(pull_resistor_226_node));
  Pull_Resistor pull_resistor_227 (.node(pull_resistor_227_node));
  Pull_Resistor pull_resistor_228 (.node(pull_resistor_228_node));
  Pull_Resistor pull_resistor_229 (.node(pull_resistor_229_node));
  Pull_Resistor pull_resistor_230 (.node(pull_resistor_230_node));
  Pull_Resistor pull_resistor_231 (.node(pull_resistor_231_node));
  Pull_Resistor pull_resistor_232 (.node(pull_resistor_232_node));
  Pull_Resistor pull_resistor_233 (.node(pull_resistor_233_node));
  Pull_Resistor pull_resistor_234 (.node(pull_resistor_234_node));
  Pull_Resistor pull_resistor_235 (.node(pull_resistor_235_node));
  Pull_Resistor pull_resistor_236 (.node(pull_resistor_236_node));
  Pull_Resistor pull_resistor_237 (.node(pull_resistor_237_node));
  Pull_Resistor pull_resistor_238 (.node(pull_resistor_238_node));
  Multiplexer #(.select(2)) multiplexer_74 (
    .in0(multiplexer_64_out), .in1(multiplexer_67_out), .in2(multiplexer_70_out),
    .out(multiplexer_56_out[5]), .sel(multiplexer_33_out));  // open: in3
  Multiplexer #(.select(2)) multiplexer_75 (
    .in0(multiplexer_65_out), .in1(multiplexer_68_out), .in2(multiplexer_71_out),
    .out(multiplexer_56_out[6]), .sel(multiplexer_33_out));  // open: in3
  Multiplexer #(.select(2)) multiplexer_76 (
    .in0(multiplexer_66_out), .in1(multiplexer_69_out), .in2(multiplexer_72_out),
    .out(multiplexer_56_out[7]), .sel(multiplexer_33_out));  // open: in3
  or or_88 (or_88_out, or_84_out, pull_resistor_239_node, pull_resistor_240_node);
  Pull_Resistor pull_resistor_239 (.node(pull_resistor_239_node));
  assign pull_resistor_239_node = or_85_out ? or_86_out : 1'bz;  // Controlled_Buffer controlled_buffer_7
  Pull_Resistor pull_resistor_240 (.node(pull_resistor_240_node));
  assign pull_resistor_240_node = decoder_3_out2 ? or_87_out : 1'bz;  // Controlled_Buffer controlled_buffer_8
  Decoder #(.select(2)) decoder_5 (
    .out1(decoder_5_out1), .out2(decoder_5_out2), .sel(multiplexer_33_out));  // open: out0, out3, en
  Multiplexer #(.enable("true"), .select(4), .width(8)) multiplexer_77 (
    .in0(adder_10_out), .in1(subtractor_5_out), .in2(multiplexer_58_out), .in3(multiplexer_61_out),
    .in4(and_87_out), .in5(or_81_out), .in6(xor_1_out), .in7(not_6_out), .in8(pull_resistor_215_node),
    .in9(pull_resistor_216_node), .in10(pull_resistor_217_node), .in11(pull_resistor_218_node),
    .in12(pull_resistor_219_node), .in13(pull_resistor_220_node), .in14(pull_resistor_221_node),
    .in15(pull_resistor_222_node), .out(multiplexer_77_out), .sel(ALU_out), .en(ENALU));
  Multiplexer #(.enable("true"), .select(4), .width(8)) multiplexer_78 (
    .in0(adder_11_out), .in1(subtractor_6_out), .in2(multiplexer_59_out), .in3(multiplexer_62_out),
    .in4(and_88_out), .in5(or_82_out), .in6(xor_2_out), .in7(not_7_out), .in8(pull_resistor_223_node),
    .in9(pull_resistor_224_node), .in10(pull_resistor_225_node), .in11(pull_resistor_226_node),
    .in12(pull_resistor_227_node), .in13(pull_resistor_228_node), .in14(pull_resistor_229_node),
    .in15(pull_resistor_230_node), .out(multiplexer_78_out), .sel(ALU_out), .en(ENALU));
  Multiplexer #(.enable("true"), .select(4), .width(8)) multiplexer_79 (
    .in0(adder_12_out), .in1(subtractor_7_out), .in2(multiplexer_60_out), .in3(multiplexer_63_out),
    .in4(and_89_out), .in5(or_83_out), .in6(xor_3_out), .in7(not_8_out), .in8(pull_resistor_231_node),
    .in9(pull_resistor_232_node), .in10(pull_resistor_233_node), .in11(pull_resistor_234_node),
    .in12(pull_resistor_235_node), .in13(pull_resistor_236_node), .in14(pull_resistor_237_node),
    .in15(pull_resistor_238_node), .out(multiplexer_79_out), .sel(ALU_out), .en(ENALU));
  buf or_89 (HCE0, decoder_4_out2);  // OR_Gate
  or or_90 (MCE1, decoder_4_out2, decoder_4_out1);
  or or_91 (LCE2, MCE1, decoder_4_out0);
  or or_92 (or_92_out, multiplexer_77_out[0], multiplexer_77_out[1], multiplexer_77_out[2], multiplexer_77_out[3], multiplexer_77_out[4], multiplexer_77_out[5], multiplexer_77_out[6], multiplexer_77_out[7]);
  or or_93 (or_93_out, decoder_5_out1, decoder_5_out2);
  Pull_Resistor pull_resistor_241 (.node(pull_resistor_241_node));
  assign pull_resistor_241_node = or_93_out ? or_94_out : 1'bz;  // Controlled_Buffer controlled_buffer_9
  or or_94 (or_94_out, multiplexer_78_out[0], multiplexer_78_out[1], multiplexer_78_out[2], multiplexer_78_out[3], multiplexer_78_out[4], multiplexer_78_out[5], multiplexer_78_out[6], multiplexer_78_out[7]);
  or or_95 (or_95_out, multiplexer_79_out[0], multiplexer_79_out[1], multiplexer_79_out[2], multiplexer_79_out[3], multiplexer_79_out[4], multiplexer_79_out[5], multiplexer_79_out[6], multiplexer_79_out[7]);
  Pull_Resistor pull_resistor_242 (.node(pull_resistor_242_node));
  assign pull_resistor_242_node = decoder_5_out2 ? or_95_out : 1'bz;  // Controlled_Buffer controlled_buffer_10
  or or_96 (multiplexer_56_out[4], pull_resistor_241_node, or_92_out, pull_resistor_242_node, or_88_out);
  Multiplexer #(.width(8)) multiplexer_80 (
    .in0(multiplexer_77_out), .in1(multiplexer_73_out[7:0]), .out(multiplexer_80_out), .sel(SW2BSU));
  Multiplexer #(.width(8)) multiplexer_81 (
    .in0(multiplexer_78_out), .in1(multiplexer_73_out[15:8]), .out(multiplexer_81_out), .sel(SW2BSU));
  Multiplexer #(.width(8)) multiplexer_82 (
    .in0(multiplexer_79_out), .in1(multiplexer_73_out[23:16]), .out(multiplexer_82_out), .sel(SW2BSU));
  Comparator comparator_11 (.a(multiplexer_80_out), .b({8{1'b0}}), .lt(comparator_11_lt));  // open: gt, eq
  Comparator #(.width(16)) comparator_12 (
    .a({multiplexer_81_out, multiplexer_80_out}), .b({16{1'b0}}), .lt(comparator_12_lt));  // open: gt, eq
  Comparator #(.width(24)) comparator_13 (
    .a({multiplexer_82_out, multiplexer_81_out, multiplexer_80_out}), .b({24{1'b0}}), .lt(comparator_13_lt));  // open: gt, eq
  Multiplexer #(.select(2)) multiplexer_83 (
    .in0(comparator_11_lt), .in1(comparator_12_lt), .in2(comparator_13_lt), .out(multiplexer_56_out[2]),
    .sel(multiplexer_33_out));  // open: in3
  Pull_Resistor pull_resistor_243 (.node(multiplexer_56_out[3]));

  // Other names for the same wires on the sheet: MOE = RAM_OE; CALL_IC_WE = CALL_AIC_WE; CALLSR = CALL_AIC_WE;
  //   MUX_RADDR = CALL_AIC_WE; WR_SR = CALL_AIC_WE; RET_IC_WE = RET_AIC_WE; RETSR = RET_AIC_WE;
  //   SEL_RET_SR = RET_AIC_WE

  // Notes on the sheet:
  //   contents of rom_1 (hex, n*v repeats v):
  //   0 1 0 0 1 0 0 1 0 0 1 0 0 1 0 0 14*2 0 2
endmodule

module TEST (
  input  in_1,
  input  CLK,
  input  in_3
);

  wire and_1_out, and_2_out, and_3_out, cpu_1_hce0, cpu_1_lce2, cpu_1_mce1, cpu_1_ram_oe, cpu_1_ram_we;
  wire [7:0] cpu_1_hdout_byte2, cpu_1_ldout_byte0, cpu_1_mdout_byte1, pull_resistor_2_node,
       pull_resistor_3_node, pull_resistor_4_node, undriven, undriven_2, undriven_3;
  wire [23:0] cpu_1_data_addr, cpu_1_inst_addr;
  wire [63:0] dualram_1_p16;

  CPU cpu_1 (
    .LDIN_BYTE0(pull_resistor_3_node), .MDIN_BYTE1(pull_resistor_4_node), .HDIN_BYTE2(pull_resistor_2_node),
    .INST_BYTE7(dualram_1_p16[7:0]), .INST_BYTE6(dualram_1_p16[15:8]), .INST_BYTE5(dualram_1_p16[23:16]),
    .INST_BYTE4(dualram_1_p16[31:24]), .INST_BYTE3(dualram_1_p16[39:32]), .INST_BYTE2(dualram_1_p16[47:40]),
    .INST_BYTE1(dualram_1_p16[55:48]), .INST_BYTE0(dualram_1_p16[63:56]), .ENABLE(in_1), .CLK(CLK),
    .RESET(in_3), .HCE0(cpu_1_hce0), .MCE1(cpu_1_mce1), .LCE2(cpu_1_lce2), .LDOUT_BYTE0(cpu_1_ldout_byte0),
    .MDOUT_BYTE1(cpu_1_mdout_byte1), .HDOUT_BYTE2(cpu_1_hdout_byte2), .DATA_ADDR(cpu_1_data_addr),
    .INST_ADDR(cpu_1_inst_addr), .RAM_WE(cpu_1_ram_we), .RAM_OE(cpu_1_ram_oe));  // open: IRQ_ID, IRQ_IN, IRQ_EN, IRQ_IN_PROCESS
  // DualRAM #(.addrWidth(24), .enables("line"), .line("octo"), .misaligned("true")) dualram_1: pin names not known; wires that end beside it: cpu_1_inst_addr, in_1, in_1, in_1, in_1, in_1, in_1, in_1, in_1, CLK, cpu_1_data_addr, cpu_1_ram_we, cpu_1_hce0, cpu_1_mce1, cpu_1_lce2, dualram_1_p16[7:0], dualram_1_p16[15:8], dualram_1_p16[23:16], dualram_1_p16[31:24], dualram_1_p16[39:32], dualram_1_p16[47:40], dualram_1_p16[55:48], dualram_1_p16[63:56]
  Pull_Resistor pull_resistor_1 ();  // open: node
  Pull_Resistor pull_resistor_2 (.node(pull_resistor_2_node));
  assign pull_resistor_2_node = and_1_out ? undriven : 8'bz;  // Controlled_Buffer controlled_buffer_1
  Pull_Resistor pull_resistor_3 (.node(pull_resistor_3_node));
  assign pull_resistor_3_node = and_3_out ? undriven_3 : 8'bz;  // Controlled_Buffer controlled_buffer_2
  Pull_Resistor pull_resistor_4 (.node(pull_resistor_4_node));
  assign pull_resistor_4_node = and_2_out ? undriven_2 : 8'bz;  // Controlled_Buffer controlled_buffer_3
  and and_1 (and_1_out, cpu_1_hce0, cpu_1_ram_oe);
  and and_2 (and_2_out, cpu_1_ram_oe, cpu_1_mce1);
  and and_3 (and_3_out, cpu_1_ram_oe, cpu_1_lce2);
endmodule
